// Logisim project CSIE1601_U201615677_LOGISIM.circ as structural Verilog: 27 circuits, main circuit ◇单周期MIPS
module \单周期MIPS  (
);

  wire \_1号中断 , \_1号中断等待指示 , \_2号中断 , \_2号中断等待指示 , \_3号中断 , \_3号中断等待指示 , Address, AluSrcB, AluSrcB1,
       and_2_out, and_3_out, and_4_out, and_5_out, and_6_out, bit_extender_4_out, BLEZ, BT, CLK, CO,
       comparator_1_eq, comparator_2_eq, ERET, Go, IRstart, JT, LH, MemToReg, MemToReg1, mips_alu_1_equal,
       multiplexer_1_out, \n4控制信号_1_alusrc , \n4控制信号_1_memtoreg , \n4控制信号_1_regdst , \n4控制信号_1_regwrite ,
       \n4控制信号_1_signedext , not_1_out, not_2_out, not_3_out, or_8_out, or_9_out, or_10_out, RegDst, RegDst1,
       RegWrite, RegWrite1, RST, SignedExt, SignedExt1, SRAV, SRLV, T, \硬布线控制器_1_beq , \硬布线控制器_1_bne ,
       \硬布线控制器_1_jal , \硬布线控制器_1_jr , \硬布线控制器_1_memwrite , \硬布线控制器_1_syscall ;
  wire [1:0] IRnum;
  wire [3:0] AluOP, AluOP1, \n4控制信号_1_alu_op ;
  wire [4:0] multiplexer_3_out, multiplexer_6_out, multiplexer_7_out, multiplexer_8_out, multiplexer_15_out;
  wire [5:0] FunC, OP;
  wire [9:0] demultiplexer_1_out0, demultiplexer_1_out1, demultiplexer_1_out2, demultiplexer_1_out3;
  wire [15:0] multiplexer_20_out, \总周期数 , \无条件分支数 , \条件分支成功数 ;
  wire [24:6] multiplexer_2_out;
  wire [31:0] a0, adder_1_out, adder_2_out, beforePC, bit_extender_1_out, bit_extender_2_out,
       bit_extender_3_out, bit_extender_5_out, LedData, mips_alu_1_result, mips_ram_1_p6, multiplexer_4_out,
       multiplexer_5_out, multiplexer_9_out, multiplexer_11_out, multiplexer_12_out, multiplexer_13_out,
       multiplexer_14_out, multiplexer_16_out, multiplexer_17_out, multiplexer_18_out, multiplexer_21_out,
       PC, PCin, PCout, rom_1_data, rom_2_data, rom_3_data, rom_4_data, rs, shifter_1_out, shifter_2_out;

  Button \u_总复位  (.out(RST));
  Button \u_继续运行  (.out(Go));
  Clock clock_1 (.out(CLK));
  not not_1 (not_1_out, and_5_out);
  or or_1 (T, not_1_out, Go);
  Button _1 (.out(\_1号中断 ));
  Button _2 (.out(\_2号中断 ));
  Button _3 (.out(\_3号中断 ));
  Register #(.width(32)) u_PC (.D(PCin), .en(T), .Q(PC), .clk(CLK), .clr(RST));
  assign AluOP = \n4控制信号_1_alu_op  | AluOP1;  // OR_Gate or_2, 4 bits wide
  or or_3 (RegDst, \n4控制信号_1_regdst , RegDst1);
  or or_4 (RegWrite, \n4控制信号_1_regwrite , RegWrite1);
  Multiplexer #(.select(2)) multiplexer_1 (
    .in0(1'b1), .in1(1'b0), .in2(1'b1), .in3(1'b1), .out(multiplexer_1_out), .sel({ERET, IRstart}));  // open: en
  Hex_Digit_Display hex_digit_display_1 (.value(LedData[31:28]));  // open: dp
  Hex_Digit_Display hex_digit_display_2 (.value(LedData[27:24]));  // open: dp
  // Probe on PC
  Hex_Digit_Display hex_digit_display_3 (.value(LedData[23:20]));  // open: dp
  Hex_Digit_Display hex_digit_display_4 (.value(LedData[19:16]));  // open: dp
  LED _1_2 (.in(\_1号中断等待指示 ));
  LED _2_2 (.in(\_2号中断等待指示 ));
  LED _3_2 (.in(\_3号中断等待指示 ));
  Demultiplexer #(.select(2), .width(10), .enable("false")) demultiplexer_1 (
    .out0(demultiplexer_1_out0), .out1(demultiplexer_1_out1), .out2(demultiplexer_1_out2),
    .out3(demultiplexer_1_out3), .in(PC[11:2]), .sel(PC[31:30]));
  // Probe on PC[31:30]
  \_4控制信号  \u_4控制信号_1  (
    .OP(OP), .Func(FunC), .ALU_OP(\n4控制信号_1_alu_op ), .RegDst(\n4控制信号_1_regdst ),
    .RegWrite(\n4控制信号_1_regwrite ), .MemToReg(\n4控制信号_1_memtoreg ), .AluSrc(\n4控制信号_1_alusrc ),
    .SignedExt(\n4控制信号_1_signedext ), .SRLV(SRLV), .SRAV(SRAV), .LH(LH), .BLEZ(BLEZ));
  CP0 cp0_1 (
    .\_1号中断 (\_1号中断 ), .IE(multiplexer_1_out), .W1(\_1号中断等待指示 ), .num(IRnum), .PCin(PC), .\_2号中断 (\_2号中断 ),
    .ERET(ERET), .W2(\_2号中断等待指示 ), .IRstart(IRstart), .\_3号中断 (\_3号中断 ), .CLK(CLK), .W3(\_3号中断等待指示 ),
    .PCout(PCout));
  Hex_Digit_Display hex_digit_display_5 (.value(LedData[15:12]));  // open: dp
  Hex_Digit_Display hex_digit_display_6 (.value(LedData[11:8]));  // open: dp
  Hex_Digit_Display hex_digit_display_7 (.value(LedData[3:0]));  // open: dp
  Hex_Digit_Display hex_digit_display_8 (.value(LedData[7:4]));  // open: dp
  ROM #(.addrWidth(10), .dataWidth(32)) rom_1 (.addr(demultiplexer_1_out0), .data(rom_1_data));  // open: sel
  ROM #(.addrWidth(10), .dataWidth(32)) rom_2 (.addr(demultiplexer_1_out1), .data(rom_2_data));  // open: sel
  ROM #(.addrWidth(10), .dataWidth(32)) rom_3 (.addr(demultiplexer_1_out2), .data(rom_3_data));  // open: sel
  ROM #(.addrWidth(10), .dataWidth(32)) rom_4 (.addr(demultiplexer_1_out3), .data(rom_4_data));  // open: sel
  Adder #(.width(32)) adder_1 (.a(PC), .b(32'h4), .out(adder_1_out));  // open: cin, cout
  Multiplexer #(.select(2), .width(32)) multiplexer_2 (
    .in0(rom_1_data), .in1(rom_2_data), .in2(rom_3_data), .in3(rom_4_data),
    .out({OP, CO, multiplexer_2_out, FunC}), .sel(PC[31:30]));  // open: en
  or or_5 (SignedExt, \n4控制信号_1_signedext , SignedExt1);
  or or_6 (AluSrcB, \n4控制信号_1_alusrc , AluSrcB1);
  or or_7 (MemToReg, \n4控制信号_1_memtoreg , MemToReg1);
  // Probe on \总周期数 
  // Probe on \无条件分支数 
  // Probe on \条件分支成功数 
  // Probe on multiplexer_6_out
  Comparator #(.width(6)) comparator_1 (.a(OP), .b(6'b010000), .eq(comparator_1_eq));  // open: gt, lt
  Comparator #(.width(6)) comparator_2 (.a(FunC), .b(6'b011000), .eq(comparator_2_eq));  // open: gt, lt
  Counter #(.width(16), .max('hffff)) counter_1 (
    .D(\总周期数 ), .count(T), .Q(\总周期数 ), .clk(CLK), .clr(RST));  // open: load, carry
  \硬布线控制器  \u_硬布线控制器_1  (
    .Func(FunC), .OP(OP), .ALU_OP(AluOP1), .MemToReg(MemToReg1), .MemWrite(\硬布线控制器_1_memwrite ),
    .ALU_SRC(AluSrcB1), .RegWrite(RegWrite1), .SysCALL(\硬布线控制器_1_syscall ), .SignedExt(SignedExt1),
    .RegDst(RegDst1), .JR(\硬布线控制器_1_jr ), .JMP(JT), .Beq(\硬布线控制器_1_beq ), .JAL(\硬布线控制器_1_jal ),
    .Bne(\硬布线控制器_1_bne ));
  Multiplexer #(.width(5), .enable("false")) multiplexer_3 (
    .in0({CO, multiplexer_2_out[24:21]}), .in1(5'b00010), .out(multiplexer_3_out), .sel(\硬布线控制器_1_syscall ));
  assign bit_extender_1_out = {{16{multiplexer_2_out[15]}}, {multiplexer_2_out[15:6], FunC}};  // Bit_Extender bit_extender_1
  assign bit_extender_2_out = {{16{1'b0}}, {multiplexer_2_out[15:6], FunC}};  // Bit_Extender bit_extender_2
  assign bit_extender_3_out = {{6{1'b0}}, {CO, multiplexer_2_out, FunC}};  // Bit_Extender bit_extender_3
  Multiplexer #(.width(32), .enable("false")) multiplexer_4 (
    .in0(beforePC), .in1(PCout), .out(multiplexer_4_out), .sel(ERET));
  Multiplexer #(.select(2), .width(32), .enable("false")) multiplexer_5 (
    .in1(32'h40000000), .in2(32'ha0000000), .in3(32'hc0000000), .out(multiplexer_5_out), .sel(IRnum));  // open: in0
  Multiplexer #(.width(5), .enable("false")) multiplexer_6 (
    .in0(multiplexer_2_out[20:16]), .in1(5'b00100), .out(multiplexer_6_out), .sel(\硬布线控制器_1_syscall ));
  Multiplexer #(.width(5), .enable("false")) multiplexer_7 (
    .in0(multiplexer_2_out[20:16]), .in1(multiplexer_2_out[15:11]), .out(multiplexer_7_out), .sel(RegDst));
  Multiplexer #(.width(5), .enable("false")) multiplexer_8 (
    .in0(multiplexer_7_out), .in1({5{1'b1}}), .out(multiplexer_8_out), .sel(\硬布线控制器_1_jal ));
  Multiplexer #(.width(32), .enable("false")) multiplexer_9 (
    .in0(multiplexer_21_out), .in1(adder_1_out), .out(multiplexer_9_out), .sel(\硬布线控制器_1_jal ));
  Multiplexer #(.width(32), .enable("false")) multiplexer_10 (
    .in0(multiplexer_4_out), .in1(multiplexer_5_out), .out(PCin), .sel(IRstart));
  Counter #(.width(16), .max('hffff)) counter_2 (
    .D(\无条件分支数 ), .count(JT), .Q(\无条件分支数 ), .clk(CLK), .clr(RST));  // open: load, carry
  // Probe on multiplexer_3_out
  and and_1 (ERET, comparator_1_eq, comparator_2_eq, CO);
  MIPS_Regifile mips_regifile_1 (
    .Din(multiplexer_9_out), .Clk(CLK), .R1(rs), .R2(a0), .WE(RegWrite), .W_num(multiplexer_8_out),
    .R1_num(multiplexer_3_out), .R2_num(multiplexer_6_out));
  // Probe on multiplexer_8_out
  Multiplexer #(.width(32), .enable("false")) multiplexer_11 (
    .in0(bit_extender_2_out), .in1(bit_extender_1_out), .out(multiplexer_11_out), .sel(SignedExt));
  or or_8 (or_8_out, JT, \硬布线控制器_1_jal );
  Counter #(.width(16), .max('hffff)) counter_3 (
    .D(\条件分支成功数 ), .count(BT), .Q(\条件分支成功数 ), .clk(CLK), .clr(RST));  // open: load, carry
  Multiplexer #(.width(32), .enable("false")) multiplexer_12 (
    .in0(a0), .in1(multiplexer_11_out), .out(multiplexer_12_out), .sel(AluSrcB));
  Shifter #(.width(32)) shifter_1 (.in(bit_extender_3_out), .\dist (5'b00010), .out(shifter_1_out));
  not not_2 (not_2_out, mips_alu_1_equal);
  // Probe on rs
  Multiplexer #(.width(32), .enable("false")) multiplexer_13 (
    .in0(multiplexer_12_out), .in1(32'h22), .out(multiplexer_13_out), .sel(\硬布线控制器_1_syscall ));
  Shifter #(.width(32)) shifter_2 (.in(bit_extender_1_out), .\dist (5'b00010), .out(shifter_2_out));
  and and_2 (and_2_out, mips_alu_1_equal, \硬布线控制器_1_beq );
  and and_3 (and_3_out, not_2_out, \硬布线控制器_1_bne );
  and and_4 (and_4_out, BLEZ, or_9_out);
  or or_9 (or_9_out, bit_extender_4_out, mips_alu_1_equal);
  Bit_Extender #(.in_width(32), .out_width(1), .\type ("sign")) bit_extender_4 (
    .in({mips_alu_1_result[31:2], Address, mips_alu_1_result[0]}), .out(bit_extender_4_out));
  // Probe on multiplexer_13_out
  Multiplexer #(.width(32), .enable("false")) multiplexer_14 (
    .in0(multiplexer_13_out), .in1({32{1'b0}}), .out(multiplexer_14_out), .sel(BLEZ));
  MIPS_ALU mips_alu_1 (
    .X(rs), .Y(multiplexer_14_out), .AluOP(AluOP), .Equal(mips_alu_1_equal),
    .Result({mips_alu_1_result[31:2], Address, mips_alu_1_result[0]}), .shamt(multiplexer_15_out));  // open: Result_2
  // Probe on multiplexer_15_out
  Multiplexer #(.width(5), .enable("false")) multiplexer_15 (
    .in0(multiplexer_2_out[10:6]), .in1(rs[4:0]), .out(multiplexer_15_out), .sel(or_10_out));
  or or_10 (or_10_out, SRAV, SRLV);
  or or_11 (BT, and_2_out, and_3_out, and_4_out);
  and and_5 (and_5_out, \硬布线控制器_1_syscall , not_3_out);
  not not_3 (not_3_out, mips_alu_1_equal);
  and and_6 (and_6_out, mips_alu_1_equal, \硬布线控制器_1_syscall );
  // Probe on {mips_alu_1_result[31:2], Address, mips_alu_1_result[0]}
  Adder #(.width(32)) adder_2 (.a(shifter_2_out), .b(adder_1_out), .out(adder_2_out));  // open: cin, cout
  // Probe on a0
  Register #(.width(32)) register_1 (.D(a0), .en(and_6_out), .Q(LedData), .clk(CLK));  // open: clr
  // Probe on a0
  Multiplexer #(.width(32), .enable("false")) multiplexer_16 (
    .in0(adder_1_out), .in1(adder_2_out), .out(multiplexer_16_out), .sel(BT));
  Multiplexer #(.width(32), .enable("false")) multiplexer_17 (
    .in0(multiplexer_16_out), .in1(shifter_1_out), .out(multiplexer_17_out), .sel(or_8_out));
  // Probe on LedData
  // MIPS_RAM mips_ram_1: pin names not known; wires that end beside it: mips_alu_1_result[21:2], a0, \硬布线控制器_1_memwrite , CLK, RST, mips_ram_1_p6
  // Probe on mips_alu_1_result[21:2]
  Multiplexer #(.width(32), .enable("false")) multiplexer_18 (
    .in0({mips_alu_1_result[31:2], Address, mips_alu_1_result[0]}), .in1(mips_ram_1_p6),
    .out(multiplexer_18_out), .sel(MemToReg));
  Multiplexer #(.width(32), .enable("false")) multiplexer_19 (
    .in0(multiplexer_17_out), .in1(rs), .out(beforePC), .sel(\硬布线控制器_1_jr ));
  Multiplexer #(.width(16), .enable("false")) multiplexer_20 (
    .in0(mips_ram_1_p6[15:0]), .in1(mips_ram_1_p6[31:16]), .out(multiplexer_20_out), .sel(Address));
  assign bit_extender_5_out = {{16{multiplexer_20_out[15]}}, multiplexer_20_out};  // Bit_Extender bit_extender_5
  Multiplexer #(.width(32), .enable("false")) multiplexer_21 (
    .in0(multiplexer_18_out), .in1(bit_extender_5_out), .out(multiplexer_21_out), .sel(LH));

  // Notes on the sheet:
  //   nextpc
  //   数码管输出
  //   contents of rom_1 (hex, n*v repeats v):
  //   20110001 8100005 20110001 20120002 20130003 8100009 20110001 20120002 20130003 810000d 20110001
  //   20120002 20130003 8100011 20110001 20120002 20130003 c1000fc 20100001 20110001 118fc0 112020
  //   20020022 c 118882 12200001 8100015 112020 20020022 c 20110001 118880 112020 20020022 c 12200001
  //   810001f 20110001 118fc0 112020 20020022 c 1188c3 112020 20020022 c 118903 112020 20020022 c 118903
  //   112020 20020022 c 118903 112020 20020022 c 118903 112020 20020022 c 118903 112020 20020022 c 118903
  //   112020 20020022 c 118903 112020 20020022 c 20100001 109fc0 139fc3 8021 2012000c 24160003 26100001
  //   3210000f 20080008 20090001 139900 2709825 132020 20020022 c 1094022 1500fff9 22100001 2018000f
  //   2188024 108700 20080008 20090001 139902 2709825 132021 20020022 c 1094022 1500fff9 108702 2c9b022
  //   12c00001 8100050 4020 1084027 84400 3508ffff 82021 20020022 c 2010ffff 20110000 ae300000 22100001
  //   22310004 ae300000 22100001 22310004 ae300000 22100001 22310004 ae300000 22100001 22310004 ae300000
  //   22100001 22310004 ae300000 22100001 22310004 ae300000 22100001 22310004 ae300000 22100001 22310004
  //   ae300000 22100001 22310004 ae300000 22100001 22310004 ae300000 22100001 22310004 ae300000 22100001
  //   22310004 ae300000 22100001 22310004 ae300000 22100001 22310004 ae300000 22100001 22310004 ae300000
  //   22100001 22310004 22100001 8020 2011003c 8e130000 8e340000 274402a 11000002 ae330000 ae140000
  //   2231fffc 1611fff8 102020 20020022 c 22100004 2011003c 1611fff2 20020032 c 20080001 20090003 20110876
  //   118d00 112020 20020022 c 200b0008 1118806 1318806 112020 20020022 c 216bffff 1560fff9 2002000a c
  //   20080001 20090003 20110876 118d00 112020 20020022 c 200b0008 1118807 1318807 112020 20020022 c
  //   216bffff 1560fff9 2002000a c 20090000 200b0010 34118483 20120404 118c00 129400 36318281 22520404
  //   ad310000 2328820 21290004 216bffff 1560fffb 200b0020 20090000 85310000 112020 20020022 c 21290002
  //   216bffff 1560fff9 2002000a c 2011fff1 112020 20020022 c 22310001 1a20fffb 2002000a c 2002000a c
  //   20100000 22100001 102020 20020022 c 22100002 102020 20020022 c 22100003 102020 20020022 c 22100004
  //   102020 20020022 c 22100005 102020 20020022 c 22100006 102020 20020022 c 22100007 102020 20020022 c
  //   22100008 102020 20020022 20020022 c 3e00008
  //   指令字
  //   contents of rom_2 (hex, n*v repeats v):
  //   27bdfffc afb00000 27bdfffc afb20000 27bdfffc afb30000 27bdfffc afa80000 27bdfffc afa90000 27bdfffc
  //   afa40000 27bdfffc afa20000 27bdfffc afb80000 20100001 109fc0 139fc3 8021 2012000c 26100001 3210000f
  //   20080008 20090001 139900 2709825 132020 20020022 c 1094022 1500fff9 22100001 2018000f 2188024 108700
  //   20080008 20090001 139902 2709825 132021 20020022 c 1094022 1500fff9 108702 4020 1084027 84400
  //   3508ffff 82021 20020022 c 8fb80000 27bd0004 8fa20000 27bd0004 8fa40000 27bd0004 8fa90000 27bd0004
  //   8fa80000 27bd0004 8fb30000 27bd0004 8fb20000 27bd0004 8fb00000 27bd0004 42000018
  //   contents of rom_3 (hex, n*v repeats v):
  //   27bdfffc afb00000 27bdfffc afb20000 27bdfffc afb30000 27bdfffc afa80000 27bdfffc afa90000 27bdfffc
  //   afa40000 27bdfffc afa20000 27bdfffc afb80000 20100001 109fc0 139fc3 8021 2012000c 26100002 3210000f
  //   20080008 20090001 139900 2709825 132020 20020022 c 1094022 1500fff9 22100001 2018000f 2188024 108700
  //   20080008 20090001 139902 2709825 132021 20020022 c 1094022 1500fff9 108702 4020 1084027 84400
  //   3508ffff 82021 20020022 c 8fb80000 27bd0004 8fa20000 27bd0004 8fa40000 27bd0004 8fa90000 27bd0004
  //   8fa80000 27bd0004 8fb30000 27bd0004 8fb20000 27bd0004 8fb00000 27bd0004 42000018
  //   contents of rom_4 (hex, n*v repeats v):
  //   27bdfffc afb00000 27bdfffc afb20000 27bdfffc afb30000 27bdfffc afa80000 27bdfffc afa90000 27bdfffc
  //   afa40000 27bdfffc afa20000 27bdfffc afb80000 20100001 109fc0 139fc3 8021 2012000c 26100003 3210000f
  //   20080008 20090001 139900 2709825 132020 20020022 c 1094022 1500fff9 22100001 2018000f 2188024 108700
  //   20080008 20090001 139902 2709825 132021 20020022 c 1094022 1500fff9 108702 4020 1084027 84400
  //   3508ffff 82021 20020022 c 8fb80000 27bd0004 8fa20000 27bd0004 8fa40000 27bd0004 8fa90000 27bd0004
  //   8fa80000 27bd0004 8fb30000 27bd0004 8fb20000 27bd0004 8fb00000 27bd0004 42000018
  //   指令字
  //   OP
  //   Func
  //   rs
  //   rt
  //   rd
  //   shamt
  //   JMP
  //   JR
  //   OP
  //   Func
  //   Beq
  //   Bne
  //   AluOP
  //   AluSrcB
  //   RegWrite
  //   JAL
  //   RegDst
  //   Syscall
  //   1
  //   3
  //   总复位信号应将除ROM以外所有存储组件全部清零
  //   MemToReg
  //   MemWrite
  //   2
  //   4
  //   10
  //   5
  //   6
  //   7
  //   8
  //   11
  //   12
  //   13
  //   9
  //   15
  //   14
  //   16
endmodule

// 单周期硬布线控制器
module \硬布线控制器  (
  input  [5:0] OP,
  input  [5:0] Func,
  output [3:0] ALU_OP,
  output MemToReg,
  output MemWrite,
  output ALU_SRC,
  output RegWrite,
  output SysCALL,
  output SignedExt,
  output RegDst,
  output Beq,
  output Bne,
  output JR,
  output JMP,
  output JAL
);

  \运算控制器  \u_运算控制器_1  (
    .OP0(OP[0]), .OP1(OP[1]), .OP2(OP[2]), .OP3(OP[3]), .OP4(OP[4]), .OP5(OP[5]), .F0(Func[0]), .F1(Func[1]),
    .F2(Func[2]), .F3(Func[3]), .F4(Func[4]), .F5(Func[5]), .S0(ALU_OP[0]), .S1(ALU_OP[1]), .S2(ALU_OP[2]),
    .S3(ALU_OP[3]));
  \控制信号生成  \u_控制信号生成_1  (
    .OP0(OP[0]), .OP1(OP[1]), .OP2(OP[2]), .OP3(OP[3]), .OP4(OP[4]), .OP5(OP[5]), .F0(Func[0]), .F1(Func[1]),
    .F2(Func[2]), .F3(Func[3]), .F4(Func[4]), .F5(Func[5]), .MemToReg(MemToReg), .MemWrite(MemWrite),
    .ALU_SRC(ALU_SRC), .RegWrite(RegWrite), .SysCALL(SysCALL), .SignedExt(SignedExt), .RegDst(RegDst),
    .BEQ(Beq), .BNE(Bne), .JR(JR), .JMP(JMP), .JAL(JAL));

  // Other names for the same wires on the sheet: OP_CODE[5:0] = OP

  // Notes on the sheet:
  //   运算器控制器，根据指令生成运算器功能选择信号
  //   控制信号生成，产生数据通路需要的其他控制信号
endmodule

// 运算器控制器
module \运算控制器  (
  input  OP0,
  input  OP1,
  input  OP2,
  input  OP3,
  input  OP4,
  input  OP5,
  input  F0,
  input  F1,
  input  F2,
  input  F3,
  input  F4,
  input  F5,
  output S0,
  output S1,
  output S2,
  output S3
);

  wire and_1_out, and_2_out, and_3_out, and_4_out, and_5_out, and_6_out, and_7_out, and_8_out, and_9_out,
       and_10_out, and_11_out, and_12_out, and_13_out, and_14_out, and_15_out, and_16_out, and_17_out,
       and_18_out, and_19_out, and_20_out, and_21_out, and_22_out, and_23_out, and_24_out, and_25_out,
       and_26_out, and_27_out, and_28_out, and_29_out, and_30_out, and_31_out, and_32_out, and_33_out,
       and_34_out, not_1_out, not_2_out, not_3_out, not_4_out, not_5_out, not_6_out, not_7_out, not_8_out,
       not_9_out, not_10_out, not_11_out, not_12_out, not_13_out, not_14_out, not_15_out, not_16_out,
       not_17_out, not_18_out, not_19_out, not_20_out, not_21_out, not_22_out, not_23_out, not_24_out,
       not_25_out, not_26_out, not_27_out, not_28_out, not_29_out, not_30_out, not_31_out, not_32_out,
       not_33_out, not_34_out, not_35_out, not_36_out, not_37_out, not_38_out, not_39_out, not_40_out,
       not_41_out, not_42_out, not_43_out, not_44_out, not_45_out, not_46_out, not_47_out, not_48_out,
       not_49_out, not_50_out, not_51_out, not_52_out, not_53_out, not_54_out, not_55_out, not_56_out,
       not_57_out, not_58_out, not_59_out, not_60_out, not_61_out, not_62_out, not_63_out, not_64_out,
       not_65_out, not_66_out, not_67_out, not_68_out, not_69_out, not_70_out, not_71_out, not_72_out,
       not_73_out, not_74_out, not_75_out, not_76_out, not_77_out, not_78_out, not_79_out, not_80_out,
       not_81_out, not_82_out, not_83_out, not_84_out, not_85_out, not_86_out, not_87_out, not_88_out,
       not_89_out, not_90_out, not_91_out, not_92_out, not_93_out, not_94_out, not_95_out, not_96_out,
       not_97_out, not_98_out, not_99_out, not_100_out, not_101_out, not_102_out, not_103_out, not_104_out,
       not_105_out, not_106_out, not_107_out, not_108_out, not_109_out, not_110_out, not_111_out,
       not_112_out, not_113_out, not_114_out, not_115_out, not_116_out, not_117_out, not_118_out,
       not_119_out, not_120_out, not_121_out, not_122_out, not_123_out, not_124_out, not_125_out,
       not_126_out, not_127_out, not_128_out, not_129_out, not_130_out, not_131_out, not_132_out,
       not_133_out, not_134_out, not_135_out, not_136_out, not_137_out, not_138_out, not_139_out,
       not_140_out, not_141_out, not_142_out, not_143_out, not_144_out, not_145_out, not_146_out,
       not_147_out, not_148_out, not_149_out, not_150_out, not_151_out, not_152_out, not_153_out,
       not_154_out, not_155_out, not_156_out, not_157_out, not_158_out, not_159_out, not_160_out,
       not_161_out, not_162_out, not_163_out, not_164_out, not_165_out, not_166_out, not_167_out,
       not_168_out, not_169_out, not_170_out, not_171_out, not_172_out, not_173_out, not_174_out,
       not_175_out, not_176_out, not_177_out, not_178_out, not_179_out, not_180_out, not_181_out,
       not_182_out, not_183_out, not_184_out, not_185_out, not_186_out, not_187_out, not_188_out,
       not_189_out, not_190_out, not_191_out, not_192_out, not_193_out, not_194_out, not_195_out,
       not_196_out, not_197_out, not_198_out, not_199_out, not_200_out, not_201_out, not_202_out,
       not_203_out, not_204_out, not_205_out, not_206_out, not_207_out, not_208_out, not_209_out,
       not_210_out, not_211_out, not_212_out, not_213_out, not_214_out, not_215_out, not_216_out,
       not_217_out, not_218_out, not_219_out, not_220_out, not_221_out, not_222_out, not_223_out,
       not_224_out, not_225_out, not_226_out, not_227_out, not_228_out, not_229_out, not_230_out,
       not_231_out, not_232_out, not_233_out, not_234_out, not_235_out, not_236_out;

  not not_1 (not_1_out, OP5);
  not not_2 (not_2_out, OP4);
  not not_3 (not_3_out, OP3);
  not not_4 (not_4_out, OP2);
  not not_5 (not_5_out, OP1);
  not not_6 (not_6_out, OP0);
  not not_7 (not_7_out, F5);
  not not_8 (not_8_out, F4);
  not not_9 (not_9_out, F3);
  not not_10 (not_10_out, F2);
  not not_11 (not_11_out, OP5);
  not not_12 (not_12_out, OP4);
  not not_13 (not_13_out, OP3);
  not not_14 (not_14_out, OP2);
  not not_15 (not_15_out, OP1);
  not not_16 (not_16_out, OP0);
  not not_17 (not_17_out, F4);
  not not_18 (not_18_out, F3);
  not not_19 (not_19_out, F2);
  not not_20 (not_20_out, F1);
  not not_21 (not_21_out, F0);
  not not_22 (not_22_out, OP5);
  not not_23 (not_23_out, OP4);
  not not_24 (not_24_out, OP3);
  not not_25 (not_25_out, OP2);
  not not_26 (not_26_out, OP1);
  not not_27 (not_27_out, OP0);
  not not_28 (not_28_out, F4);
  not not_29 (not_29_out, F3);
  not not_30 (not_30_out, F2);
  not not_31 (not_31_out, F1);
  not not_32 (not_32_out, OP5);
  not not_33 (not_33_out, OP4);
  not not_34 (not_34_out, OP3);
  not not_35 (not_35_out, OP2);
  not not_36 (not_36_out, OP1);
  not not_37 (not_37_out, OP0);
  not not_38 (not_38_out, F4);
  not not_39 (not_39_out, F3);
  not not_40 (not_40_out, F1);
  not not_41 (not_41_out, F0);
  not not_42 (not_42_out, OP5);
  not not_43 (not_43_out, OP4);
  not not_44 (not_44_out, OP3);
  not not_45 (not_45_out, OP2);
  not not_46 (not_46_out, OP1);
  not not_47 (not_47_out, OP0);
  not not_48 (not_48_out, F4);
  not not_49 (not_49_out, F2);
  not not_50 (not_50_out, F0);
  not not_51 (not_51_out, OP5);
  not not_52 (not_52_out, OP4);
  not not_53 (not_53_out, OP2);
  not not_54 (not_54_out, OP1);
  not not_55 (not_55_out, OP0);
  not not_56 (not_56_out, OP5);
  not not_57 (not_57_out, OP4);
  not not_58 (not_58_out, OP1);
  not not_59 (not_59_out, OP0);
  not not_60 (not_60_out, OP5);
  not not_61 (not_61_out, OP4);
  not not_62 (not_62_out, OP2);
  not not_63 (not_63_out, OP1);
  not not_64 (not_64_out, OP5);
  not not_65 (not_65_out, OP4);
  not not_66 (not_66_out, OP2);
  not not_67 (not_67_out, OP0);
  not not_68 (not_68_out, OP4);
  not not_69 (not_69_out, OP3);
  not not_70 (not_70_out, OP2);
  not not_71 (not_71_out, OP4);
  not not_72 (not_72_out, OP2);
  not not_73 (not_73_out, OP5);
  not not_74 (not_74_out, OP4);
  not not_75 (not_75_out, OP3);
  not not_76 (not_76_out, OP2);
  not not_77 (not_77_out, OP1);
  not not_78 (not_78_out, OP0);
  not not_79 (not_79_out, F5);
  not not_80 (not_80_out, F4);
  not not_81 (not_81_out, F3);
  not not_82 (not_82_out, F2);
  not not_83 (not_83_out, F0);
  not not_84 (not_84_out, OP5);
  not not_85 (not_85_out, OP4);
  not not_86 (not_86_out, OP3);
  not not_87 (not_87_out, OP2);
  not not_88 (not_88_out, OP1);
  not not_89 (not_89_out, OP0);
  not not_90 (not_90_out, F4);
  not not_91 (not_91_out, F3);
  not not_92 (not_92_out, F2);
  not not_93 (not_93_out, F0);
  not not_94 (not_94_out, OP5);
  not not_95 (not_95_out, OP4);
  not not_96 (not_96_out, OP3);
  not not_97 (not_97_out, OP2);
  not not_98 (not_98_out, OP1);
  not not_99 (not_99_out, OP0);
  not not_100 (not_100_out, F4);
  not not_101 (not_101_out, F3);
  not not_102 (not_102_out, F1);
  not not_103 (not_103_out, F0);
  not not_104 (not_104_out, OP5);
  not not_105 (not_105_out, OP4);
  not not_106 (not_106_out, OP3);
  not not_107 (not_107_out, OP2);
  not not_108 (not_108_out, OP1);
  not not_109 (not_109_out, OP0);
  not not_110 (not_110_out, F4);
  not not_111 (not_111_out, F3);
  not not_112 (not_112_out, OP5);
  not not_113 (not_113_out, OP4);
  not not_114 (not_114_out, OP3);
  not not_115 (not_115_out, OP2);
  not not_116 (not_116_out, OP1);
  not not_117 (not_117_out, OP0);
  not not_118 (not_118_out, F4);
  not not_119 (not_119_out, F2);
  not not_120 (not_120_out, F0);
  not not_121 (not_121_out, OP5);
  not not_122 (not_122_out, OP4);
  not not_123 (not_123_out, OP1);
  not not_124 (not_124_out, OP0);
  not not_125 (not_125_out, OP5);
  not not_126 (not_126_out, OP4);
  not not_127 (not_127_out, OP2);
  not not_128 (not_128_out, OP0);
  not not_129 (not_129_out, OP5);
  not not_130 (not_130_out, OP4);
  not not_131 (not_131_out, OP3);
  not not_132 (not_132_out, OP2);
  not not_133 (not_133_out, OP1);
  not not_134 (not_134_out, OP0);
  not not_135 (not_135_out, F4);
  not not_136 (not_136_out, F3);
  not not_137 (not_137_out, F2);
  not not_138 (not_138_out, F1);
  not not_139 (not_139_out, F0);
  not not_140 (not_140_out, OP5);
  not not_141 (not_141_out, OP4);
  not not_142 (not_142_out, OP3);
  not not_143 (not_143_out, OP2);
  not not_144 (not_144_out, OP1);
  not not_145 (not_145_out, OP0);
  not not_146 (not_146_out, F4);
  not not_147 (not_147_out, F3);
  not not_148 (not_148_out, F2);
  not not_149 (not_149_out, F1);
  not not_150 (not_150_out, OP5);
  not not_151 (not_151_out, OP4);
  not not_152 (not_152_out, OP3);
  not not_153 (not_153_out, OP2);
  not not_154 (not_154_out, OP1);
  not not_155 (not_155_out, OP0);
  not not_156 (not_156_out, F4);
  not not_157 (not_157_out, F3);
  not not_158 (not_158_out, F2);
  not not_159 (not_159_out, F0);
  not not_160 (not_160_out, OP5);
  not not_161 (not_161_out, OP4);
  not not_162 (not_162_out, OP3);
  not not_163 (not_163_out, OP2);
  not not_164 (not_164_out, OP1);
  not not_165 (not_165_out, OP0);
  not not_166 (not_166_out, F4);
  not not_167 (not_167_out, F3);
  not not_168 (not_168_out, F1);
  not not_169 (not_169_out, F0);
  not not_170 (not_170_out, OP5);
  not not_171 (not_171_out, OP4);
  not not_172 (not_172_out, OP3);
  not not_173 (not_173_out, OP2);
  not not_174 (not_174_out, OP1);
  not not_175 (not_175_out, OP0);
  not not_176 (not_176_out, F4);
  not not_177 (not_177_out, F2);
  not not_178 (not_178_out, OP5);
  not not_179 (not_179_out, OP4);
  not not_180 (not_180_out, OP2);
  not not_181 (not_181_out, OP1);
  not not_182 (not_182_out, OP0);
  not not_183 (not_183_out, OP5);
  not not_184 (not_184_out, OP4);
  not not_185 (not_185_out, OP1);
  not not_186 (not_186_out, OP0);
  not not_187 (not_187_out, OP5);
  not not_188 (not_188_out, OP4);
  not not_189 (not_189_out, OP2);
  not not_190 (not_190_out, OP1);
  not not_191 (not_191_out, OP4);
  not not_192 (not_192_out, OP3);
  not not_193 (not_193_out, OP2);
  not not_194 (not_194_out, OP4);
  not not_195 (not_195_out, OP2);
  not not_196 (not_196_out, OP5);
  not not_197 (not_197_out, OP4);
  not not_198 (not_198_out, OP3);
  not not_199 (not_199_out, OP2);
  not not_200 (not_200_out, OP1);
  not not_201 (not_201_out, OP0);
  not not_202 (not_202_out, F4);
  not not_203 (not_203_out, F3);
  not not_204 (not_204_out, F1);
  not not_205 (not_205_out, OP5);
  not not_206 (not_206_out, OP4);
  not not_207 (not_207_out, OP3);
  not not_208 (not_208_out, OP2);
  not not_209 (not_209_out, OP1);
  not not_210 (not_210_out, OP0);
  not not_211 (not_211_out, F4);
  not not_212 (not_212_out, F3);
  not not_213 (not_213_out, OP5);
  not not_214 (not_214_out, OP4);
  not not_215 (not_215_out, OP3);
  not not_216 (not_216_out, OP2);
  not not_217 (not_217_out, OP1);
  not not_218 (not_218_out, OP0);
  not not_219 (not_219_out, F4);
  not not_220 (not_220_out, F2);
  not not_221 (not_221_out, F0);
  not not_222 (not_222_out, OP5);
  not not_223 (not_223_out, OP4);
  not not_224 (not_224_out, OP3);
  not not_225 (not_225_out, OP2);
  not not_226 (not_226_out, OP1);
  not not_227 (not_227_out, OP0);
  not not_228 (not_228_out, F4);
  not not_229 (not_229_out, F2);
  not not_230 (not_230_out, OP5);
  not not_231 (not_231_out, OP4);
  not not_232 (not_232_out, OP2);
  not not_233 (not_233_out, OP0);
  not not_234 (not_234_out, OP5);
  not not_235 (not_235_out, OP4);
  not not_236 (not_236_out, OP1);
  and and_1 (and_1_out, not_1_out, not_2_out, not_3_out, not_4_out, not_5_out, not_6_out, not_7_out, not_8_out, not_9_out, not_10_out, F1, F0);
  and and_2 (and_2_out, not_11_out, not_12_out, not_13_out, not_14_out, not_15_out, not_16_out, F5, not_17_out, not_18_out, not_19_out, not_20_out, not_21_out);
  and and_3 (and_3_out, not_22_out, not_23_out, not_24_out, not_25_out, not_26_out, not_27_out, F5, not_28_out, not_29_out, not_30_out, not_31_out, F0);
  and and_4 (and_4_out, not_32_out, not_33_out, not_34_out, not_35_out, not_36_out, not_37_out, F5, not_38_out, not_39_out, F2, not_40_out, not_41_out);
  and and_5 (and_5_out, not_42_out, not_43_out, not_44_out, not_45_out, not_46_out, not_47_out, F5, not_48_out, F3, not_49_out, F1, not_50_out);
  and and_6 (and_6_out, not_51_out, not_52_out, OP3, not_53_out, not_54_out, not_55_out);
  and and_7 (and_7_out, not_56_out, not_57_out, OP3, OP2, not_58_out, not_59_out);
  and and_8 (and_8_out, not_60_out, not_61_out, OP3, not_62_out, not_63_out, OP0);
  and and_9 (and_9_out, not_64_out, not_65_out, OP3, not_66_out, OP1, not_67_out);
  and and_10 (and_10_out, OP5, not_68_out, not_69_out, not_70_out, OP1, OP0);
  and and_11 (and_11_out, OP5, not_71_out, OP3, not_72_out, OP1, OP0);
  and and_12 (and_12_out, not_73_out, not_74_out, not_75_out, not_76_out, not_77_out, not_78_out, not_79_out, not_80_out, not_81_out, not_82_out, F1, not_83_out);
  and and_13 (and_13_out, not_84_out, not_85_out, not_86_out, not_87_out, not_88_out, not_89_out, F5, not_90_out, not_91_out, not_92_out, F1, not_93_out);
  and and_14 (and_14_out, not_94_out, not_95_out, not_96_out, not_97_out, not_98_out, not_99_out, F5, not_100_out, not_101_out, F2, not_102_out, not_103_out);
  and and_15 (and_15_out, not_104_out, not_105_out, not_106_out, not_107_out, not_108_out, not_109_out, F5, not_110_out, not_111_out, F2, F1, F0);
  and and_16 (and_16_out, not_112_out, not_113_out, not_114_out, not_115_out, not_116_out, not_117_out, F5, not_118_out, F3, not_119_out, F1, not_120_out);
  and and_17 (and_17_out, not_121_out, not_122_out, OP3, OP2, not_123_out, not_124_out);
  and and_18 (and_18_out, not_125_out, not_126_out, OP3, not_127_out, OP1, not_128_out);
  and and_19 (and_19_out, not_129_out, not_130_out, not_131_out, not_132_out, not_133_out, not_134_out, F5, not_135_out, not_136_out, not_137_out, not_138_out, not_139_out);
  and and_20 (and_20_out, not_140_out, not_141_out, not_142_out, not_143_out, not_144_out, not_145_out, F5, not_146_out, not_147_out, not_148_out, not_149_out, F0);
  and and_21 (and_21_out, not_150_out, not_151_out, not_152_out, not_153_out, not_154_out, not_155_out, F5, not_156_out, not_157_out, not_158_out, F1, not_159_out);
  and and_22 (and_22_out, not_160_out, not_161_out, not_162_out, not_163_out, not_164_out, not_165_out, F5, not_166_out, not_167_out, F2, not_168_out, not_169_out);
  and and_23 (and_23_out, not_170_out, not_171_out, not_172_out, not_173_out, not_174_out, not_175_out, F5, not_176_out, F3, not_177_out, F1, F0);
  and and_24 (and_24_out, not_178_out, not_179_out, OP3, not_180_out, not_181_out, not_182_out);
  and and_25 (and_25_out, not_183_out, not_184_out, OP3, OP2, not_185_out, not_186_out);
  and and_26 (and_26_out, not_187_out, not_188_out, OP3, not_189_out, not_190_out, OP0);
  and and_27 (and_27_out, OP5, not_191_out, not_192_out, not_193_out, OP1, OP0);
  and and_28 (and_28_out, OP5, not_194_out, OP3, not_195_out, OP1, OP0);
  and and_29 (and_29_out, not_196_out, not_197_out, not_198_out, not_199_out, not_200_out, not_201_out, F5, not_202_out, not_203_out, F2, not_204_out, F0);
  and and_30 (and_30_out, not_205_out, not_206_out, not_207_out, not_208_out, not_209_out, not_210_out, F5, not_211_out, not_212_out, F2, F1, F0);
  and and_31 (and_31_out, not_213_out, not_214_out, not_215_out, not_216_out, not_217_out, not_218_out, F5, not_219_out, F3, not_220_out, F1, not_221_out);
  and and_32 (and_32_out, not_222_out, not_223_out, not_224_out, not_225_out, not_226_out, not_227_out, F5, not_228_out, F3, not_229_out, F1, F0);
  and and_33 (and_33_out, not_230_out, not_231_out, OP3, not_232_out, OP1, not_233_out);
  and and_34 (and_34_out, not_234_out, not_235_out, OP3, OP2, not_236_out, OP0);
  or or_1 (S0, and_1_out, and_2_out, and_3_out, and_4_out, and_5_out, and_6_out, and_7_out, and_8_out, and_9_out, and_10_out, and_11_out);
  or or_2 (S1, and_12_out, and_13_out, and_14_out, and_15_out, and_16_out, and_17_out, and_18_out);
  or or_3 (S2, and_19_out, and_20_out, and_21_out, and_22_out, and_23_out, and_24_out, and_25_out, and_26_out, and_27_out, and_28_out);
  or or_4 (S3, and_29_out, and_30_out, and_31_out, and_32_out, and_33_out, and_34_out);
endmodule

// 控制信号生成
module \控制信号生成  (
  input  OP0,
  input  OP1,
  input  OP2,
  input  OP3,
  input  OP4,
  input  OP5,
  input  F0,
  input  F1,
  input  F2,
  input  F3,
  input  F4,
  input  F5,
  output MemToReg,
  output MemWrite,
  output ALU_SRC,
  output RegWrite,
  output SysCALL,
  output SignedExt,
  output RegDst,
  output BEQ,
  output BNE,
  output JR,
  output JMP,
  output JAL
);

  wire and_3_out, and_4_out, and_5_out, and_6_out, and_7_out, and_8_out, and_9_out, and_10_out, and_11_out,
       and_12_out, and_13_out, and_14_out, and_15_out, and_16_out, and_17_out, and_18_out, and_19_out,
       and_20_out, and_21_out, and_22_out, and_23_out, and_24_out, and_25_out, and_26_out, and_27_out,
       and_29_out, and_30_out, and_31_out, and_32_out, and_33_out, and_34_out, and_35_out, and_36_out,
       and_37_out, and_38_out, and_39_out, and_40_out, and_41_out, and_42_out, and_43_out, and_44_out,
       and_48_out, and_49_out, and_50_out, not_1_out, not_2_out, not_3_out, not_4_out, not_5_out, not_6_out,
       not_7_out, not_8_out, not_9_out, not_10_out, not_11_out, not_12_out, not_13_out, not_14_out,
       not_15_out, not_16_out, not_17_out, not_18_out, not_19_out, not_20_out, not_21_out, not_22_out,
       not_23_out, not_24_out, not_25_out, not_26_out, not_27_out, not_28_out, not_29_out, not_30_out,
       not_31_out, not_32_out, not_33_out, not_34_out, not_35_out, not_36_out, not_37_out, not_38_out,
       not_39_out, not_40_out, not_41_out, not_42_out, not_43_out, not_44_out, not_45_out, not_46_out,
       not_47_out, not_48_out, not_49_out, not_50_out, not_51_out, not_52_out, not_53_out, not_54_out,
       not_55_out, not_56_out, not_57_out, not_58_out, not_59_out, not_60_out, not_61_out, not_62_out,
       not_63_out, not_64_out, not_65_out, not_66_out, not_67_out, not_68_out, not_69_out, not_70_out,
       not_71_out, not_72_out, not_73_out, not_74_out, not_75_out, not_76_out, not_77_out, not_78_out,
       not_79_out, not_80_out, not_81_out, not_82_out, not_83_out, not_84_out, not_85_out, not_86_out,
       not_87_out, not_88_out, not_89_out, not_90_out, not_91_out, not_92_out, not_93_out, not_94_out,
       not_95_out, not_96_out, not_97_out, not_98_out, not_99_out, not_100_out, not_101_out, not_102_out,
       not_103_out, not_104_out, not_105_out, not_106_out, not_107_out, not_108_out, not_109_out,
       not_110_out, not_111_out, not_112_out, not_113_out, not_114_out, not_115_out, not_116_out,
       not_117_out, not_118_out, not_119_out, not_120_out, not_121_out, not_122_out, not_123_out,
       not_124_out, not_125_out, not_126_out, not_127_out, not_128_out, not_129_out, not_130_out,
       not_131_out, not_132_out, not_133_out, not_134_out, not_135_out, not_136_out, not_137_out,
       not_138_out, not_139_out, not_140_out, not_141_out, not_142_out, not_143_out, not_144_out,
       not_145_out, not_146_out, not_147_out, not_148_out, not_149_out, not_150_out, not_151_out,
       not_152_out, not_153_out, not_154_out, not_155_out, not_156_out, not_157_out, not_158_out,
       not_159_out, not_160_out, not_161_out, not_162_out, not_163_out, not_164_out, not_165_out,
       not_166_out, not_167_out, not_168_out, not_169_out, not_170_out, not_171_out, not_172_out,
       not_173_out, not_174_out, not_175_out, not_176_out, not_177_out, not_178_out, not_179_out,
       not_180_out, not_181_out, not_182_out, not_183_out, not_184_out, not_185_out, not_186_out,
       not_187_out, not_188_out, not_189_out, not_190_out, not_191_out, not_192_out, not_193_out,
       not_194_out, not_195_out, not_196_out, not_197_out, not_198_out, not_199_out, not_200_out,
       not_201_out, not_202_out, not_203_out, not_204_out, not_205_out, not_206_out, not_207_out,
       not_208_out, not_209_out, not_210_out, not_211_out, not_212_out, not_213_out, not_214_out,
       not_215_out, not_216_out, not_217_out, not_218_out, not_219_out, not_220_out, not_221_out,
       not_222_out, not_223_out, not_224_out, not_225_out, not_226_out, not_227_out, not_228_out,
       not_229_out, not_230_out, not_231_out, not_232_out, not_233_out, not_234_out, not_235_out,
       not_236_out, not_237_out, not_238_out, not_239_out, not_240_out, not_241_out, not_242_out,
       not_243_out, not_244_out, not_245_out, not_246_out, not_247_out, not_248_out, not_249_out,
       not_250_out, not_251_out, not_252_out, not_253_out, not_254_out, not_255_out, not_256_out,
       not_257_out, not_258_out, not_259_out, not_260_out, not_261_out, not_262_out, not_263_out,
       not_264_out, not_265_out, not_266_out, not_267_out, not_268_out, not_269_out, not_270_out,
       not_271_out, not_272_out, not_273_out, not_274_out, not_275_out, not_276_out, not_277_out,
       not_278_out, not_279_out, not_280_out, not_281_out, not_282_out, not_283_out, not_284_out,
       not_285_out, not_286_out, not_287_out, not_288_out, not_289_out, not_290_out, not_291_out,
       not_292_out, not_293_out, not_294_out, not_295_out, not_296_out, not_297_out, not_298_out,
       not_299_out, not_300_out, not_301_out, not_302_out, not_303_out, not_304_out, not_305_out,
       not_306_out, not_307_out, not_308_out, not_309_out, not_310_out, not_311_out, not_312_out,
       not_313_out, not_314_out, not_315_out, not_316_out, not_317_out, not_318_out, not_319_out,
       not_320_out, not_321_out, not_322_out, not_323_out, not_324_out, not_325_out, not_326_out,
       not_327_out, not_328_out, not_329_out, not_330_out, not_331_out, not_332_out, not_333_out,
       not_334_out, not_335_out, not_336_out, not_337_out, not_338_out, not_339_out, not_340_out,
       not_341_out, not_342_out, not_343_out, not_344_out, not_345_out;

  not not_1 (not_1_out, OP4);
  not not_2 (not_2_out, OP3);
  not not_3 (not_3_out, OP2);
  not not_4 (not_4_out, OP4);
  not not_5 (not_5_out, OP2);
  not not_6 (not_6_out, OP5);
  not not_7 (not_7_out, OP4);
  not not_8 (not_8_out, OP2);
  not not_9 (not_9_out, OP1);
  not not_10 (not_10_out, OP0);
  not not_11 (not_11_out, OP5);
  not not_12 (not_12_out, OP4);
  not not_13 (not_13_out, OP1);
  not not_14 (not_14_out, OP0);
  not not_15 (not_15_out, OP5);
  not not_16 (not_16_out, OP4);
  not not_17 (not_17_out, OP2);
  not not_18 (not_18_out, OP1);
  not not_19 (not_19_out, OP5);
  not not_20 (not_20_out, OP4);
  not not_21 (not_21_out, OP2);
  not not_22 (not_22_out, OP0);
  not not_23 (not_23_out, OP5);
  not not_24 (not_24_out, OP4);
  not not_25 (not_25_out, OP1);
  not not_26 (not_26_out, OP4);
  not not_27 (not_27_out, OP3);
  not not_28 (not_28_out, OP2);
  not not_29 (not_29_out, OP4);
  not not_30 (not_30_out, OP2);
  not not_31 (not_31_out, OP5);
  not not_32 (not_32_out, OP4);
  not not_33 (not_33_out, OP3);
  not not_34 (not_34_out, OP2);
  not not_35 (not_35_out, OP1);
  not not_36 (not_36_out, OP0);
  not not_37 (not_37_out, F5);
  not not_38 (not_38_out, F4);
  not not_39 (not_39_out, F3);
  not not_40 (not_40_out, F2);
  not not_41 (not_41_out, F1);
  not not_42 (not_42_out, F0);
  not not_43 (not_43_out, OP5);
  not not_44 (not_44_out, OP4);
  not not_45 (not_45_out, OP3);
  not not_46 (not_46_out, OP2);
  not not_47 (not_47_out, OP1);
  not not_48 (not_48_out, OP0);
  not not_49 (not_49_out, F5);
  not not_50 (not_50_out, F4);
  not not_51 (not_51_out, F3);
  not not_52 (not_52_out, F2);
  not not_53 (not_53_out, OP5);
  not not_54 (not_54_out, OP4);
  not not_55 (not_55_out, OP3);
  not not_56 (not_56_out, OP2);
  not not_57 (not_57_out, OP1);
  not not_58 (not_58_out, OP0);
  not not_59 (not_59_out, F5);
  not not_60 (not_60_out, F4);
  not not_61 (not_61_out, F3);
  not not_62 (not_62_out, F2);
  not not_63 (not_63_out, F0);
  not not_64 (not_64_out, OP5);
  not not_65 (not_65_out, OP4);
  not not_66 (not_66_out, OP3);
  not not_67 (not_67_out, OP2);
  not not_68 (not_68_out, OP1);
  not not_69 (not_69_out, OP0);
  not not_70 (not_70_out, F4);
  not not_71 (not_71_out, F3);
  not not_72 (not_72_out, F2);
  not not_73 (not_73_out, F1);
  not not_74 (not_74_out, F0);
  not not_75 (not_75_out, OP5);
  not not_76 (not_76_out, OP4);
  not not_77 (not_77_out, OP3);
  not not_78 (not_78_out, OP2);
  not not_79 (not_79_out, OP1);
  not not_80 (not_80_out, OP0);
  not not_81 (not_81_out, F4);
  not not_82 (not_82_out, F3);
  not not_83 (not_83_out, F2);
  not not_84 (not_84_out, F1);
  not not_85 (not_85_out, OP5);
  not not_86 (not_86_out, OP4);
  not not_87 (not_87_out, OP3);
  not not_88 (not_88_out, OP2);
  not not_89 (not_89_out, OP1);
  not not_90 (not_90_out, OP0);
  not not_91 (not_91_out, F4);
  not not_92 (not_92_out, F3);
  not not_93 (not_93_out, F2);
  not not_94 (not_94_out, F0);
  not not_95 (not_95_out, OP5);
  not not_96 (not_96_out, OP4);
  not not_97 (not_97_out, OP3);
  not not_98 (not_98_out, OP2);
  not not_99 (not_99_out, OP1);
  not not_100 (not_100_out, OP0);
  not not_101 (not_101_out, F4);
  not not_102 (not_102_out, F3);
  not not_103 (not_103_out, F1);
  not not_104 (not_104_out, F0);
  not not_105 (not_105_out, OP5);
  not not_106 (not_106_out, OP4);
  not not_107 (not_107_out, OP3);
  not not_108 (not_108_out, OP2);
  not not_109 (not_109_out, OP1);
  not not_110 (not_110_out, OP0);
  not not_111 (not_111_out, F4);
  not not_112 (not_112_out, F3);
  not not_113 (not_113_out, F1);
  not not_114 (not_114_out, OP5);
  not not_115 (not_115_out, OP4);
  not not_116 (not_116_out, OP3);
  not not_117 (not_117_out, OP2);
  not not_118 (not_118_out, OP1);
  not not_119 (not_119_out, OP0);
  not not_120 (not_120_out, F4);
  not not_121 (not_121_out, F3);
  not not_122 (not_122_out, OP5);
  not not_123 (not_123_out, OP4);
  not not_124 (not_124_out, OP3);
  not not_125 (not_125_out, OP2);
  not not_126 (not_126_out, OP1);
  not not_127 (not_127_out, OP0);
  not not_128 (not_128_out, F4);
  not not_129 (not_129_out, F2);
  not not_130 (not_130_out, F0);
  not not_131 (not_131_out, OP5);
  not not_132 (not_132_out, OP4);
  not not_133 (not_133_out, OP3);
  not not_134 (not_134_out, OP2);
  not not_135 (not_135_out, OP1);
  not not_136 (not_136_out, OP0);
  not not_137 (not_137_out, F4);
  not not_138 (not_138_out, F2);
  not not_139 (not_139_out, OP5);
  not not_140 (not_140_out, OP4);
  not not_141 (not_141_out, OP3);
  not not_142 (not_142_out, OP2);
  not not_143 (not_143_out, OP5);
  not not_144 (not_144_out, OP4);
  not not_145 (not_145_out, OP2);
  not not_146 (not_146_out, OP1);
  not not_147 (not_147_out, OP0);
  not not_148 (not_148_out, OP5);
  not not_149 (not_149_out, OP4);
  not not_150 (not_150_out, OP1);
  not not_151 (not_151_out, OP0);
  not not_152 (not_152_out, OP5);
  not not_153 (not_153_out, OP4);
  not not_154 (not_154_out, OP2);
  not not_155 (not_155_out, OP1);
  not not_156 (not_156_out, OP5);
  not not_157 (not_157_out, OP4);
  not not_158 (not_158_out, OP2);
  not not_159 (not_159_out, OP0);
  not not_160 (not_160_out, OP5);
  not not_161 (not_161_out, OP4);
  not not_162 (not_162_out, OP1);
  not not_163 (not_163_out, OP4);
  not not_164 (not_164_out, OP3);
  not not_165 (not_165_out, OP2);
  not not_166 (not_166_out, OP5);
  not not_167 (not_167_out, OP4);
  not not_168 (not_168_out, OP3);
  not not_169 (not_169_out, OP2);
  not not_170 (not_170_out, OP1);
  not not_171 (not_171_out, OP0);
  not not_172 (not_172_out, F5);
  not not_173 (not_173_out, F4);
  not not_174 (not_174_out, F1);
  not not_175 (not_175_out, F0);
  not not_176 (not_176_out, OP5);
  not not_177 (not_177_out, OP4);
  not not_178 (not_178_out, OP2);
  not not_179 (not_179_out, OP1);
  not not_180 (not_180_out, OP0);
  not not_181 (not_181_out, OP5);
  not not_182 (not_182_out, OP4);
  not not_183 (not_183_out, OP2);
  not not_184 (not_184_out, OP1);
  not not_185 (not_185_out, OP5);
  not not_186 (not_186_out, OP4);
  not not_187 (not_187_out, OP2);
  not not_188 (not_188_out, OP0);
  not not_189 (not_189_out, OP4);
  not not_190 (not_190_out, OP3);
  not not_191 (not_191_out, OP2);
  not not_192 (not_192_out, OP4);
  not not_193 (not_193_out, OP2);
  not not_194 (not_194_out, OP5);
  not not_195 (not_195_out, OP4);
  not not_196 (not_196_out, OP3);
  not not_197 (not_197_out, OP2);
  not not_198 (not_198_out, OP1);
  not not_199 (not_199_out, OP0);
  not not_200 (not_200_out, F5);
  not not_201 (not_201_out, F4);
  not not_202 (not_202_out, F3);
  not not_203 (not_203_out, F2);
  not not_204 (not_204_out, F1);
  not not_205 (not_205_out, F0);
  not not_206 (not_206_out, OP5);
  not not_207 (not_207_out, OP4);
  not not_208 (not_208_out, OP3);
  not not_209 (not_209_out, OP2);
  not not_210 (not_210_out, OP1);
  not not_211 (not_211_out, OP0);
  not not_212 (not_212_out, F5);
  not not_213 (not_213_out, F4);
  not not_214 (not_214_out, F3);
  not not_215 (not_215_out, F2);
  not not_216 (not_216_out, OP5);
  not not_217 (not_217_out, OP4);
  not not_218 (not_218_out, OP3);
  not not_219 (not_219_out, OP2);
  not not_220 (not_220_out, OP1);
  not not_221 (not_221_out, OP0);
  not not_222 (not_222_out, F5);
  not not_223 (not_223_out, F4);
  not not_224 (not_224_out, F3);
  not not_225 (not_225_out, F2);
  not not_226 (not_226_out, F0);
  not not_227 (not_227_out, OP5);
  not not_228 (not_228_out, OP4);
  not not_229 (not_229_out, OP3);
  not not_230 (not_230_out, OP2);
  not not_231 (not_231_out, OP1);
  not not_232 (not_232_out, OP0);
  not not_233 (not_233_out, F4);
  not not_234 (not_234_out, F3);
  not not_235 (not_235_out, F2);
  not not_236 (not_236_out, F1);
  not not_237 (not_237_out, F0);
  not not_238 (not_238_out, OP5);
  not not_239 (not_239_out, OP4);
  not not_240 (not_240_out, OP3);
  not not_241 (not_241_out, OP2);
  not not_242 (not_242_out, OP1);
  not not_243 (not_243_out, OP0);
  not not_244 (not_244_out, F4);
  not not_245 (not_245_out, F3);
  not not_246 (not_246_out, F2);
  not not_247 (not_247_out, F1);
  not not_248 (not_248_out, OP5);
  not not_249 (not_249_out, OP4);
  not not_250 (not_250_out, OP3);
  not not_251 (not_251_out, OP2);
  not not_252 (not_252_out, OP1);
  not not_253 (not_253_out, OP0);
  not not_254 (not_254_out, F4);
  not not_255 (not_255_out, F3);
  not not_256 (not_256_out, F2);
  not not_257 (not_257_out, F0);
  not not_258 (not_258_out, OP5);
  not not_259 (not_259_out, OP4);
  not not_260 (not_260_out, OP3);
  not not_261 (not_261_out, OP2);
  not not_262 (not_262_out, OP1);
  not not_263 (not_263_out, OP0);
  not not_264 (not_264_out, F4);
  not not_265 (not_265_out, F3);
  not not_266 (not_266_out, F1);
  not not_267 (not_267_out, F0);
  not not_268 (not_268_out, OP5);
  not not_269 (not_269_out, OP4);
  not not_270 (not_270_out, OP3);
  not not_271 (not_271_out, OP2);
  not not_272 (not_272_out, OP1);
  not not_273 (not_273_out, OP0);
  not not_274 (not_274_out, F4);
  not not_275 (not_275_out, F3);
  not not_276 (not_276_out, F1);
  not not_277 (not_277_out, OP5);
  not not_278 (not_278_out, OP4);
  not not_279 (not_279_out, OP3);
  not not_280 (not_280_out, OP2);
  not not_281 (not_281_out, OP1);
  not not_282 (not_282_out, OP0);
  not not_283 (not_283_out, F4);
  not not_284 (not_284_out, F3);
  not not_285 (not_285_out, OP5);
  not not_286 (not_286_out, OP4);
  not not_287 (not_287_out, OP3);
  not not_288 (not_288_out, OP2);
  not not_289 (not_289_out, OP1);
  not not_290 (not_290_out, OP0);
  not not_291 (not_291_out, F4);
  not not_292 (not_292_out, F2);
  not not_293 (not_293_out, F0);
  not not_294 (not_294_out, OP5);
  not not_295 (not_295_out, OP4);
  not not_296 (not_296_out, OP3);
  not not_297 (not_297_out, OP2);
  not not_298 (not_298_out, OP1);
  not not_299 (not_299_out, OP0);
  not not_300 (not_300_out, F4);
  not not_301 (not_301_out, F2);
  not not_302 (not_302_out, OP5);
  not not_303 (not_303_out, OP4);
  not not_304 (not_304_out, OP3);
  not not_305 (not_305_out, OP1);
  not not_306 (not_306_out, OP0);
  not not_307 (not_307_out, OP5);
  not not_308 (not_308_out, OP4);
  not not_309 (not_309_out, OP3);
  not not_310 (not_310_out, OP1);
  not not_311 (not_311_out, OP5);
  not not_312 (not_312_out, OP4);
  not not_313 (not_313_out, OP3);
  not not_314 (not_314_out, OP2);
  not not_315 (not_315_out, OP1);
  not not_316 (not_316_out, OP0);
  not not_317 (not_317_out, F5);
  not not_318 (not_318_out, F4);
  not not_319 (not_319_out, F2);
  not not_320 (not_320_out, F1);
  not not_321 (not_321_out, F0);
  not not_322 (not_322_out, OP5);
  not not_323 (not_323_out, OP4);
  not not_324 (not_324_out, OP3);
  not not_325 (not_325_out, OP2);
  not not_326 (not_326_out, OP1);
  not not_327 (not_327_out, OP0);
  not not_328 (not_328_out, F5);
  not not_329 (not_329_out, F4);
  not not_330 (not_330_out, F2);
  not not_331 (not_331_out, F1);
  not not_332 (not_332_out, F0);
  not not_333 (not_333_out, OP5);
  not not_334 (not_334_out, OP4);
  not not_335 (not_335_out, OP3);
  not not_336 (not_336_out, OP2);
  not not_337 (not_337_out, OP0);
  not not_338 (not_338_out, OP5);
  not not_339 (not_339_out, OP4);
  not not_340 (not_340_out, OP3);
  not not_341 (not_341_out, OP2);
  not not_342 (not_342_out, OP5);
  not not_343 (not_343_out, OP4);
  not not_344 (not_344_out, OP3);
  not not_345 (not_345_out, OP2);
  and and_1 (MemToReg, OP5, not_1_out, not_2_out, not_3_out, OP1, OP0);
  and and_2 (MemWrite, OP5, not_4_out, OP3, not_5_out, OP1, OP0);
  and and_3 (and_3_out, not_6_out, not_7_out, OP3, not_8_out, not_9_out, not_10_out);
  and and_4 (and_4_out, not_11_out, not_12_out, OP3, OP2, not_13_out, not_14_out);
  and and_5 (and_5_out, not_15_out, not_16_out, OP3, not_17_out, not_18_out, OP0);
  and and_6 (and_6_out, not_19_out, not_20_out, OP3, not_21_out, OP1, not_22_out);
  and and_7 (and_7_out, not_23_out, not_24_out, OP3, OP2, not_25_out, OP0);
  and and_8 (and_8_out, OP5, not_26_out, not_27_out, not_28_out, OP1, OP0);
  and and_9 (and_9_out, OP5, not_29_out, OP3, not_30_out, OP1, OP0);
  and and_10 (and_10_out, not_31_out, not_32_out, not_33_out, not_34_out, not_35_out, not_36_out, not_37_out, not_38_out, not_39_out, not_40_out, not_41_out, not_42_out);
  and and_11 (and_11_out, not_43_out, not_44_out, not_45_out, not_46_out, not_47_out, not_48_out, not_49_out, not_50_out, not_51_out, not_52_out, F1, F0);
  and and_12 (and_12_out, not_53_out, not_54_out, not_55_out, not_56_out, not_57_out, not_58_out, not_59_out, not_60_out, not_61_out, not_62_out, F1, not_63_out);
  and and_13 (and_13_out, not_64_out, not_65_out, not_66_out, not_67_out, not_68_out, not_69_out, F5, not_70_out, not_71_out, not_72_out, not_73_out, not_74_out);
  and and_14 (and_14_out, not_75_out, not_76_out, not_77_out, not_78_out, not_79_out, not_80_out, F5, not_81_out, not_82_out, not_83_out, not_84_out, F0);
  and and_15 (and_15_out, not_85_out, not_86_out, not_87_out, not_88_out, not_89_out, not_90_out, F5, not_91_out, not_92_out, not_93_out, F1, not_94_out);
  and and_16 (and_16_out, not_95_out, not_96_out, not_97_out, not_98_out, not_99_out, not_100_out, F5, not_101_out, not_102_out, F2, not_103_out, not_104_out);
  and and_17 (and_17_out, not_105_out, not_106_out, not_107_out, not_108_out, not_109_out, not_110_out, F5, not_111_out, not_112_out, F2, not_113_out, F0);
  and and_18 (and_18_out, not_114_out, not_115_out, not_116_out, not_117_out, not_118_out, not_119_out, F5, not_120_out, not_121_out, F2, F1, F0);
  and and_19 (and_19_out, not_122_out, not_123_out, not_124_out, not_125_out, not_126_out, not_127_out, F5, not_128_out, F3, not_129_out, F1, not_130_out);
  and and_20 (and_20_out, not_131_out, not_132_out, not_133_out, not_134_out, not_135_out, not_136_out, F5, not_137_out, F3, not_138_out, F1, F0);
  and and_21 (and_21_out, not_139_out, not_140_out, not_141_out, not_142_out, OP1, OP0);
  and and_22 (and_22_out, not_143_out, not_144_out, OP3, not_145_out, not_146_out, not_147_out);
  and and_23 (and_23_out, not_148_out, not_149_out, OP3, OP2, not_150_out, not_151_out);
  and and_24 (and_24_out, not_152_out, not_153_out, OP3, not_154_out, not_155_out, OP0);
  and and_25 (and_25_out, not_156_out, not_157_out, OP3, not_158_out, OP1, not_159_out);
  and and_26 (and_26_out, not_160_out, not_161_out, OP3, OP2, not_162_out, OP0);
  and and_27 (and_27_out, OP5, not_163_out, not_164_out, not_165_out, OP1, OP0);
  and and_28 (SysCALL, not_166_out, not_167_out, not_168_out, not_169_out, not_170_out, not_171_out, not_172_out, not_173_out, F3, F2, not_174_out, not_175_out);
  and and_29 (and_29_out, not_176_out, not_177_out, OP3, not_178_out, not_179_out, not_180_out);
  and and_30 (and_30_out, not_181_out, not_182_out, OP3, not_183_out, not_184_out, OP0);
  and and_31 (and_31_out, not_185_out, not_186_out, OP3, not_187_out, OP1, not_188_out);
  and and_32 (and_32_out, OP5, not_189_out, not_190_out, not_191_out, OP1, OP0);
  and and_33 (and_33_out, OP5, not_192_out, OP3, not_193_out, OP1, OP0);
  and and_34 (and_34_out, not_194_out, not_195_out, not_196_out, not_197_out, not_198_out, not_199_out, not_200_out, not_201_out, not_202_out, not_203_out, not_204_out, not_205_out);
  and and_35 (and_35_out, not_206_out, not_207_out, not_208_out, not_209_out, not_210_out, not_211_out, not_212_out, not_213_out, not_214_out, not_215_out, F1, F0);
  and and_36 (and_36_out, not_216_out, not_217_out, not_218_out, not_219_out, not_220_out, not_221_out, not_222_out, not_223_out, not_224_out, not_225_out, F1, not_226_out);
  and and_37 (and_37_out, not_227_out, not_228_out, not_229_out, not_230_out, not_231_out, not_232_out, F5, not_233_out, not_234_out, not_235_out, not_236_out, not_237_out);
  and and_38 (and_38_out, not_238_out, not_239_out, not_240_out, not_241_out, not_242_out, not_243_out, F5, not_244_out, not_245_out, not_246_out, not_247_out, F0);
  and and_39 (and_39_out, not_248_out, not_249_out, not_250_out, not_251_out, not_252_out, not_253_out, F5, not_254_out, not_255_out, not_256_out, F1, not_257_out);
  and and_40 (and_40_out, not_258_out, not_259_out, not_260_out, not_261_out, not_262_out, not_263_out, F5, not_264_out, not_265_out, F2, not_266_out, not_267_out);
  and and_41 (and_41_out, not_268_out, not_269_out, not_270_out, not_271_out, not_272_out, not_273_out, F5, not_274_out, not_275_out, F2, not_276_out, F0);
  and and_42 (and_42_out, not_277_out, not_278_out, not_279_out, not_280_out, not_281_out, not_282_out, F5, not_283_out, not_284_out, F2, F1, F0);
  and and_43 (and_43_out, not_285_out, not_286_out, not_287_out, not_288_out, not_289_out, not_290_out, F5, not_291_out, F3, not_292_out, F1, not_293_out);
  and and_44 (and_44_out, not_294_out, not_295_out, not_296_out, not_297_out, not_298_out, not_299_out, F5, not_300_out, F3, not_301_out, F1, F0);
  and and_45 (BEQ, not_302_out, not_303_out, not_304_out, OP2, not_305_out, not_306_out);
  and and_46 (BNE, not_307_out, not_308_out, not_309_out, OP2, not_310_out, OP0);
  and and_47 (JR, not_311_out, not_312_out, not_313_out, not_314_out, not_315_out, not_316_out, not_317_out, not_318_out, F3, not_319_out, not_320_out, not_321_out);
  and and_48 (and_48_out, not_322_out, not_323_out, not_324_out, not_325_out, not_326_out, not_327_out, not_328_out, not_329_out, F3, not_330_out, not_331_out, not_332_out);
  and and_49 (and_49_out, not_333_out, not_334_out, not_335_out, not_336_out, OP1, not_337_out);
  and and_50 (and_50_out, not_338_out, not_339_out, not_340_out, not_341_out, OP1, OP0);
  and and_51 (JAL, not_342_out, not_343_out, not_344_out, not_345_out, OP1, OP0);
  or or_1 (ALU_SRC, and_3_out, and_4_out, and_5_out, and_6_out, and_7_out, and_8_out, and_9_out);
  or or_2 (SignedExt, and_29_out, and_30_out, and_31_out, and_32_out, and_33_out);
  or or_3 (RegDst, and_34_out, and_35_out, and_36_out, and_37_out, and_38_out, and_39_out, and_40_out, and_41_out, and_42_out, and_43_out, and_44_out);
  or or_4 (JMP, and_48_out, and_49_out, and_50_out);
  or or_5 (RegWrite, and_10_out, and_11_out, and_12_out, and_13_out, and_14_out, and_15_out, and_16_out, and_17_out, and_18_out, and_19_out, and_20_out, and_21_out, and_22_out, and_23_out, and_24_out, and_25_out, and_26_out, and_27_out);
endmodule

// ALU
module MIPS_ALU (
  input  [4:0] shamt,
  input  [31:0] X,
  input  [31:0] Y,
  input  [3:0] AluOP,
  output Equal,
  output [31:0] Result,
  output [31:0] Result_2
);

  wire [0:0] comparator_1_lt, comparator_2_lt;
  wire [31:0] adder_1_out, AND_out, divider_1_out, divider_1_rem, multiplier_1_cout, multiplier_1_out,
       NOR_out, OR_out, shifter_1_out, shifter_2_out, shifter_3_out, subtractor_1_out, XOR_out;

  assign AND_out = X & Y;  // AND_Gate AND, 32 bits wide
  assign OR_out = X | Y;  // OR_Gate OR, 32 bits wide
  Shifter #(.width(32)) shifter_1 (.in(Y), .\dist (shamt), .out(shifter_1_out));
  Shifter #(.width(32), .shift("ar")) shifter_2 (.in(Y), .\dist (shamt), .out(shifter_2_out));
  Shifter #(.width(32), .shift("lr")) shifter_3 (.in(Y), .\dist (shamt), .out(shifter_3_out));
  Multiplier #(.width(32)) multiplier_1 (.a(X), .b(Y), .out(multiplier_1_out), .cout(multiplier_1_cout));  // open: cin
  Divider #(.width(32)) divider_1 (.a(X), .b(Y), .out(divider_1_out), .rem(divider_1_rem));  // open: upper
  Adder #(.width(32)) adder_1 (.a(X), .b(Y), .out(adder_1_out));  // open: cin, cout
  Subtractor #(.width(32)) subtractor_1 (.a(X), .b(Y), .out(subtractor_1_out));  // open: bin, bout
  assign XOR_out = X ^ Y;  // XOR_Gate XOR, 32 bits wide
  assign NOR_out = ~(X | Y);  // NOR_Gate NOR, 32 bits wide
  Comparator #(.width(32)) comparator_1 (.a(X), .b(Y), .eq(Equal), .lt(comparator_1_lt[0]));  // open: gt
  Comparator #(.width(32), .mode("unsigned")) comparator_2 (.a(X), .b(Y), .lt(comparator_2_lt[0]));  // open: gt, eq
  Multiplexer #(.select(4), .width(32), .enable("false")) multiplexer_1 (
    .in0(shifter_1_out), .in1(shifter_2_out), .in2(shifter_3_out), .in3(multiplier_1_out),
    .in4(divider_1_out), .in5(adder_1_out), .in6(subtractor_1_out), .in7(AND_out), .in8(OR_out),
    .in9(XOR_out), .in10(NOR_out), .in11({{31{1'b0}}, comparator_1_lt[0]}),
    .in12({{31{1'b0}}, comparator_2_lt[0]}), .in13({32{1'b0}}), .in14({32{1'b0}}), .in15({32{1'b0}}),
    .out(Result), .sel(AluOP));
  Multiplexer #(.select(4), .width(32), .enable("false")) multiplexer_2 (
    .in0({32{1'b0}}), .in1({32{1'b0}}), .in2({32{1'b0}}), .in3(multiplier_1_cout), .in4(divider_1_rem),
    .in5({32{1'b0}}), .in6({32{1'b0}}), .in7({32{1'b0}}), .in8({32{1'b0}}), .in9({32{1'b0}}),
    .in10({32{1'b0}}), .in11({32{1'b0}}), .in12({32{1'b0}}), .in13({32{1'b0}}), .in14({32{1'b0}}),
    .in15({32{1'b0}}), .out(Result_2), .sel(AluOP));

  // Other names for the same wires on the sheet: Result2[31:0] = Result_2; S[3:0] = AluOP

  // Notes on the sheet:
  //   不要改变此引脚区域内容，也不要改变ALU封装形式
  //   输入引脚
  //   输出引脚
endmodule

module MIPS_Regifile (
  input  [31:0] Din,
  input  Clk,
  input  WE,
  input  [4:0] R1_num,
  input  [4:0] W_num,
  input  [4:0] R2_num,
  output [31:0] R1,
  output [31:0] R2
);

  // RegisterFile registerfile_1: pin names not known; wires that end beside it: Din, Clk, WE, W_num, R1_num, R2_num, R1, R2
endmodule

module \理想流水线  (
);

  wire alusrc, and_1_out, and_2_out, beq, bne, CLK, Ena, ex_mem_1_memtoreg_2, ex_mem_1_memwrite_2,
       ex_mem_1_regdst_2, ex_mem_1_regwrite_2, ex_mem_1_syscall_2, Go, id_ex_1_p23, id_ex_1_p24, id_ex_1_p25,
       id_ex_1_p26, id_ex_1_p27, id_ex_1_p28, id_ex_1_p29, id_ex_1_p30, IR1, IR2, IR3, jal,
       mem_wb_1_memtoreg_2, mem_wb_1_regdst_2, mem_wb_1_regwrite_2, MemToReg, Memwrite, mips_alu_1_equal,
       not_1_out, not_2_out, or_1_out, redgdst, regwrite, RST, signedext, syscall, W1, W2, W3;
  wire [3:0] aluop, id_ex_1_p31;
  wire [4:0] ex_mem_1_rd_2, ex_mem_1_rt_2, id_ex_1_p32, id_ex_1_p33, mem_wb_1_rd_2, mem_wb_1_rt_2,
       multiplexer_4_out, shamt;
  wire [15:0] \LoadUse次数 , \总周期数 , \插入气泡数 , \无条件分支数 , \条件分支成功数 ;
  wire [31:0] adder_1_out, adder_2_out, adder_3_out, Alu_B, bit_extender_1_out, ex_mem_1_alub_2,
       ex_mem_1_ir_2, ex_mem_1_result_2, EX_PC, id_ex_1_p35, id_ex_1_p37, id_ex_1_p39, id_ex_1_p40, ID_PC,
       IF_PC, IR, LedData, MEM_PC, mem_wb_1_memdata_2, mem_wb_1_result_2, mips_alu_1_result, mips_ram_1_p6,
       mips_regifile_1_r1, mips_regifile_1_r2, multiplexer_1_out, multiplexer_2_out, multiplexer_3_out,
       rom_1_data, shifter_1_out, WB_PC;

  Button \u_总复位  (.out(RST));
  Button _1 (.out(IR1));
  Button _2 (.out(IR2));
  Button _3 (.out(IR3));
  Button \u_继续运行  (.out(Go));
  LED led_1 (.in(W1));
  LED led_2 (.in(W2));
  LED led_3 (.in(W3));
  not not_1 (not_1_out, Ena);
  Multiplexer #(.width(32), .enable("false")) multiplexer_1 (
    .in0(adder_1_out), .in1(adder_3_out), .out(multiplexer_1_out), .sel(or_1_out));
  Hex_Digit_Display hex_digit_display_1 (.value(LedData[31:28]));  // open: dp
  Register #(.width(32)) PC (.D(multiplexer_1_out), .en(not_1_out), .Q(IF_PC), .clk(CLK));  // open: clr
  Hex_Digit_Display hex_digit_display_2 (.value(LedData[27:24]));  // open: dp
  Hex_Digit_Display hex_digit_display_3 (.value(LedData[23:20]));  // open: dp
  Hex_Digit_Display hex_digit_display_4 (.value(LedData[15:12]));  // open: dp
  Hex_Digit_Display hex_digit_display_5 (.value(LedData[19:16]));  // open: dp
  Counter #(.width(16), .max('hffff)) counter_1 (
    .D(\总周期数 ), .count(not_1_out), .Q(\总周期数 ), .clk(CLK), .clr(RST));  // open: load, carry
  Adder #(.width(32)) adder_1 (.a(32'h4), .b(IF_PC), .out(adder_1_out));  // open: cin, cout
  ROM #(.addrWidth(10), .dataWidth(32)) rom_1 (.addr(IF_PC[11:2]), .data(rom_1_data));  // open: sel
  Hex_Digit_Display hex_digit_display_6 (.value(LedData[7:4]));  // open: dp
  Hex_Digit_Display hex_digit_display_7 (.value(LedData[11:8]));  // open: dp
  Clock clock_1 (.out(CLK));
  IF_ID if_id_1 (
    .clk(CLK), .\使能端_低电平有效_stall_高电平有效 (Ena), .\同步清零_气泡_高电平有效 (RST), .IR(rom_1_data), .ir_2(IR), .PC(IF_PC),
    .pc_2(ID_PC));  // open: 传输状态Out_表明当前传输数据有效, 传输状态In_表明当前传输数据有效, IF_matchnum, IF_match, IF_matchnum_2, IF_match_2
  Hex_Digit_Display hex_digit_display_8 (.value(LedData[3:0]));  // open: dp
  // Probe on \总周期数 
  // Probe on \无条件分支数 
  // Probe on \条件分支成功数 
  // Probe on \插入气泡数 
  // Probe on \LoadUse次数 
  \硬布线控制器  \u_硬布线控制器_1  (
    .Func(IR[5:0]), .OP(IR[31:26]), .ALU_OP(aluop), .MemToReg(MemToReg), .MemWrite(Memwrite),
    .ALU_SRC(alusrc), .RegWrite(regwrite), .SysCALL(syscall), .SignedExt(signedext), .RegDst(redgdst),
    .Beq(beq), .JAL(jal), .Bne(bne));  // open: JR, JMP
  // Probe on IF_PC[11:0]
  MIPS_Regifile mips_regifile_1 (
    .Din(multiplexer_3_out), .Clk(CLK), .R1(mips_regifile_1_r1), .R2(mips_regifile_1_r2),
    .WE(mem_wb_1_regwrite_2), .W_num(multiplexer_4_out), .R1_num(IR[25:21]), .R2_num(IR[20:16]));
  Adder #(.width(32)) adder_2 (.a(ID_PC), .b(32'h4), .out(adder_2_out));  // open: cin, cout
  // Probe on ID_PC[11:0]
  assign bit_extender_1_out = {{16{IR[15]}}, IR[15:0]};  // Bit_Extender bit_extender_1
  // Probe on EX_PC[11:0]
  // Probe on MEM_PC[11:0]
  // Probe on WB_PC[11:0]
  // ID_EX id_ex_1: pin names not known; wires that end beside it: MemToReg, syscall, Memwrite, alusrc, redgdst, regwrite, signedext, bne, beq, aluop, IR[20:16], IR[15:11], IR[10:6], mips_regifile_1_r1, mips_regifile_1_r2, bit_extender_1_out, ID_PC, IR, adder_2_out, Ena, CLK, RST, id_ex_1_p23, id_ex_1_p24, id_ex_1_p25, id_ex_1_p26, id_ex_1_p27, id_ex_1_p28, id_ex_1_p29, id_ex_1_p30, id_ex_1_p31, id_ex_1_p32, id_ex_1_p33, shamt, id_ex_1_p35, Alu_B, id_ex_1_p37, EX_PC, id_ex_1_p39, id_ex_1_p40
  Multiplexer #(.width(32), .enable("false")) multiplexer_2 (
    .in0(Alu_B), .in1(id_ex_1_p37), .out(multiplexer_2_out), .sel(id_ex_1_p26));
  Shifter #(.width(32)) shifter_1 (.in(id_ex_1_p37), .\dist (5'b00010), .out(shifter_1_out));
  not not_2 (not_2_out, mips_alu_1_equal);
  MIPS_ALU mips_alu_1 (
    .X(id_ex_1_p35), .Y(multiplexer_2_out), .AluOP(id_ex_1_p31), .Equal(mips_alu_1_equal),
    .Result(mips_alu_1_result), .shamt(shamt));  // open: Result_2
  Adder #(.width(32)) adder_3 (.a(shifter_1_out), .b(id_ex_1_p40), .out(adder_3_out));  // open: cin, cout
  and and_1 (and_1_out, not_2_out, id_ex_1_p29);
  or or_1 (or_1_out, and_1_out, and_2_out);
  and and_2 (and_2_out, id_ex_1_p30, mips_alu_1_equal);
  EX_MEM ex_mem_1 (
    .Memtoreg(id_ex_1_p23), .Syscall(id_ex_1_p24), .Memwrite(id_ex_1_p25), .Regdst(id_ex_1_p27),
    .Regwrite(id_ex_1_p28), .clk(CLK), .\使能端_低电平有效_stall_高电平有效 (Ena), .\同步清零_气泡_高电平有效 (RST),
    .result(mips_alu_1_result), .IR(id_ex_1_p39), .PC(EX_PC), .ALUB(Alu_B), .memtoreg_2(ex_mem_1_memtoreg_2),
    .syscall_2(ex_mem_1_syscall_2), .memwrite_2(ex_mem_1_memwrite_2), .regdst_2(ex_mem_1_regdst_2),
    .regwrite_2(ex_mem_1_regwrite_2), .result_2(ex_mem_1_result_2), .ir_2(ex_mem_1_ir_2), .PC_2(MEM_PC),
    .ALUB_2(ex_mem_1_alub_2), .rt(id_ex_1_p32), .rd(id_ex_1_p33), .rt_2(ex_mem_1_rt_2), .rd_2(ex_mem_1_rd_2));  // open: Srlv, Jr, equal, Jmp, Lh, Jal, 传输状态In_表明当前传输数据有效, srlv_2, jr_2, equal_2, jmp_2, lh_2, jal_2, 传输状态Out_表明当前传输数据有效
  // MIPS_RAM mips_ram_1: pin names not known; wires that end beside it: ex_mem_1_result_2[21:2], ex_mem_1_alub_2, ex_mem_1_memwrite_2, CLK, RST, mips_ram_1_p6
  MEM_WB mem_wb_1 (
    .Memtoreg(ex_mem_1_memtoreg_2), .Syscall(ex_mem_1_syscall_2), .Regdst(ex_mem_1_regdst_2),
    .Regwrite(ex_mem_1_regwrite_2), .clk(CLK), .\使能端_低电平有效_stall_高电平有效 (Ena), .\同步清零_气泡_高电平有效 (RST),
    .result(ex_mem_1_result_2), .IR(ex_mem_1_ir_2), .PC(MEM_PC), .memdata(mips_ram_1_p6),
    .memtoreg_2(mem_wb_1_memtoreg_2), .syscall_2(Ena), .regdst_2(mem_wb_1_regdst_2),
    .regwrite_2(mem_wb_1_regwrite_2), .result_2(mem_wb_1_result_2), .PC_2(WB_PC),
    .memdata_2(mem_wb_1_memdata_2), .rt(ex_mem_1_rt_2), .rd(ex_mem_1_rd_2), .rt_2(mem_wb_1_rt_2),
    .rd_2(mem_wb_1_rd_2));  // open: Srlv, Jr, equal, Jmp, Lh, Jal, srlv_2, jr_2, equal_2, jmp_2, lh_2, jal_2, ir_2, 传输状态Out_表明当前传输数据有效, 传输状态In_表明当前传输数据有效
  Multiplexer #(.width(32), .enable("false")) multiplexer_3 (
    .in0(mem_wb_1_result_2), .in1(mem_wb_1_memdata_2), .out(multiplexer_3_out), .sel(mem_wb_1_memtoreg_2));
  Multiplexer #(.width(5), .enable("false")) multiplexer_4 (
    .in0(mem_wb_1_rt_2), .in1(mem_wb_1_rd_2), .out(multiplexer_4_out), .sel(mem_wb_1_regdst_2));

  // Other names for the same wires on the sheet: rd[4:0] = IR[15:11]; rt[4:0] = IR[20:16]

  // Notes on the sheet:
  //   中断源
  //   中断等待指示
  //   数码管输出
  //   contents of rom_1 (hex, n*v repeats v):
  //   20100000 20110001 20120002 20130003 36100000 36310001 36520002 36730003 ae100000 ae110004 ae120008
  //   ae13000c 2002000a 0 0 0 c
  //   指令字
  //   OP
  //   Func
  //   rs
  //   rt
  //   rd
  //   shamt
  //   imm
  //   PC+4
  //   流水调试日志用
endmodule

// 源寄存器使用情况
module \源寄存器使用情况  (
  input  OP0,
  input  OP1,
  input  OP2,
  input  OP3,
  input  OP4,
  input  OP5,
  input  F0,
  input  F1,
  input  F2,
  input  F3,
  input  F4,
  input  F5,
  output R1_Used,
  output R2_Used
);

  wire and_1_out, and_2_out, and_3_out, and_4_out, and_5_out, and_6_out, and_7_out, and_8_out, and_9_out,
       and_10_out, and_11_out, and_12_out, and_13_out, and_14_out, and_15_out, and_16_out, and_17_out,
       and_18_out, and_19_out, and_20_out, and_21_out, and_22_out, and_23_out, and_24_out, and_25_out,
       and_26_out, and_27_out, and_28_out, and_29_out, and_30_out, and_31_out, and_32_out, and_33_out,
       and_34_out, and_35_out, and_36_out, and_37_out, and_38_out, and_39_out, and_40_out, and_41_out,
       and_42_out, not_1_out, not_2_out, not_3_out, not_4_out, not_5_out, not_6_out, not_7_out, not_8_out,
       not_9_out, not_10_out, not_11_out, not_12_out, not_13_out, not_14_out, not_15_out, not_16_out,
       not_17_out, not_18_out, not_19_out, not_20_out, not_21_out, not_22_out, not_23_out, not_24_out,
       not_25_out, not_26_out, not_27_out, not_28_out, not_29_out, not_30_out, not_31_out, not_32_out,
       not_33_out, not_34_out, not_35_out, not_36_out, not_37_out, not_38_out, not_39_out, not_40_out,
       not_41_out, not_42_out, not_43_out, not_44_out, not_45_out, not_46_out, not_47_out, not_48_out,
       not_49_out, not_50_out, not_51_out, not_52_out, not_53_out, not_54_out, not_55_out, not_56_out,
       not_57_out, not_58_out, not_59_out, not_60_out, not_61_out, not_62_out, not_63_out, not_64_out,
       not_65_out, not_66_out, not_67_out, not_68_out, not_69_out, not_70_out, not_71_out, not_72_out,
       not_73_out, not_74_out, not_75_out, not_76_out, not_77_out, not_78_out, not_79_out, not_80_out,
       not_81_out, not_82_out, not_83_out, not_84_out, not_85_out, not_86_out, not_87_out, not_88_out,
       not_89_out, not_90_out, not_91_out, not_92_out, not_93_out, not_94_out, not_95_out, not_96_out,
       not_97_out, not_98_out, not_99_out, not_100_out, not_101_out, not_102_out, not_103_out, not_104_out,
       not_105_out, not_106_out, not_107_out, not_108_out, not_109_out, not_110_out, not_111_out,
       not_112_out, not_113_out, not_114_out, not_115_out, not_116_out, not_117_out, not_118_out,
       not_119_out, not_120_out, not_121_out, not_122_out, not_123_out, not_124_out, not_125_out,
       not_126_out, not_127_out, not_128_out, not_129_out, not_130_out, not_131_out, not_132_out,
       not_133_out, not_134_out, not_135_out, not_136_out, not_137_out, not_138_out, not_139_out,
       not_140_out, not_141_out, not_142_out, not_143_out, not_144_out, not_145_out, not_146_out,
       not_147_out, not_148_out, not_149_out, not_150_out, not_151_out, not_152_out, not_153_out,
       not_154_out, not_155_out, not_156_out, not_157_out, not_158_out, not_159_out, not_160_out,
       not_161_out, not_162_out, not_163_out, not_164_out, not_165_out, not_166_out, not_167_out,
       not_168_out, not_169_out, not_170_out, not_171_out, not_172_out, not_173_out, not_174_out,
       not_175_out, not_176_out, not_177_out, not_178_out, not_179_out, not_180_out, not_181_out,
       not_182_out, not_183_out, not_184_out, not_185_out, not_186_out, not_187_out, not_188_out,
       not_189_out, not_190_out, not_191_out, not_192_out, not_193_out, not_194_out, not_195_out,
       not_196_out, not_197_out, not_198_out, not_199_out, not_200_out, not_201_out, not_202_out,
       not_203_out, not_204_out, not_205_out, not_206_out, not_207_out, not_208_out, not_209_out,
       not_210_out, not_211_out, not_212_out, not_213_out, not_214_out, not_215_out, not_216_out,
       not_217_out, not_218_out, not_219_out, not_220_out, not_221_out, not_222_out, not_223_out,
       not_224_out, not_225_out, not_226_out, not_227_out, not_228_out, not_229_out, not_230_out,
       not_231_out, not_232_out, not_233_out, not_234_out, not_235_out, not_236_out, not_237_out,
       not_238_out, not_239_out, not_240_out, not_241_out, not_242_out, not_243_out, not_244_out,
       not_245_out, not_246_out, not_247_out, not_248_out, not_249_out, not_250_out, not_251_out,
       not_252_out, not_253_out, not_254_out, not_255_out, not_256_out, not_257_out, not_258_out,
       not_259_out, not_260_out, not_261_out, not_262_out, not_263_out, not_264_out, not_265_out,
       not_266_out, not_267_out, not_268_out, not_269_out, not_270_out, not_271_out, not_272_out,
       not_273_out, not_274_out, not_275_out, not_276_out, not_277_out, not_278_out, not_279_out,
       not_280_out, not_281_out, not_282_out, not_283_out, not_284_out, not_285_out, not_286_out,
       not_287_out, not_288_out, not_289_out, not_290_out, not_291_out, not_292_out, not_293_out,
       not_294_out, not_295_out, not_296_out, not_297_out, not_298_out, not_299_out, not_300_out,
       not_301_out, not_302_out, not_303_out, not_304_out, not_305_out, not_306_out, not_307_out,
       not_308_out, not_309_out, not_310_out, not_311_out;

  not not_1 (not_1_out, OP5);
  not not_2 (not_2_out, OP4);
  not not_3 (not_3_out, OP3);
  not not_4 (not_4_out, OP2);
  not not_5 (not_5_out, OP1);
  not not_6 (not_6_out, OP0);
  not not_7 (not_7_out, F4);
  not not_8 (not_8_out, F3);
  not not_9 (not_9_out, F2);
  not not_10 (not_10_out, F1);
  not not_11 (not_11_out, F0);
  not not_12 (not_12_out, OP5);
  not not_13 (not_13_out, OP4);
  not not_14 (not_14_out, OP3);
  not not_15 (not_15_out, OP2);
  not not_16 (not_16_out, OP1);
  not not_17 (not_17_out, OP0);
  not not_18 (not_18_out, F4);
  not not_19 (not_19_out, F3);
  not not_20 (not_20_out, F2);
  not not_21 (not_21_out, F1);
  not not_22 (not_22_out, OP5);
  not not_23 (not_23_out, OP4);
  not not_24 (not_24_out, OP3);
  not not_25 (not_25_out, OP2);
  not not_26 (not_26_out, OP1);
  not not_27 (not_27_out, OP0);
  not not_28 (not_28_out, F4);
  not not_29 (not_29_out, F3);
  not not_30 (not_30_out, F2);
  not not_31 (not_31_out, F0);
  not not_32 (not_32_out, OP5);
  not not_33 (not_33_out, OP4);
  not not_34 (not_34_out, OP3);
  not not_35 (not_35_out, OP2);
  not not_36 (not_36_out, OP1);
  not not_37 (not_37_out, OP0);
  not not_38 (not_38_out, F4);
  not not_39 (not_39_out, F3);
  not not_40 (not_40_out, F1);
  not not_41 (not_41_out, F0);
  not not_42 (not_42_out, OP5);
  not not_43 (not_43_out, OP4);
  not not_44 (not_44_out, OP3);
  not not_45 (not_45_out, OP2);
  not not_46 (not_46_out, OP1);
  not not_47 (not_47_out, OP0);
  not not_48 (not_48_out, F4);
  not not_49 (not_49_out, F3);
  not not_50 (not_50_out, F1);
  not not_51 (not_51_out, OP5);
  not not_52 (not_52_out, OP4);
  not not_53 (not_53_out, OP3);
  not not_54 (not_54_out, OP2);
  not not_55 (not_55_out, OP1);
  not not_56 (not_56_out, OP0);
  not not_57 (not_57_out, F4);
  not not_58 (not_58_out, F3);
  not not_59 (not_59_out, OP5);
  not not_60 (not_60_out, OP4);
  not not_61 (not_61_out, OP3);
  not not_62 (not_62_out, OP2);
  not not_63 (not_63_out, OP1);
  not not_64 (not_64_out, OP0);
  not not_65 (not_65_out, F4);
  not not_66 (not_66_out, F2);
  not not_67 (not_67_out, F0);
  not not_68 (not_68_out, OP5);
  not not_69 (not_69_out, OP4);
  not not_70 (not_70_out, OP3);
  not not_71 (not_71_out, OP2);
  not not_72 (not_72_out, OP1);
  not not_73 (not_73_out, OP0);
  not not_74 (not_74_out, F4);
  not not_75 (not_75_out, F2);
  not not_76 (not_76_out, OP5);
  not not_77 (not_77_out, OP4);
  not not_78 (not_78_out, OP3);
  not not_79 (not_79_out, OP2);
  not not_80 (not_80_out, OP1);
  not not_81 (not_81_out, OP0);
  not not_82 (not_82_out, F5);
  not not_83 (not_83_out, F4);
  not not_84 (not_84_out, F2);
  not not_85 (not_85_out, F1);
  not not_86 (not_86_out, F0);
  not not_87 (not_87_out, OP5);
  not not_88 (not_88_out, OP4);
  not not_89 (not_89_out, OP3);
  not not_90 (not_90_out, OP2);
  not not_91 (not_91_out, OP1);
  not not_92 (not_92_out, OP0);
  not not_93 (not_93_out, F5);
  not not_94 (not_94_out, F4);
  not not_95 (not_95_out, F1);
  not not_96 (not_96_out, F0);
  not not_97 (not_97_out, OP5);
  not not_98 (not_98_out, OP4);
  not not_99 (not_99_out, OP3);
  not not_100 (not_100_out, OP1);
  not not_101 (not_101_out, OP0);
  not not_102 (not_102_out, OP5);
  not not_103 (not_103_out, OP4);
  not not_104 (not_104_out, OP3);
  not not_105 (not_105_out, OP1);
  not not_106 (not_106_out, OP5);
  not not_107 (not_107_out, OP4);
  not not_108 (not_108_out, OP2);
  not not_109 (not_109_out, OP1);
  not not_110 (not_110_out, OP0);
  not not_111 (not_111_out, OP5);
  not not_112 (not_112_out, OP4);
  not not_113 (not_113_out, OP1);
  not not_114 (not_114_out, OP0);
  not not_115 (not_115_out, OP5);
  not not_116 (not_116_out, OP4);
  not not_117 (not_117_out, OP2);
  not not_118 (not_118_out, OP1);
  not not_119 (not_119_out, OP5);
  not not_120 (not_120_out, OP4);
  not not_121 (not_121_out, OP2);
  not not_122 (not_122_out, OP0);
  not not_123 (not_123_out, OP5);
  not not_124 (not_124_out, OP4);
  not not_125 (not_125_out, OP1);
  not not_126 (not_126_out, OP4);
  not not_127 (not_127_out, OP3);
  not not_128 (not_128_out, OP2);
  not not_129 (not_129_out, OP4);
  not not_130 (not_130_out, OP2);
  not not_131 (not_131_out, OP5);
  not not_132 (not_132_out, OP4);
  not not_133 (not_133_out, OP3);
  not not_134 (not_134_out, OP2);
  not not_135 (not_135_out, OP1);
  not not_136 (not_136_out, OP0);
  not not_137 (not_137_out, F5);
  not not_138 (not_138_out, F4);
  not not_139 (not_139_out, F3);
  not not_140 (not_140_out, OP5);
  not not_141 (not_141_out, OP4);
  not not_142 (not_142_out, OP3);
  not not_143 (not_143_out, OP2);
  not not_144 (not_144_out, OP1);
  not not_145 (not_145_out, OP0);
  not not_146 (not_146_out, F5);
  not not_147 (not_147_out, F4);
  not not_148 (not_148_out, F3);
  not not_149 (not_149_out, F0);
  not not_150 (not_150_out, OP4);
  not not_151 (not_151_out, OP3);
  not not_152 (not_152_out, OP2);
  not not_153 (not_153_out, OP1);
  not not_154 (not_154_out, OP5);
  not not_155 (not_155_out, OP4);
  not not_156 (not_156_out, OP3);
  not not_157 (not_157_out, OP0);
  not not_158 (not_158_out, OP5);
  not not_159 (not_159_out, OP4);
  not not_160 (not_160_out, OP3);
  not not_161 (not_161_out, OP2);
  not not_162 (not_162_out, OP1);
  not not_163 (not_163_out, OP0);
  not not_164 (not_164_out, F5);
  not not_165 (not_165_out, F4);
  not not_166 (not_166_out, F3);
  not not_167 (not_167_out, F2);
  not not_168 (not_168_out, F1);
  not not_169 (not_169_out, F0);
  not not_170 (not_170_out, OP5);
  not not_171 (not_171_out, OP4);
  not not_172 (not_172_out, OP3);
  not not_173 (not_173_out, OP2);
  not not_174 (not_174_out, OP1);
  not not_175 (not_175_out, OP0);
  not not_176 (not_176_out, F5);
  not not_177 (not_177_out, F4);
  not not_178 (not_178_out, F3);
  not not_179 (not_179_out, F2);
  not not_180 (not_180_out, OP5);
  not not_181 (not_181_out, OP4);
  not not_182 (not_182_out, OP3);
  not not_183 (not_183_out, OP2);
  not not_184 (not_184_out, OP1);
  not not_185 (not_185_out, OP0);
  not not_186 (not_186_out, F5);
  not not_187 (not_187_out, F4);
  not not_188 (not_188_out, F3);
  not not_189 (not_189_out, F2);
  not not_190 (not_190_out, F0);
  not not_191 (not_191_out, OP5);
  not not_192 (not_192_out, OP4);
  not not_193 (not_193_out, OP3);
  not not_194 (not_194_out, OP2);
  not not_195 (not_195_out, OP1);
  not not_196 (not_196_out, OP0);
  not not_197 (not_197_out, F4);
  not not_198 (not_198_out, F3);
  not not_199 (not_199_out, F2);
  not not_200 (not_200_out, F1);
  not not_201 (not_201_out, F0);
  not not_202 (not_202_out, OP5);
  not not_203 (not_203_out, OP4);
  not not_204 (not_204_out, OP3);
  not not_205 (not_205_out, OP2);
  not not_206 (not_206_out, OP1);
  not not_207 (not_207_out, OP0);
  not not_208 (not_208_out, F4);
  not not_209 (not_209_out, F3);
  not not_210 (not_210_out, F2);
  not not_211 (not_211_out, F1);
  not not_212 (not_212_out, OP5);
  not not_213 (not_213_out, OP4);
  not not_214 (not_214_out, OP3);
  not not_215 (not_215_out, OP2);
  not not_216 (not_216_out, OP1);
  not not_217 (not_217_out, OP0);
  not not_218 (not_218_out, F4);
  not not_219 (not_219_out, F3);
  not not_220 (not_220_out, F2);
  not not_221 (not_221_out, F0);
  not not_222 (not_222_out, OP5);
  not not_223 (not_223_out, OP4);
  not not_224 (not_224_out, OP3);
  not not_225 (not_225_out, OP2);
  not not_226 (not_226_out, OP1);
  not not_227 (not_227_out, OP0);
  not not_228 (not_228_out, F4);
  not not_229 (not_229_out, F3);
  not not_230 (not_230_out, F1);
  not not_231 (not_231_out, F0);
  not not_232 (not_232_out, OP5);
  not not_233 (not_233_out, OP4);
  not not_234 (not_234_out, OP3);
  not not_235 (not_235_out, OP2);
  not not_236 (not_236_out, OP1);
  not not_237 (not_237_out, OP0);
  not not_238 (not_238_out, F4);
  not not_239 (not_239_out, F3);
  not not_240 (not_240_out, F1);
  not not_241 (not_241_out, OP5);
  not not_242 (not_242_out, OP4);
  not not_243 (not_243_out, OP3);
  not not_244 (not_244_out, OP2);
  not not_245 (not_245_out, OP1);
  not not_246 (not_246_out, OP0);
  not not_247 (not_247_out, F4);
  not not_248 (not_248_out, F3);
  not not_249 (not_249_out, OP5);
  not not_250 (not_250_out, OP4);
  not not_251 (not_251_out, OP3);
  not not_252 (not_252_out, OP2);
  not not_253 (not_253_out, OP1);
  not not_254 (not_254_out, OP0);
  not not_255 (not_255_out, F4);
  not not_256 (not_256_out, F2);
  not not_257 (not_257_out, F0);
  not not_258 (not_258_out, OP5);
  not not_259 (not_259_out, OP4);
  not not_260 (not_260_out, OP3);
  not not_261 (not_261_out, OP2);
  not not_262 (not_262_out, OP1);
  not not_263 (not_263_out, OP0);
  not not_264 (not_264_out, F4);
  not not_265 (not_265_out, F2);
  not not_266 (not_266_out, OP5);
  not not_267 (not_267_out, OP4);
  not not_268 (not_268_out, OP3);
  not not_269 (not_269_out, OP2);
  not not_270 (not_270_out, OP1);
  not not_271 (not_271_out, OP0);
  not not_272 (not_272_out, F5);
  not not_273 (not_273_out, F4);
  not not_274 (not_274_out, F1);
  not not_275 (not_275_out, F0);
  not not_276 (not_276_out, OP5);
  not not_277 (not_277_out, OP4);
  not not_278 (not_278_out, OP3);
  not not_279 (not_279_out, OP1);
  not not_280 (not_280_out, OP0);
  not not_281 (not_281_out, OP5);
  not not_282 (not_282_out, OP4);
  not not_283 (not_283_out, OP3);
  not not_284 (not_284_out, OP1);
  not not_285 (not_285_out, OP5);
  not not_286 (not_286_out, OP4);
  not not_287 (not_287_out, OP3);
  not not_288 (not_288_out, OP2);
  not not_289 (not_289_out, OP1);
  not not_290 (not_290_out, OP0);
  not not_291 (not_291_out, F5);
  not not_292 (not_292_out, F4);
  not not_293 (not_293_out, F3);
  not not_294 (not_294_out, OP5);
  not not_295 (not_295_out, OP4);
  not not_296 (not_296_out, OP3);
  not not_297 (not_297_out, OP2);
  not not_298 (not_298_out, OP1);
  not not_299 (not_299_out, OP0);
  not not_300 (not_300_out, F5);
  not not_301 (not_301_out, F4);
  not not_302 (not_302_out, F3);
  not not_303 (not_303_out, F0);
  not not_304 (not_304_out, OP5);
  not not_305 (not_305_out, OP4);
  not not_306 (not_306_out, OP3);
  not not_307 (not_307_out, OP0);
  not not_308 (not_308_out, OP4);
  not not_309 (not_309_out, OP2);
  not not_310 (not_310_out, OP4);
  not not_311 (not_311_out, OP2);
  and and_1 (and_1_out, not_1_out, not_2_out, not_3_out, not_4_out, not_5_out, not_6_out, F5, not_7_out, not_8_out, not_9_out, not_10_out, not_11_out);
  and and_2 (and_2_out, not_12_out, not_13_out, not_14_out, not_15_out, not_16_out, not_17_out, F5, not_18_out, not_19_out, not_20_out, not_21_out, F0);
  and and_3 (and_3_out, not_22_out, not_23_out, not_24_out, not_25_out, not_26_out, not_27_out, F5, not_28_out, not_29_out, not_30_out, F1, not_31_out);
  and and_4 (and_4_out, not_32_out, not_33_out, not_34_out, not_35_out, not_36_out, not_37_out, F5, not_38_out, not_39_out, F2, not_40_out, not_41_out);
  and and_5 (and_5_out, not_42_out, not_43_out, not_44_out, not_45_out, not_46_out, not_47_out, F5, not_48_out, not_49_out, F2, not_50_out, F0);
  and and_6 (and_6_out, not_51_out, not_52_out, not_53_out, not_54_out, not_55_out, not_56_out, F5, not_57_out, not_58_out, F2, F1, F0);
  and and_7 (and_7_out, not_59_out, not_60_out, not_61_out, not_62_out, not_63_out, not_64_out, F5, not_65_out, F3, not_66_out, F1, not_67_out);
  and and_8 (and_8_out, not_68_out, not_69_out, not_70_out, not_71_out, not_72_out, not_73_out, F5, not_74_out, F3, not_75_out, F1, F0);
  and and_9 (and_9_out, not_76_out, not_77_out, not_78_out, not_79_out, not_80_out, not_81_out, not_82_out, not_83_out, F3, not_84_out, not_85_out, not_86_out);
  and and_10 (and_10_out, not_87_out, not_88_out, not_89_out, not_90_out, not_91_out, not_92_out, not_93_out, not_94_out, F3, F2, not_95_out, not_96_out);
  and and_11 (and_11_out, not_97_out, not_98_out, not_99_out, OP2, not_100_out, not_101_out);
  and and_12 (and_12_out, not_102_out, not_103_out, not_104_out, OP2, not_105_out, OP0);
  and and_13 (and_13_out, not_106_out, not_107_out, OP3, not_108_out, not_109_out, not_110_out);
  and and_14 (and_14_out, not_111_out, not_112_out, OP3, OP2, not_113_out, not_114_out);
  and and_15 (and_15_out, not_115_out, not_116_out, OP3, not_117_out, not_118_out, OP0);
  and and_16 (and_16_out, not_119_out, not_120_out, OP3, not_121_out, OP1, not_122_out);
  and and_17 (and_17_out, not_123_out, not_124_out, OP3, OP2, not_125_out, OP0);
  and and_18 (and_18_out, OP5, not_126_out, not_127_out, not_128_out, OP1, OP0);
  and and_19 (and_19_out, OP5, not_129_out, OP3, not_130_out, OP1, OP0);
  and and_20 (and_20_out, not_131_out, not_132_out, not_133_out, not_134_out, not_135_out, not_136_out, not_137_out, not_138_out, not_139_out, F2, F1, F0);
  and and_21 (and_21_out, not_140_out, not_141_out, not_142_out, not_143_out, not_144_out, not_145_out, not_146_out, not_147_out, not_148_out, F2, F1, not_149_out);
  and and_22 (and_22_out, OP5, not_150_out, not_151_out, not_152_out, not_153_out, OP0);
  and and_23 (and_23_out, not_154_out, not_155_out, not_156_out, OP2, OP1, not_157_out);
  and and_24 (and_24_out, not_158_out, not_159_out, not_160_out, not_161_out, not_162_out, not_163_out, not_164_out, not_165_out, not_166_out, not_167_out, not_168_out, not_169_out);
  and and_25 (and_25_out, not_170_out, not_171_out, not_172_out, not_173_out, not_174_out, not_175_out, not_176_out, not_177_out, not_178_out, not_179_out, F1, F0);
  and and_26 (and_26_out, not_180_out, not_181_out, not_182_out, not_183_out, not_184_out, not_185_out, not_186_out, not_187_out, not_188_out, not_189_out, F1, not_190_out);
  and and_27 (and_27_out, not_191_out, not_192_out, not_193_out, not_194_out, not_195_out, not_196_out, F5, not_197_out, not_198_out, not_199_out, not_200_out, not_201_out);
  and and_28 (and_28_out, not_202_out, not_203_out, not_204_out, not_205_out, not_206_out, not_207_out, F5, not_208_out, not_209_out, not_210_out, not_211_out, F0);
  and and_29 (and_29_out, not_212_out, not_213_out, not_214_out, not_215_out, not_216_out, not_217_out, F5, not_218_out, not_219_out, not_220_out, F1, not_221_out);
  and and_30 (and_30_out, not_222_out, not_223_out, not_224_out, not_225_out, not_226_out, not_227_out, F5, not_228_out, not_229_out, F2, not_230_out, not_231_out);
  and and_31 (and_31_out, not_232_out, not_233_out, not_234_out, not_235_out, not_236_out, not_237_out, F5, not_238_out, not_239_out, F2, not_240_out, F0);
  and and_32 (and_32_out, not_241_out, not_242_out, not_243_out, not_244_out, not_245_out, not_246_out, F5, not_247_out, not_248_out, F2, F1, F0);
  and and_33 (and_33_out, not_249_out, not_250_out, not_251_out, not_252_out, not_253_out, not_254_out, F5, not_255_out, F3, not_256_out, F1, not_257_out);
  and and_34 (and_34_out, not_258_out, not_259_out, not_260_out, not_261_out, not_262_out, not_263_out, F5, not_264_out, F3, not_265_out, F1, F0);
  and and_35 (and_35_out, not_266_out, not_267_out, not_268_out, not_269_out, not_270_out, not_271_out, not_272_out, not_273_out, F3, F2, not_274_out, not_275_out);
  and and_36 (and_36_out, not_276_out, not_277_out, not_278_out, OP2, not_279_out, not_280_out);
  and and_37 (and_37_out, not_281_out, not_282_out, not_283_out, OP2, not_284_out, OP0);
  and and_38 (and_38_out, not_285_out, not_286_out, not_287_out, not_288_out, not_289_out, not_290_out, not_291_out, not_292_out, not_293_out, F2, F1, F0);
  and and_39 (and_39_out, not_294_out, not_295_out, not_296_out, not_297_out, not_298_out, not_299_out, not_300_out, not_301_out, not_302_out, F2, F1, not_303_out);
  and and_40 (and_40_out, not_304_out, not_305_out, not_306_out, OP2, OP1, not_307_out);
  and and_41 (and_41_out, OP5, not_308_out, OP3, not_309_out, OP1, OP0);
  and and_42 (and_42_out, OP5, not_310_out, OP3, not_311_out, OP1, OP0);
  or or_1 (R1_Used, and_1_out, and_2_out, and_3_out, and_4_out, and_5_out, and_6_out, and_7_out, and_8_out, and_9_out, and_10_out, and_11_out, and_12_out, and_13_out, and_14_out, and_15_out, and_16_out, and_17_out, and_18_out, and_19_out, and_20_out, and_21_out, and_22_out, and_23_out);
  or or_2 (R2_Used, and_24_out, and_25_out, and_26_out, and_27_out, and_28_out, and_29_out, and_30_out, and_31_out, and_32_out, and_33_out, and_34_out, and_35_out, and_36_out, and_37_out, and_38_out, and_39_out, and_40_out, and_41_out, and_42_out);
endmodule

module \数据相关检测  (
  input  [5:0] OP,
  input  [4:0] EX_WriteReg_num,
  input  EX_RegWrite,
  input  [4:0] MEM_WriteReg_num,
  input  MEM_RegWrite,
  input  [5:0] Func,
  input  [4:0] ID_R1_num,
  input  [4:0] ID_R2_num,
  output \数据相关 
);

  wire and_1_out, and_2_out, and_3_out, and_4_out, and_5_out, and_6_out, and_7_out, and_8_out,
       comparator_1_eq, comparator_2_eq, comparator_3_eq, comparator_4_eq, comparator_5_eq, comparator_6_eq,
       not_1_out, not_2_out, or_1_out, or_2_out, \源寄存器使用情况_1_r1_used , \源寄存器使用情况_1_r2_used ;

  \源寄存器使用情况  \u_源寄存器使用情况_1  (
    .OP0(OP[0]), .OP1(OP[1]), .OP2(OP[2]), .OP3(OP[3]), .OP4(OP[4]), .OP5(OP[5]), .F0(Func[0]), .F1(Func[1]),
    .F2(Func[2]), .F3(Func[3]), .F4(Func[4]), .F5(Func[5]), .R1_Used(\源寄存器使用情况_1_r1_used ),
    .R2_Used(\源寄存器使用情况_1_r2_used ));
  Comparator #(.width(5)) comparator_1 (.a(ID_R1_num), .b({5{1'b0}}), .eq(comparator_1_eq));  // open: gt, lt
  Comparator #(.width(5)) comparator_2 (.a(ID_R1_num), .b(EX_WriteReg_num), .eq(comparator_2_eq));  // open: gt, lt
  Comparator #(.width(5)) comparator_3 (.a(ID_R1_num), .b(MEM_WriteReg_num), .eq(comparator_3_eq));  // open: gt, lt
  Comparator #(.width(5)) comparator_4 (.a(ID_R2_num), .b(EX_WriteReg_num), .eq(comparator_4_eq));  // open: gt, lt
  Comparator #(.width(5)) comparator_5 (.a(ID_R2_num), .b(MEM_WriteReg_num), .eq(comparator_5_eq));  // open: gt, lt
  Comparator #(.width(5)) comparator_6 (.a(ID_R2_num), .b({5{1'b0}}), .eq(comparator_6_eq));  // open: gt, lt
  not not_1 (not_1_out, comparator_1_eq);
  and and_1 (and_1_out, comparator_2_eq, EX_RegWrite);
  and and_2 (and_2_out, comparator_3_eq, MEM_RegWrite);
  and and_3 (and_3_out, comparator_4_eq, EX_RegWrite);
  and and_4 (and_4_out, comparator_5_eq, MEM_RegWrite);
  not not_2 (not_2_out, comparator_6_eq);
  and and_5 (and_5_out, not_1_out, or_1_out);
  or or_1 (or_1_out, and_1_out, and_2_out);
  or or_2 (or_2_out, and_3_out, and_4_out);
  and and_6 (and_6_out, or_2_out, not_2_out);
  and and_7 (and_7_out, \源寄存器使用情况_1_r1_used , and_5_out);
  and and_8 (and_8_out, \源寄存器使用情况_1_r2_used , and_6_out);
  or or_3 (\数据相关 , and_7_out, and_8_out);

  // Other names for the same wires on the sheet: OP_CODE[5:0] = OP
endmodule

module IF_ID (
  input  clk,
  input  \使能端_低电平有效_stall_高电平有效 ,
  input  \同步清零_气泡_高电平有效 ,
  input  [31:0] IR,
  input  \传输状态In_表明当前传输数据有效 ,
  input  [31:0] PC,
  input  [1:0] IF_matchnum,
  input  IF_match,
  output [31:0] ir_2,
  output \传输状态Out_表明当前传输数据有效 ,
  output [31:0] pc_2,
  output [1:0] IF_matchnum_2,
  output IF_match_2
);

  wire multiplexer_1_out, multiplexer_5_out, not_1_out;
  wire [1:0] multiplexer_4_out;
  wire [31:0] multiplexer_2_out, multiplexer_3_out;

  not not_1 (not_1_out, \使能端_低电平有效_stall_高电平有效 );
  Multiplexer #(.enable("false")) multiplexer_1 (
    .in0(\传输状态In_表明当前传输数据有效 ), .in1(1'b0), .out(multiplexer_1_out), .sel(\同步清零_气泡_高电平有效 ));
  Register #(.width(1)) register_1 (
    .D(multiplexer_1_out), .en(not_1_out), .Q(\传输状态Out_表明当前传输数据有效 ), .clk(clk));  // open: clr
  Multiplexer #(.width(32), .enable("false")) multiplexer_2 (
    .in0(IR), .in1({32{1'b0}}), .out(multiplexer_2_out), .sel(\同步清零_气泡_高电平有效 ));
  Multiplexer #(.width(32), .enable("false")) multiplexer_3 (
    .in0(PC), .in1({32{1'b0}}), .out(multiplexer_3_out), .sel(\同步清零_气泡_高电平有效 ));
  Multiplexer #(.width(2), .enable("false")) multiplexer_4 (
    .in0(IF_matchnum), .in1(2'b00), .out(multiplexer_4_out), .sel(\同步清零_气泡_高电平有效 ));
  Register #(.width(32)) register_2 (.D(multiplexer_2_out), .en(not_1_out), .Q(ir_2), .clk(clk));  // open: clr
  Register #(.width(32)) register_3 (.D(multiplexer_3_out), .en(not_1_out), .Q(pc_2), .clk(clk));  // open: clr
  Register #(.width(2)) register_4 (.D(multiplexer_4_out), .en(not_1_out), .Q(IF_matchnum_2), .clk(clk));  // open: clr
  Multiplexer #(.enable("false")) multiplexer_5 (
    .in0(IF_match), .in1(1'b0), .out(multiplexer_5_out), .sel(\同步清零_气泡_高电平有效 ));
  Register #(.width(1)) register_5 (.D(multiplexer_5_out), .en(not_1_out), .Q(IF_match_2), .clk(clk));  // open: clr
endmodule
module ID_EX (
  input  Memtoreg,
  input  Syscall,
  input  Bne,
  input  Srlv,
  input  Memwrite,
  input  Jr,
  input  Srav,
  input  Alusrc,
  input  Regdst,
  input  Jmp,
  input  Lh,
  input  Regwrite,
  input  Beq,
  input  Jal,
  input  Blez,
  input  clk,
  input  \使能端_低电平有效_stall_高电平有效 ,
  input  \同步清零_气泡_高电平有效 ,
  input  [31:0] IMM,
  input  [31:0] PC_4,
  input  [31:0] Jimm,
  input  [31:0] IR,
  input  [31:0] PC,
  input  [3:0] Aluop,
  input  [4:0] rt,
  input  [4:0] rd,
  input  [4:0] shamt,
  input  [31:0] R1,
  input  [31:0] R2,
  input  [4:0] R1_num,
  input  [4:0] R2_num,
  input  [1:0] EX_matchnum,
  input  EX_match,
  output memtoreg_2,
  output syscall_2,
  output bne_2,
  output srlv_2,
  output memwrite_2,
  output jr_2,
  output srav_2,
  output alusrc_2,
  output regdst_2,
  output jmp_2,
  output lh_2,
  output regwrite_2,
  output beq_2,
  output jal_2,
  output blez_2,
  output [31:0] imm_2,
  output [31:0] PC_4_2,
  output [31:0] JIMM_2,
  output [31:0] ir_2,
  output [31:0] pc_2,
  output [3:0] aluop_2,
  output [4:0] rt_2,
  output [4:0] rd_2,
  output [4:0] shamt_2,
  output [31:0] r1_2,
  output [31:0] r2_2,
  output [4:0] R1_num_2,
  output [4:0] R2_num_2,
  output [1:0] EX_matchnum_2,
  output EX_match_2
);

  wire multiplexer_1_out, multiplexer_2_out, multiplexer_3_out, multiplexer_4_out, multiplexer_8_out,
       multiplexer_9_out, multiplexer_10_out, multiplexer_12_out, multiplexer_13_out, multiplexer_14_out,
       multiplexer_15_out, multiplexer_16_out, multiplexer_20_out, multiplexer_21_out, multiplexer_22_out,
       multiplexer_23_out, not_1_out;
  wire [1:0] multiplexer_7_out;
  wire [3:0] multiplexer_18_out;
  wire [4:0] multiplexer_24_out, multiplexer_26_out, multiplexer_27_out, multiplexer_28_out,
       multiplexer_30_out;
  wire [31:0] multiplexer_5_out, multiplexer_6_out, multiplexer_11_out, multiplexer_17_out,
       multiplexer_19_out, multiplexer_25_out, multiplexer_29_out;

  not not_1 (not_1_out, \使能端_低电平有效_stall_高电平有效 );
  Multiplexer #(.enable("false")) multiplexer_1 (
    .in0(Memtoreg), .in1(1'b0), .out(multiplexer_1_out), .sel(\同步清零_气泡_高电平有效 ));
  Multiplexer #(.enable("false")) multiplexer_2 (
    .in0(Memwrite), .in1(1'b0), .out(multiplexer_2_out), .sel(\同步清零_气泡_高电平有效 ));
  Multiplexer #(.enable("false")) multiplexer_3 (
    .in0(Alusrc), .in1(1'b0), .out(multiplexer_3_out), .sel(\同步清零_气泡_高电平有效 ));
  Multiplexer #(.enable("false")) multiplexer_4 (
    .in0(Regwrite), .in1(1'b0), .out(multiplexer_4_out), .sel(\同步清零_气泡_高电平有效 ));
  Register #(.width(1)) register_1 (.D(multiplexer_1_out), .en(not_1_out), .Q(memtoreg_2), .clk(clk));  // open: clr
  Register #(.width(1)) register_2 (.D(multiplexer_2_out), .en(not_1_out), .Q(memwrite_2), .clk(clk));  // open: clr
  Register #(.width(1)) register_3 (.D(multiplexer_3_out), .en(not_1_out), .Q(alusrc_2), .clk(clk));  // open: clr
  Register #(.width(1)) register_4 (.D(multiplexer_4_out), .en(not_1_out), .Q(regwrite_2), .clk(clk));  // open: clr
  Multiplexer #(.width(32), .enable("false")) multiplexer_5 (
    .in0(IR), .in1({32{1'b0}}), .out(multiplexer_5_out), .sel(\同步清零_气泡_高电平有效 ));
  Multiplexer #(.width(32), .enable("false")) multiplexer_6 (
    .in0(PC), .in1({32{1'b0}}), .out(multiplexer_6_out), .sel(\同步清零_气泡_高电平有效 ));
  Multiplexer #(.width(2), .enable("false")) multiplexer_7 (
    .in0(EX_matchnum), .in1(2'b00), .out(multiplexer_7_out), .sel(\同步清零_气泡_高电平有效 ));
  Multiplexer #(.enable("false")) multiplexer_8 (
    .in0(Syscall), .in1(1'b0), .out(multiplexer_8_out), .sel(\同步清零_气泡_高电平有效 ));
  Multiplexer #(.enable("false")) multiplexer_9 (
    .in0(Regdst), .in1(1'b0), .out(multiplexer_9_out), .sel(\同步清零_气泡_高电平有效 ));
  Multiplexer #(.enable("false")) multiplexer_10 (
    .in0(Beq), .in1(1'b0), .out(multiplexer_10_out), .sel(\同步清零_气泡_高电平有效 ));
  Register #(.width(32)) register_5 (.D(multiplexer_5_out), .en(not_1_out), .Q(ir_2), .clk(clk));  // open: clr
  Register #(.width(32)) register_6 (.D(multiplexer_6_out), .en(not_1_out), .Q(pc_2), .clk(clk));  // open: clr
  Multiplexer #(.width(32), .enable("false")) multiplexer_11 (
    .in0(R1), .in1({32{1'b0}}), .out(multiplexer_11_out), .sel(\同步清零_气泡_高电平有效 ));
  Register #(.width(2)) register_7 (.D(multiplexer_7_out), .en(not_1_out), .Q(EX_matchnum_2), .clk(clk));  // open: clr
  Register #(.width(32)) register_8 (.D(multiplexer_11_out), .en(not_1_out), .Q(r1_2), .clk(clk));  // open: clr
  Register #(.width(1)) register_9 (.D(multiplexer_8_out), .en(not_1_out), .Q(syscall_2), .clk(clk));  // open: clr
  Register #(.width(1)) register_10 (.D(multiplexer_9_out), .en(not_1_out), .Q(regdst_2), .clk(clk));  // open: clr
  Register #(.width(1)) register_11 (.D(multiplexer_10_out), .en(not_1_out), .Q(beq_2), .clk(clk));  // open: clr
  Multiplexer #(.enable("false")) multiplexer_12 (
    .in0(EX_match), .in1(1'b0), .out(multiplexer_12_out), .sel(\同步清零_气泡_高电平有效 ));
  Multiplexer #(.enable("false")) multiplexer_13 (
    .in0(Bne), .in1(1'b0), .out(multiplexer_13_out), .sel(\同步清零_气泡_高电平有效 ));
  Multiplexer #(.enable("false")) multiplexer_14 (
    .in0(Jr), .in1(1'b0), .out(multiplexer_14_out), .sel(\同步清零_气泡_高电平有效 ));
  Multiplexer #(.enable("false")) multiplexer_15 (
    .in0(Jmp), .in1(1'b0), .out(multiplexer_15_out), .sel(\同步清零_气泡_高电平有效 ));
  Multiplexer #(.enable("false")) multiplexer_16 (
    .in0(Jal), .in1(1'b0), .out(multiplexer_16_out), .sel(\同步清零_气泡_高电平有效 ));
  Multiplexer #(.width(32), .enable("false")) multiplexer_17 (
    .in0(IMM), .in1({32{1'b0}}), .out(multiplexer_17_out), .sel(\同步清零_气泡_高电平有效 ));
  Multiplexer #(.width(4), .enable("false")) multiplexer_18 (
    .in0(Aluop), .in1(4'b0000), .out(multiplexer_18_out), .sel(\同步清零_气泡_高电平有效 ));
  Register #(.width(1)) register_12 (.D(multiplexer_12_out), .en(not_1_out), .Q(EX_match_2), .clk(clk));  // open: clr
  Register #(.width(1)) register_13 (.D(multiplexer_13_out), .en(not_1_out), .Q(bne_2), .clk(clk));  // open: clr
  Register #(.width(1)) register_14 (.D(multiplexer_14_out), .en(not_1_out), .Q(jr_2), .clk(clk));  // open: clr
  Register #(.width(1)) register_15 (.D(multiplexer_15_out), .en(not_1_out), .Q(jmp_2), .clk(clk));  // open: clr
  Register #(.width(1)) register_16 (.D(multiplexer_16_out), .en(not_1_out), .Q(jal_2), .clk(clk));  // open: clr
  Register #(.width(32)) register_17 (.D(multiplexer_17_out), .en(not_1_out), .Q(imm_2), .clk(clk));  // open: clr
  Register #(.width(4)) register_18 (.D(multiplexer_18_out), .en(not_1_out), .Q(aluop_2), .clk(clk));  // open: clr
  Multiplexer #(.width(32), .enable("false")) multiplexer_19 (
    .in0(R2), .in1({32{1'b0}}), .out(multiplexer_19_out), .sel(\同步清零_气泡_高电平有效 ));
  Register #(.width(32)) register_19 (.D(multiplexer_19_out), .en(not_1_out), .Q(r2_2), .clk(clk));  // open: clr
  Multiplexer #(.enable("false")) multiplexer_20 (
    .in0(Srlv), .in1(1'b0), .out(multiplexer_20_out), .sel(\同步清零_气泡_高电平有效 ));
  Multiplexer #(.enable("false")) multiplexer_21 (
    .in0(Srav), .in1(1'b0), .out(multiplexer_21_out), .sel(\同步清零_气泡_高电平有效 ));
  Multiplexer #(.enable("false")) multiplexer_22 (
    .in0(Lh), .in1(1'b0), .out(multiplexer_22_out), .sel(\同步清零_气泡_高电平有效 ));
  Multiplexer #(.enable("false")) multiplexer_23 (
    .in0(Blez), .in1(1'b0), .out(multiplexer_23_out), .sel(\同步清零_气泡_高电平有效 ));
  Multiplexer #(.width(5), .enable("false")) multiplexer_24 (
    .in0(rt), .in1({5{1'b0}}), .out(multiplexer_24_out), .sel(\同步清零_气泡_高电平有效 ));
  Register #(.width(1)) register_20 (.D(multiplexer_20_out), .en(not_1_out), .Q(srlv_2), .clk(clk));  // open: clr
  Register #(.width(1)) register_21 (.D(multiplexer_21_out), .en(not_1_out), .Q(srav_2), .clk(clk));  // open: clr
  Register #(.width(1)) register_22 (.D(multiplexer_22_out), .en(not_1_out), .Q(lh_2), .clk(clk));  // open: clr
  Register #(.width(1)) register_23 (.D(multiplexer_23_out), .en(not_1_out), .Q(blez_2), .clk(clk));  // open: clr
  Multiplexer #(.width(32), .enable("false")) multiplexer_25 (
    .in0(PC_4), .in1({32{1'b0}}), .out(multiplexer_25_out), .sel(\同步清零_气泡_高电平有效 ));
  Register #(.width(5)) register_24 (.D(multiplexer_24_out), .en(not_1_out), .Q(rt_2), .clk(clk));  // open: clr
  Register #(.width(32)) register_25 (.D(multiplexer_25_out), .en(not_1_out), .Q(PC_4_2), .clk(clk));  // open: clr
  Multiplexer #(.width(5), .enable("false")) multiplexer_26 (
    .in0(R1_num), .in1({5{1'b0}}), .out(multiplexer_26_out), .sel(\同步清零_气泡_高电平有效 ));
  Register #(.width(5)) register_26 (.D(multiplexer_26_out), .en(not_1_out), .Q(R1_num_2), .clk(clk));  // open: clr
  Multiplexer #(.width(5), .enable("false")) multiplexer_27 (
    .in0(rd), .in1({5{1'b0}}), .out(multiplexer_27_out), .sel(\同步清零_气泡_高电平有效 ));
  Register #(.width(5)) register_27 (.D(multiplexer_27_out), .en(not_1_out), .Q(rd_2), .clk(clk));  // open: clr
  Multiplexer #(.width(5), .enable("false")) multiplexer_28 (
    .in0(R2_num), .in1({5{1'b0}}), .out(multiplexer_28_out), .sel(\同步清零_气泡_高电平有效 ));
  Multiplexer #(.width(32), .enable("false")) multiplexer_29 (
    .in0(Jimm), .in1({32{1'b0}}), .out(multiplexer_29_out), .sel(\同步清零_气泡_高电平有效 ));
  Register #(.width(5)) register_28 (.D(multiplexer_28_out), .en(not_1_out), .Q(R2_num_2), .clk(clk));  // open: clr
  Register #(.width(32)) register_29 (.D(multiplexer_29_out), .en(not_1_out), .Q(JIMM_2), .clk(clk));  // open: clr
  Multiplexer #(.width(5), .enable("false")) multiplexer_30 (
    .in0(shamt), .in1({5{1'b0}}), .out(multiplexer_30_out), .sel(\同步清零_气泡_高电平有效 ));
  Register #(.width(5)) register_30 (.D(multiplexer_30_out), .en(not_1_out), .Q(shamt_2), .clk(clk));  // open: clr
endmodule

module EX_MEM (
  input  Memtoreg,
  input  Syscall,
  input  Srlv,
  input  Memwrite,
  input  Jr,
  input  equal,
  input  Regdst,
  input  Jmp,
  input  Lh,
  input  Regwrite,
  input  Jal,
  input  clk,
  input  \使能端_低电平有效_stall_高电平有效 ,
  input  \同步清零_气泡_高电平有效 ,
  input  [31:0] result,
  input  [31:0] IR,
  input  [4:0] rt,
  input  [4:0] rd,
  input  \传输状态In_表明当前传输数据有效 ,
  input  [31:0] PC,
  input  [31:0] ALUB,
  output memtoreg_2,
  output syscall_2,
  output srlv_2,
  output memwrite_2,
  output jr_2,
  output equal_2,
  output regdst_2,
  output jmp_2,
  output lh_2,
  output regwrite_2,
  output jal_2,
  output [31:0] result_2,
  output [31:0] ir_2,
  output [4:0] rt_2,
  output [4:0] rd_2,
  output \传输状态Out_表明当前传输数据有效 ,
  output [31:0] PC_2,
  output [31:0] ALUB_2
);

  wire multiplexer_1_out, multiplexer_2_out, multiplexer_3_out, multiplexer_4_out, multiplexer_6_out,
       multiplexer_7_out, multiplexer_9_out, multiplexer_10_out, multiplexer_11_out, multiplexer_14_out,
       multiplexer_15_out, multiplexer_16_out, not_1_out;
  wire [4:0] multiplexer_17_out, multiplexer_18_out;
  wire [31:0] multiplexer_5_out, multiplexer_8_out, multiplexer_12_out, multiplexer_13_out;

  not not_1 (not_1_out, \使能端_低电平有效_stall_高电平有效 );
  Multiplexer #(.enable("false")) multiplexer_1 (
    .in0(\传输状态In_表明当前传输数据有效 ), .in1(1'b0), .out(multiplexer_1_out), .sel(\同步清零_气泡_高电平有效 ));
  Register #(.width(1)) register_1 (
    .D(multiplexer_1_out), .en(not_1_out), .Q(\传输状态Out_表明当前传输数据有效 ), .clk(clk));  // open: clr
  Multiplexer #(.enable("false")) multiplexer_2 (
    .in0(Memtoreg), .in1(1'b0), .out(multiplexer_2_out), .sel(\同步清零_气泡_高电平有效 ));
  Multiplexer #(.enable("false")) multiplexer_3 (
    .in0(Memwrite), .in1(1'b0), .out(multiplexer_3_out), .sel(\同步清零_气泡_高电平有效 ));
  Multiplexer #(.enable("false")) multiplexer_4 (
    .in0(Regwrite), .in1(1'b0), .out(multiplexer_4_out), .sel(\同步清零_气泡_高电平有效 ));
  Register #(.width(1)) register_2 (.D(multiplexer_2_out), .en(not_1_out), .Q(memtoreg_2), .clk(clk));  // open: clr
  Register #(.width(1)) register_3 (.D(multiplexer_3_out), .en(not_1_out), .Q(memwrite_2), .clk(clk));  // open: clr
  Register #(.width(1)) register_4 (.D(multiplexer_4_out), .en(not_1_out), .Q(regwrite_2), .clk(clk));  // open: clr
  Multiplexer #(.width(32), .enable("false")) multiplexer_5 (
    .in0(IR), .in1({32{1'b0}}), .out(multiplexer_5_out), .sel(\同步清零_气泡_高电平有效 ));
  Multiplexer #(.enable("false")) multiplexer_6 (
    .in0(Syscall), .in1(1'b0), .out(multiplexer_6_out), .sel(\同步清零_气泡_高电平有效 ));
  Multiplexer #(.enable("false")) multiplexer_7 (
    .in0(Regdst), .in1(1'b0), .out(multiplexer_7_out), .sel(\同步清零_气泡_高电平有效 ));
  Register #(.width(32)) register_5 (.D(multiplexer_5_out), .en(not_1_out), .Q(ir_2), .clk(clk));  // open: clr
  Multiplexer #(.width(32), .enable("false")) multiplexer_8 (
    .in0(PC), .in1({32{1'b0}}), .out(multiplexer_8_out), .sel(\同步清零_气泡_高电平有效 ));
  Register #(.width(32)) register_6 (.D(multiplexer_8_out), .en(not_1_out), .Q(PC_2), .clk(clk));  // open: clr
  Register #(.width(1)) register_7 (.D(multiplexer_6_out), .en(not_1_out), .Q(syscall_2), .clk(clk));  // open: clr
  Register #(.width(1)) register_8 (.D(multiplexer_7_out), .en(not_1_out), .Q(regdst_2), .clk(clk));  // open: clr
  Multiplexer #(.enable("false")) multiplexer_9 (.in0(Jr), .in1(1'b0), .out(multiplexer_9_out), .sel(\同步清零_气泡_高电平有效 ));
  Multiplexer #(.enable("false")) multiplexer_10 (
    .in0(Jmp), .in1(1'b0), .out(multiplexer_10_out), .sel(\同步清零_气泡_高电平有效 ));
  Multiplexer #(.enable("false")) multiplexer_11 (
    .in0(Jal), .in1(1'b0), .out(multiplexer_11_out), .sel(\同步清零_气泡_高电平有效 ));
  Multiplexer #(.width(32), .enable("false")) multiplexer_12 (
    .in0(result), .in1({32{1'b0}}), .out(multiplexer_12_out), .sel(\同步清零_气泡_高电平有效 ));
  Register #(.width(1)) register_9 (.D(multiplexer_9_out), .en(not_1_out), .Q(jr_2), .clk(clk));  // open: clr
  Register #(.width(1)) register_10 (.D(multiplexer_10_out), .en(not_1_out), .Q(jmp_2), .clk(clk));  // open: clr
  Register #(.width(1)) register_11 (.D(multiplexer_11_out), .en(not_1_out), .Q(jal_2), .clk(clk));  // open: clr
  Register #(.width(32)) register_12 (.D(multiplexer_12_out), .en(not_1_out), .Q(result_2), .clk(clk));  // open: clr
  Multiplexer #(.width(32), .enable("false")) multiplexer_13 (
    .in0(ALUB), .in1({32{1'b0}}), .out(multiplexer_13_out), .sel(\同步清零_气泡_高电平有效 ));
  Register #(.width(32)) register_13 (.D(multiplexer_13_out), .en(not_1_out), .Q(ALUB_2), .clk(clk));  // open: clr
  Multiplexer #(.enable("false")) multiplexer_14 (
    .in0(Srlv), .in1(1'b0), .out(multiplexer_14_out), .sel(\同步清零_气泡_高电平有效 ));
  Multiplexer #(.enable("false")) multiplexer_15 (
    .in0(equal), .in1(1'b0), .out(multiplexer_15_out), .sel(\同步清零_气泡_高电平有效 ));
  Multiplexer #(.enable("false")) multiplexer_16 (
    .in0(Lh), .in1(1'b0), .out(multiplexer_16_out), .sel(\同步清零_气泡_高电平有效 ));
  Register #(.width(1)) register_14 (.D(multiplexer_14_out), .en(not_1_out), .Q(srlv_2), .clk(clk));  // open: clr
  Register #(.width(1)) register_15 (.D(multiplexer_15_out), .en(not_1_out), .Q(equal_2), .clk(clk));  // open: clr
  Register #(.width(1)) register_16 (.D(multiplexer_16_out), .en(not_1_out), .Q(lh_2), .clk(clk));  // open: clr
  Multiplexer #(.width(5), .enable("false")) multiplexer_17 (
    .in0(rt), .in1({5{1'b0}}), .out(multiplexer_17_out), .sel(\同步清零_气泡_高电平有效 ));
  Register #(.width(5)) register_17 (.D(multiplexer_17_out), .en(not_1_out), .Q(rt_2), .clk(clk));  // open: clr
  Multiplexer #(.width(5), .enable("false")) multiplexer_18 (
    .in0(rd), .in1({5{1'b0}}), .out(multiplexer_18_out), .sel(\同步清零_气泡_高电平有效 ));
  Register #(.width(5)) register_18 (.D(multiplexer_18_out), .en(not_1_out), .Q(rd_2), .clk(clk));  // open: clr
endmodule

module MEM_WB (
  input  Memtoreg,
  input  Syscall,
  input  Srlv,
  input  Jr,
  input  equal,
  input  Regdst,
  input  Jmp,
  input  Lh,
  input  Regwrite,
  input  Jal,
  input  clk,
  input  \使能端_低电平有效_stall_高电平有效 ,
  input  \同步清零_气泡_高电平有效 ,
  input  [31:0] result,
  input  [31:0] IR,
  input  [4:0] rt,
  input  [4:0] rd,
  input  \传输状态In_表明当前传输数据有效 ,
  input  [31:0] PC,
  input  [31:0] memdata,
  output memtoreg_2,
  output syscall_2,
  output srlv_2,
  output jr_2,
  output equal_2,
  output regdst_2,
  output jmp_2,
  output lh_2,
  output regwrite_2,
  output jal_2,
  output [31:0] result_2,
  output [31:0] ir_2,
  output [4:0] rt_2,
  output [4:0] rd_2,
  output \传输状态Out_表明当前传输数据有效 ,
  output [31:0] PC_2,
  output [31:0] memdata_2
);

  wire multiplexer_1_out, multiplexer_2_out, multiplexer_3_out, multiplexer_5_out, multiplexer_6_out,
       multiplexer_8_out, multiplexer_9_out, multiplexer_10_out, multiplexer_13_out, multiplexer_14_out,
       multiplexer_15_out, not_1_out;
  wire [4:0] multiplexer_16_out, multiplexer_17_out;
  wire [31:0] multiplexer_4_out, multiplexer_7_out, multiplexer_11_out, multiplexer_12_out;

  not not_1 (not_1_out, \使能端_低电平有效_stall_高电平有效 );
  Multiplexer #(.enable("false")) multiplexer_1 (
    .in0(\传输状态In_表明当前传输数据有效 ), .in1(1'b0), .out(multiplexer_1_out), .sel(\同步清零_气泡_高电平有效 ));
  Register #(.width(1)) register_1 (
    .D(multiplexer_1_out), .en(not_1_out), .Q(\传输状态Out_表明当前传输数据有效 ), .clk(clk));  // open: clr
  Multiplexer #(.enable("false")) multiplexer_2 (
    .in0(Memtoreg), .in1(1'b0), .out(multiplexer_2_out), .sel(\同步清零_气泡_高电平有效 ));
  Multiplexer #(.enable("false")) multiplexer_3 (
    .in0(Regwrite), .in1(1'b0), .out(multiplexer_3_out), .sel(\同步清零_气泡_高电平有效 ));
  Register #(.width(1)) register_2 (.D(multiplexer_2_out), .en(not_1_out), .Q(memtoreg_2), .clk(clk));  // open: clr
  Register #(.width(1)) register_3 (.D(multiplexer_3_out), .en(not_1_out), .Q(regwrite_2), .clk(clk));  // open: clr
  Multiplexer #(.width(32), .enable("false")) multiplexer_4 (
    .in0(IR), .in1({32{1'b0}}), .out(multiplexer_4_out), .sel(\同步清零_气泡_高电平有效 ));
  Multiplexer #(.enable("false")) multiplexer_5 (
    .in0(Syscall), .in1(1'b0), .out(multiplexer_5_out), .sel(\同步清零_气泡_高电平有效 ));
  Multiplexer #(.enable("false")) multiplexer_6 (
    .in0(Regdst), .in1(1'b0), .out(multiplexer_6_out), .sel(\同步清零_气泡_高电平有效 ));
  Register #(.width(32)) register_4 (.D(multiplexer_4_out), .en(not_1_out), .Q(ir_2), .clk(clk));  // open: clr
  Multiplexer #(.width(32), .enable("false")) multiplexer_7 (
    .in0(PC), .in1({32{1'b0}}), .out(multiplexer_7_out), .sel(\同步清零_气泡_高电平有效 ));
  Register #(.width(32)) register_5 (.D(multiplexer_7_out), .en(not_1_out), .Q(PC_2), .clk(clk));  // open: clr
  Register #(.width(1)) register_6 (.D(multiplexer_5_out), .en(not_1_out), .Q(syscall_2), .clk(clk));  // open: clr
  Register #(.width(1)) register_7 (.D(multiplexer_6_out), .en(not_1_out), .Q(regdst_2), .clk(clk));  // open: clr
  Multiplexer #(.enable("false")) multiplexer_8 (.in0(Jr), .in1(1'b0), .out(multiplexer_8_out), .sel(\同步清零_气泡_高电平有效 ));
  Multiplexer #(.enable("false")) multiplexer_9 (.in0(Jmp), .in1(1'b0), .out(multiplexer_9_out), .sel(\同步清零_气泡_高电平有效 ));
  Multiplexer #(.enable("false")) multiplexer_10 (
    .in0(Jal), .in1(1'b0), .out(multiplexer_10_out), .sel(\同步清零_气泡_高电平有效 ));
  Multiplexer #(.width(32), .enable("false")) multiplexer_11 (
    .in0(result), .in1({32{1'b0}}), .out(multiplexer_11_out), .sel(\同步清零_气泡_高电平有效 ));
  Register #(.width(1)) register_8 (.D(multiplexer_8_out), .en(not_1_out), .Q(jr_2), .clk(clk));  // open: clr
  Register #(.width(1)) register_9 (.D(multiplexer_9_out), .en(not_1_out), .Q(jmp_2), .clk(clk));  // open: clr
  Register #(.width(1)) register_10 (.D(multiplexer_10_out), .en(not_1_out), .Q(jal_2), .clk(clk));  // open: clr
  Register #(.width(32)) register_11 (.D(multiplexer_11_out), .en(not_1_out), .Q(result_2), .clk(clk));  // open: clr
  Multiplexer #(.width(32), .enable("false")) multiplexer_12 (
    .in0(memdata), .in1({32{1'b0}}), .out(multiplexer_12_out), .sel(\同步清零_气泡_高电平有效 ));
  Register #(.width(32)) register_12 (.D(multiplexer_12_out), .en(not_1_out), .Q(memdata_2), .clk(clk));  // open: clr
  Multiplexer #(.enable("false")) multiplexer_13 (
    .in0(Srlv), .in1(1'b0), .out(multiplexer_13_out), .sel(\同步清零_气泡_高电平有效 ));
  Multiplexer #(.enable("false")) multiplexer_14 (
    .in0(equal), .in1(1'b0), .out(multiplexer_14_out), .sel(\同步清零_气泡_高电平有效 ));
  Multiplexer #(.enable("false")) multiplexer_15 (
    .in0(Lh), .in1(1'b0), .out(multiplexer_15_out), .sel(\同步清零_气泡_高电平有效 ));
  Register #(.width(1)) register_13 (.D(multiplexer_13_out), .en(not_1_out), .Q(srlv_2), .clk(clk));  // open: clr
  Register #(.width(1)) register_14 (.D(multiplexer_14_out), .en(not_1_out), .Q(equal_2), .clk(clk));  // open: clr
  Register #(.width(1)) register_15 (.D(multiplexer_15_out), .en(not_1_out), .Q(lh_2), .clk(clk));  // open: clr
  Register #(.width(5)) register_16 (.D(multiplexer_16_out), .en(not_1_out), .Q(rt_2), .clk(clk));  // open: clr
  Multiplexer #(.width(5), .enable("false")) multiplexer_16 (
    .in0(rt), .in1({5{1'b0}}), .out(multiplexer_16_out), .sel(\同步清零_气泡_高电平有效 ));
  Multiplexer #(.width(5), .enable("false")) multiplexer_17 (
    .in0(rd), .in1({5{1'b0}}), .out(multiplexer_17_out), .sel(\同步清零_气泡_高电平有效 ));
  Register #(.width(5)) register_17 (.D(multiplexer_17_out), .en(not_1_out), .Q(rd_2), .clk(clk));  // open: clr
endmodule

module \分支相关流水线  (
);

  wire alusrc, and_1_out, and_3_out, and_4_out, B_success, beq, bne, CLK, Ena, ex_mem_1_jal_2,
       ex_mem_1_memtoreg_2, ex_mem_1_memwrite_2, ex_mem_1_regdst_2, ex_mem_1_regwrite_2, ex_mem_1_syscall_2,
       Go, id_ex_1_p27, id_ex_1_p28, id_ex_1_p29, id_ex_1_p30, id_ex_1_p31, id_ex_1_p32, id_ex_1_p33,
       id_ex_1_p34, id_ex_1_p35, id_ex_1_p36, id_ex_1_p37, IR1, IR2, IR3, J_success, jal, jmp, jr,
       mem_wb_1_jal_2, mem_wb_1_memtoreg_2, mem_wb_1_regdst_2, mem_wb_1_regwrite_2, MemToReg, Memwrite,
       mips_alu_1_equal, not_1_out, not_2_out, not_3_out, or_1_out, or_3_out, redgdst, regwrite, RST,
       signedext, syscall, W1, W2, W3;
  wire [3:0] aluop, id_ex_1_p38;
  wire [4:0] ex_mem_1_rd_2, ex_mem_1_rt_2, id_ex_1_p39, id_ex_1_p40, mem_wb_1_rd_2, mem_wb_1_rt_2,
       multiplexer_1_out, multiplexer_2_out, multiplexer_10_out, multiplexer_12_out, shamt;
  wire [15:0] \LoadUse次数 , \总周期数 , \插入气泡数 , \无条件分支数 , \条件分支成功数 ;
  wire [31:0] adder_2_out, adder_3_out, adder_4_out, Alu_B, bit_extender_1_out, bit_extender_2_out,
       bit_extender_3_out, ex_mem_1_alub_2, ex_mem_1_ir_2, ex_mem_1_result_2, EX_PC, id_ex_1_p42,
       id_ex_1_p44, id_ex_1_p45, id_ex_1_p47, id_ex_1_p48, ID_PC, IF_PC, IR, LedData, MEM_PC,
       mem_wb_1_memdata_2, mem_wb_1_result_2, mips_alu_1_result, mips_ram_1_p6, mips_regifile_1_r1,
       mips_regifile_1_r2, multiplexer_3_out, multiplexer_4_out, multiplexer_5_out, multiplexer_6_out,
       multiplexer_7_out, multiplexer_8_out, multiplexer_9_out, multiplexer_11_out, next_pc, rom_1_data,
       shifter_1_out, shifter_2_out, WB_PC;

  Button \u_总复位  (.out(RST));
  Button _1 (.out(IR1));
  Button _2 (.out(IR2));
  Button _3 (.out(IR3));
  Button \u_继续运行  (.out(Go));
  LED led_1 (.in(W1));
  LED led_2 (.in(W2));
  LED led_3 (.in(W3));
  not not_1 (not_1_out, Ena);
  Hex_Digit_Display hex_digit_display_1 (.value(LedData[31:28]));  // open: dp
  Register #(.width(32)) PC (.D(multiplexer_4_out), .en(not_1_out), .Q(IF_PC), .clk(CLK));  // open: clr
  Hex_Digit_Display hex_digit_display_2 (.value(LedData[23:20]));  // open: dp
  Hex_Digit_Display hex_digit_display_3 (.value(LedData[27:24]));  // open: dp
  or or_1 (or_1_out, RST, B_success, J_success);
  Hex_Digit_Display hex_digit_display_4 (.value(LedData[19:16]));  // open: dp
  Hex_Digit_Display hex_digit_display_5 (.value(LedData[15:12]));  // open: dp
  Counter #(.width(16), .max('hffff)) counter_1 (
    .D(\总周期数 ), .count(not_1_out), .Q(\总周期数 ), .clk(CLK), .clr(RST));  // open: load, carry
  Adder #(.width(32)) adder_1 (.a(32'h4), .b(IF_PC), .out(next_pc));  // open: cin, cout
  ROM #(.addrWidth(10), .dataWidth(32)) rom_1 (.addr(IF_PC[11:2]), .data(rom_1_data));  // open: sel
  Hex_Digit_Display hex_digit_display_6 (.value(LedData[7:4]));  // open: dp
  Hex_Digit_Display hex_digit_display_7 (.value(LedData[11:8]));  // open: dp
  Clock clock_1 (.out(CLK));
  IF_ID if_id_1 (
    .clk(CLK), .\使能端_低电平有效_stall_高电平有效 (Ena), .\同步清零_气泡_高电平有效 (or_1_out), .IR(rom_1_data), .ir_2(IR),
    .PC(IF_PC), .pc_2(ID_PC));  // open: 传输状态Out_表明当前传输数据有效, 传输状态In_表明当前传输数据有效, IF_matchnum, IF_match, IF_matchnum_2, IF_match_2
  Hex_Digit_Display hex_digit_display_8 (.value(LedData[3:0]));  // open: dp
  // Probe on \总周期数 
  // Probe on \无条件分支数 
  // Probe on \条件分支成功数 
  // Probe on \插入气泡数 
  // Probe on \LoadUse次数 
  \硬布线控制器  \u_硬布线控制器_1  (
    .Func(IR[5:0]), .OP(IR[31:26]), .ALU_OP(aluop), .MemToReg(MemToReg), .MemWrite(Memwrite),
    .ALU_SRC(alusrc), .RegWrite(regwrite), .SysCALL(syscall), .SignedExt(signedext), .RegDst(redgdst),
    .JR(jr), .JMP(jmp), .Beq(beq), .JAL(jal), .Bne(bne));
  assign bit_extender_1_out = {{6{1'b0}}, IR[25:0]};  // Bit_Extender bit_extender_1
  assign bit_extender_2_out = {{16{IR[15]}}, IR[15:0]};  // Bit_Extender bit_extender_2
  Adder #(.width(32)) adder_2 (.a(ID_PC), .b(32'h4), .out(adder_2_out));  // open: cin, cout
  // Probe on IF_PC[11:0]
  Multiplexer #(.width(5), .enable("false")) multiplexer_1 (
    .in0(IR[25:21]), .in1(5'b00010), .out(multiplexer_1_out), .sel(syscall));
  Multiplexer #(.width(5), .enable("false")) multiplexer_2 (
    .in0(IR[20:16]), .in1(5'b00100), .out(multiplexer_2_out), .sel(syscall));
  // Probe on ID_PC[11:0]
  Shifter #(.width(32)) shifter_1 (.in(bit_extender_1_out), .\dist (5'b00010), .out(shifter_1_out));
  assign bit_extender_3_out = {{16{1'b0}}, IR[15:0]};  // Bit_Extender bit_extender_3
  // Probe on EX_PC[11:0]
  // Probe on MEM_PC[11:0]
  MIPS_Regifile mips_regifile_1 (
    .Din(multiplexer_11_out), .Clk(CLK), .R1(mips_regifile_1_r1), .R2(mips_regifile_1_r2),
    .WE(mem_wb_1_regwrite_2), .W_num(multiplexer_12_out), .R1_num(multiplexer_1_out),
    .R2_num(multiplexer_2_out));
  // Probe on WB_PC[11:0]
  Multiplexer #(.width(32), .enable("false")) multiplexer_3 (
    .in0(bit_extender_3_out), .in1(bit_extender_2_out), .out(multiplexer_3_out), .sel(signedext));
  Counter #(.width(16), .max('hffff)) counter_2 (
    .D(\无条件分支数 ), .count(J_success), .Q(\无条件分支数 ), .clk(CLK), .clr(RST));  // open: load, carry
  // ID_EX id_ex_1: pin names not known; wires that end beside it: MemToReg, syscall, Memwrite, alusrc, redgdst, regwrite, signedext, jmp, jal, jr, bne, beq, aluop, IR[20:16], IR[15:11], IR[10:6], mips_regifile_1_r1, mips_regifile_1_r2, multiplexer_3_out, shifter_1_out, ID_PC, IR, adder_2_out, Ena, CLK, or_1_out, id_ex_1_p27, id_ex_1_p28, id_ex_1_p29, id_ex_1_p30, id_ex_1_p31, id_ex_1_p32, id_ex_1_p33, id_ex_1_p34, id_ex_1_p35, id_ex_1_p36, id_ex_1_p37, id_ex_1_p38, id_ex_1_p39, id_ex_1_p40, shamt, id_ex_1_p42, Alu_B, id_ex_1_p44, id_ex_1_p45, EX_PC, id_ex_1_p47, id_ex_1_p48
  or or_2 (J_success, id_ex_1_p33, id_ex_1_p34, id_ex_1_p35);
  Multiplexer #(.width(32), .enable("false")) multiplexer_4 (
    .in0(multiplexer_5_out), .in1(id_ex_1_p42), .out(multiplexer_4_out), .sel(id_ex_1_p35));
  or or_3 (or_3_out, id_ex_1_p33, id_ex_1_p34);
  Multiplexer #(.width(32), .enable("false")) multiplexer_5 (
    .in0(multiplexer_8_out), .in1(id_ex_1_p45), .out(multiplexer_5_out), .sel(or_3_out));
  Counter #(.width(16), .max('hffff)) counter_3 (
    .D(\条件分支成功数 ), .count(B_success), .Q(\条件分支成功数 ), .clk(CLK), .clr(RST));  // open: load, carry
  Multiplexer #(.width(32), .enable("false")) multiplexer_6 (
    .in0(Alu_B), .in1(id_ex_1_p44), .out(multiplexer_6_out), .sel(id_ex_1_p30));
  Multiplexer #(.width(32), .enable("false")) multiplexer_7 (
    .in0(multiplexer_6_out), .in1(32'h22), .out(multiplexer_7_out), .sel(id_ex_1_p28));
  Shifter #(.width(32)) shifter_2 (.in(id_ex_1_p44), .\dist (5'b00010), .out(shifter_2_out));
  Multiplexer #(.width(32), .enable("false")) multiplexer_8 (
    .in0(next_pc), .in1(adder_3_out), .out(multiplexer_8_out), .sel(B_success));
  and and_1 (and_1_out, id_ex_1_p28, mips_alu_1_equal);
  and and_2 (Ena, id_ex_1_p28, not_2_out);
  not not_2 (not_2_out, mips_alu_1_equal);
  not not_3 (not_3_out, mips_alu_1_equal);
  MIPS_ALU mips_alu_1 (
    .X(id_ex_1_p42), .Y(multiplexer_7_out), .AluOP(id_ex_1_p38), .Equal(mips_alu_1_equal),
    .Result(mips_alu_1_result), .shamt(shamt));  // open: Result_2
  Adder #(.width(32)) adder_3 (.a(shifter_2_out), .b(id_ex_1_p48), .out(adder_3_out));  // open: cin, cout
  Register #(.width(32)) register_1 (.D(Alu_B), .en(and_1_out), .Q(LedData), .clk(CLK));  // open: clr
  and and_3 (and_3_out, not_3_out, id_ex_1_p36);
  or or_4 (B_success, and_3_out, and_4_out);
  and and_4 (and_4_out, id_ex_1_p37, mips_alu_1_equal);
  EX_MEM ex_mem_1 (
    .Memtoreg(id_ex_1_p27), .Syscall(id_ex_1_p28), .Memwrite(id_ex_1_p29), .Regdst(id_ex_1_p31),
    .Regwrite(id_ex_1_p32), .Jal(id_ex_1_p34), .clk(CLK), .\使能端_低电平有效_stall_高电平有效 (Ena),
    .\同步清零_气泡_高电平有效 (RST), .result(mips_alu_1_result), .IR(id_ex_1_p47), .PC(EX_PC), .ALUB(Alu_B),
    .memtoreg_2(ex_mem_1_memtoreg_2), .syscall_2(ex_mem_1_syscall_2), .memwrite_2(ex_mem_1_memwrite_2),
    .regdst_2(ex_mem_1_regdst_2), .regwrite_2(ex_mem_1_regwrite_2), .jal_2(ex_mem_1_jal_2),
    .result_2(ex_mem_1_result_2), .ir_2(ex_mem_1_ir_2), .PC_2(MEM_PC), .ALUB_2(ex_mem_1_alub_2),
    .rt(id_ex_1_p39), .rd(id_ex_1_p40), .rt_2(ex_mem_1_rt_2), .rd_2(ex_mem_1_rd_2));  // open: Srlv, Jr, equal, Jmp, Lh, 传输状态In_表明当前传输数据有效, srlv_2, jr_2, equal_2, jmp_2, lh_2, 传输状态Out_表明当前传输数据有效
  // MIPS_RAM mips_ram_1: pin names not known; wires that end beside it: ex_mem_1_result_2[21:2], ex_mem_1_alub_2, ex_mem_1_memwrite_2, CLK, RST, mips_ram_1_p6
  MEM_WB mem_wb_1 (
    .Memtoreg(ex_mem_1_memtoreg_2), .Syscall(ex_mem_1_syscall_2), .Regdst(ex_mem_1_regdst_2),
    .Regwrite(ex_mem_1_regwrite_2), .Jal(ex_mem_1_jal_2), .clk(CLK), .\使能端_低电平有效_stall_高电平有效 (Ena),
    .\同步清零_气泡_高电平有效 (RST), .result(ex_mem_1_result_2), .IR(ex_mem_1_ir_2), .PC(MEM_PC),
    .memdata(mips_ram_1_p6), .memtoreg_2(mem_wb_1_memtoreg_2), .regdst_2(mem_wb_1_regdst_2),
    .regwrite_2(mem_wb_1_regwrite_2), .jal_2(mem_wb_1_jal_2), .result_2(mem_wb_1_result_2), .PC_2(WB_PC),
    .memdata_2(mem_wb_1_memdata_2), .rt(ex_mem_1_rt_2), .rd(ex_mem_1_rd_2), .rt_2(mem_wb_1_rt_2),
    .rd_2(mem_wb_1_rd_2));  // open: Srlv, Jr, equal, Jmp, Lh, syscall_2, srlv_2, jr_2, equal_2, jmp_2, lh_2, ir_2, 传输状态Out_表明当前传输数据有效, 传输状态In_表明当前传输数据有效
  Multiplexer #(.width(32), .enable("false")) multiplexer_9 (
    .in0(mem_wb_1_result_2), .in1(mem_wb_1_memdata_2), .out(multiplexer_9_out), .sel(mem_wb_1_memtoreg_2));
  Adder #(.width(32)) adder_4 (.a(WB_PC), .b(32'h4), .out(adder_4_out));  // open: cin, cout
  Multiplexer #(.width(5), .enable("false")) multiplexer_10 (
    .in0(mem_wb_1_rt_2), .in1(mem_wb_1_rd_2), .out(multiplexer_10_out), .sel(mem_wb_1_regdst_2));
  Multiplexer #(.width(32), .enable("false")) multiplexer_11 (
    .in0(multiplexer_9_out), .in1(adder_4_out), .out(multiplexer_11_out), .sel(mem_wb_1_jal_2));
  Multiplexer #(.width(5), .enable("false")) multiplexer_12 (
    .in0(multiplexer_10_out), .in1({5{1'b1}}), .out(multiplexer_12_out), .sel(mem_wb_1_jal_2));

  // Other names for the same wires on the sheet: rd[4:0] = IR[15:11]; rt[4:0] = IR[20:16]

  // Notes on the sheet:
  //   中断源
  //   中断等待指示
  //   数码管输出
  //   contents of rom_1 (hex, n*v repeats v):
  //   20110020 20020022 8000c06 20110000 20110000 2002000a 10000003 20110000 20110000 2002000a 14110003
  //   20110000 20110000 2002000a c000c14 2002000a 0 0 0 c 2231ffff 0 0 0 112020 0 0 0 c 1620fff6 3e00008
  //   指令字
  //   OP
  //   Func
  //   rs
  //   rt
  //   rd
  //   shamt
  //   imm
  //   PC+4
  //   流水调试日志用
endmodule

module \气泡流水线  (
);

  wire alusrc, and_1_out, and_2_out, and_3_out, and_4_out, and_5_out, and_7_out, and_8_out, B_success, beq,
       bit_extender_4_out, bne, CLK, Ena, EX_jal, EX_lh, ex_mem_1_equal_2, ex_mem_1_jal_2, ex_mem_1_lh_2,
       ex_mem_1_memtoreg_2, ex_mem_1_memwrite_2, ex_mem_1_regdst_2, ex_mem_1_syscall_2, EX_regdst,
       EX_Regwrite, EX_SRAV, EX_SRLV, Go, ID_alusrc, ID_BLEZ, id_ex_1_alusrc_2, id_ex_1_beq_2,
       id_ex_1_blez_2, id_ex_1_bne_2, id_ex_1_jmp_2, id_ex_1_jr_2, id_ex_1_memtoreg_2, id_ex_1_memwrite_2,
       id_ex_1_syscall_2, ID_LH, ID_MemToReg, ID_redgdst, ID_regwrite, ID_signedext, ID_SRAV, ID_SRLV, IR1,
       IR2, IR3, J_success, jal, jmp, jr, LH_Address, MEM_LH, MEM_Regwrite, mem_wb_1_equal_2, mem_wb_1_jal_2,
       mem_wb_1_memtoreg_2, mem_wb_1_regdst_2, mem_wb_1_regwrite_2, mem_wb_1_syscall_2, MemToReg, Memwrite,
       mips_alu_1_equal, \n4控制信号_1_alusrc , \n4控制信号_1_memtoreg , \n4控制信号_1_regdst , \n4控制信号_1_regwrite ,
       \n4控制信号_1_signedext , not_1_out, not_2_out, not_3_out, not_4_out, not_5_out, not_6_out, not_7_out,
       or_1_out, or_5_out, or_6_out, or_10_out, or_12_out, or_13_out, or_14_out, redgdst, regwrite, RST,
       SignedExt, syscall, W1, W2, W3, \数据相关 ;
  wire [3:0] aluop, ID_aluop, id_ex_1_aluop_2, \n4控制信号_1_alu_op ;
  wire [4:0] ex_mem_1_rd_2, ex_mem_1_rt_2, EX_rd, EX_Regwrite_num, EX_rt, ID_R1, ID_R2, MEM_Regwrite_num,
       mem_wb_1_rd_2, mem_wb_1_rt_2, multiplexer_1_out, multiplexer_11_out, multiplexer_12_out,
       multiplexer_15_out, multiplexer_17_out, shamt;
  wire [5:0] ID_Func, ID_OP;
  wire [15:0] \LoadUse次数 , multiplexer_19_out, \总周期数 , \插入气泡数 , \无条件分支数 , \条件分支成功数 ;
  wire [25:6] IR;
  wire [31:0] adder_2_out, adder_3_out, adder_4_out, Alu_B, bit_extender_1_out, bit_extender_2_out,
       bit_extender_3_out, bit_extender_5_out, ex_mem_1_alub_2, ex_mem_1_ir_2, ex_mem_1_result_2, EX_PC,
       EX_R1, id_ex_1_imm_2, id_ex_1_ir_2, id_ex_1_jimm_2, id_ex_1_pc_4_2, ID_PC, IF_PC, LedData, MEM_PC,
       mem_wb_1_memdata_2, mem_wb_1_result_2, mips_alu_1_result, mips_ram_1_p6, mips_regifile_1_r1,
       mips_regifile_1_r2, multiplexer_5_out, multiplexer_6_out, multiplexer_7_out, multiplexer_8_out,
       multiplexer_9_out, multiplexer_10_out, multiplexer_14_out, multiplexer_16_out, multiplexer_18_out,
       next_pc, rom_1_data, shifter_1_out, shifter_2_out, WB_PC;

  Button \u_总复位  (.out(RST));
  Button _1 (.out(IR1));
  Button _2 (.out(IR2));
  Button _3 (.out(IR3));
  Button \u_继续运行  (.out(Go));
  LED led_1 (.in(W1));
  LED led_2 (.in(W2));
  LED led_3 (.in(W3));
  not not_1 (not_1_out, Ena);
  not not_2 (not_2_out, \数据相关 );
  or or_1 (or_1_out, not_1_out, Go);
  and and_1 (and_1_out, not_2_out, or_1_out);
  \数据相关检测  \u_数据相关检测_1  (
    .OP(ID_OP), .EX_WriteReg_num(EX_Regwrite_num), .EX_RegWrite(EX_Regwrite),
    .MEM_WriteReg_num(MEM_Regwrite_num), .MEM_RegWrite(MEM_Regwrite), .\数据相关 (\数据相关 ), .Func(ID_Func),
    .ID_R1_num(ID_R1), .ID_R2_num(ID_R2));
  assign aluop = \n4控制信号_1_alu_op  | ID_aluop;  // OR_Gate or_2, 4 bits wide
  or or_3 (redgdst, \n4控制信号_1_regdst , ID_redgdst);
  or or_4 (regwrite, \n4控制信号_1_regwrite , ID_regwrite);
  Hex_Digit_Display hex_digit_display_1 (.value(LedData[31:28]));  // open: dp
  Register #(.width(32)) PC (.D(multiplexer_6_out), .en(and_1_out), .Q(IF_PC), .clk(CLK));  // open: clr
  not not_3 (not_3_out, Go);
  Hex_Digit_Display hex_digit_display_2 (.value(LedData[23:20]));  // open: dp
  Hex_Digit_Display hex_digit_display_3 (.value(LedData[27:24]));  // open: dp
  or or_5 (or_5_out, RST, B_success, J_success);
  \_4控制信号  \u_4控制信号_1  (
    .OP(ID_OP), .Func(ID_Func), .ALU_OP(\n4控制信号_1_alu_op ), .RegDst(\n4控制信号_1_regdst ),
    .RegWrite(\n4控制信号_1_regwrite ), .MemToReg(\n4控制信号_1_memtoreg ), .AluSrc(\n4控制信号_1_alusrc ),
    .SignedExt(\n4控制信号_1_signedext ), .SRLV(ID_SRLV), .SRAV(ID_SRAV), .LH(ID_LH), .BLEZ(ID_BLEZ));
  Hex_Digit_Display hex_digit_display_4 (.value(LedData[15:12]));  // open: dp
  Hex_Digit_Display hex_digit_display_5 (.value(LedData[19:16]));  // open: dp
  Counter #(.width(16), .max('hffff)) counter_1 (
    .D(\总周期数 ), .count(not_1_out), .Q(\总周期数 ), .clk(CLK), .clr(RST));  // open: load, carry
  Adder #(.width(32)) adder_1 (.a(32'h4), .b(IF_PC), .out(next_pc));  // open: cin, cout
  ROM #(.addrWidth(10), .dataWidth(32)) rom_1 (.addr(IF_PC[11:2]), .data(rom_1_data));  // open: sel
  and and_2 (and_2_out, not_3_out, Ena);
  Hex_Digit_Display hex_digit_display_6 (.value(LedData[7:4]));  // open: dp
  Hex_Digit_Display hex_digit_display_7 (.value(LedData[11:8]));  // open: dp
  Clock clock_1 (.out(CLK));
  IF_ID if_id_1 (
    .clk(CLK), .\使能端_低电平有效_stall_高电平有效 (or_6_out), .\同步清零_气泡_高电平有效 (or_5_out), .IR(rom_1_data),
    .ir_2({ID_OP, IR, ID_Func}), .PC(IF_PC), .pc_2(ID_PC));  // open: 传输状态Out_表明当前传输数据有效, 传输状态In_表明当前传输数据有效, IF_matchnum, IF_match, IF_matchnum_2, IF_match_2
  or or_6 (or_6_out, \数据相关 , and_2_out);
  Hex_Digit_Display hex_digit_display_8 (.value(LedData[3:0]));  // open: dp
  or or_7 (SignedExt, \n4控制信号_1_signedext , ID_signedext);
  or or_8 (alusrc, \n4控制信号_1_alusrc , ID_alusrc);
  or or_9 (MemToReg, \n4控制信号_1_memtoreg , ID_MemToReg);
  // Probe on \总周期数 
  // Probe on \无条件分支数 
  // Probe on \条件分支成功数 
  // Probe on \插入气泡数 
  // Probe on \LoadUse次数 
  \硬布线控制器  \u_硬布线控制器_1  (
    .Func(ID_Func), .OP(ID_OP), .ALU_OP(ID_aluop), .MemToReg(ID_MemToReg), .MemWrite(Memwrite),
    .ALU_SRC(ID_alusrc), .RegWrite(ID_regwrite), .SysCALL(syscall), .SignedExt(ID_signedext),
    .RegDst(ID_redgdst), .JR(jr), .JMP(jmp), .Beq(beq), .JAL(jal), .Bne(bne));
  assign bit_extender_1_out = {{6{1'b0}}, {IR, ID_Func}};  // Bit_Extender bit_extender_1
  assign bit_extender_2_out = {{16{IR[15]}}, {IR[15:6], ID_Func}};  // Bit_Extender bit_extender_2
  Adder #(.width(32)) adder_2 (.a(ID_PC), .b(32'h4), .out(adder_2_out));  // open: cin, cout
  Multiplexer #(.width(5), .enable("false")) multiplexer_1 (
    .in0(EX_rt), .in1(EX_rd), .out(multiplexer_1_out), .sel(EX_regdst));
  // Probe on IF_PC[11:0]
  Multiplexer #(.width(5), .enable("false")) multiplexer_2 (
    .in0(IR[25:21]), .in1(5'b00010), .out(ID_R1), .sel(syscall));
  Multiplexer #(.width(5), .enable("false")) multiplexer_3 (
    .in0(IR[20:16]), .in1(5'b00100), .out(ID_R2), .sel(syscall));
  Multiplexer #(.width(5), .enable("false")) multiplexer_4 (
    .in0(multiplexer_1_out), .in1({5{1'b1}}), .out(EX_Regwrite_num), .sel(EX_jal));
  // Probe on ID_PC[11:0]
  Shifter #(.width(32)) shifter_1 (.in(bit_extender_1_out), .\dist (5'b00010), .out(shifter_1_out));
  assign bit_extender_3_out = {{16{1'b0}}, {IR[15:6], ID_Func}};  // Bit_Extender bit_extender_3
  // Probe on EX_PC[11:0]
  // Probe on MEM_PC[11:0]
  MIPS_Regifile mips_regifile_1 (
    .Din(multiplexer_18_out), .Clk(CLK), .R1(mips_regifile_1_r1), .R2(mips_regifile_1_r2),
    .WE(mem_wb_1_regwrite_2), .W_num(multiplexer_17_out), .R1_num(ID_R1), .R2_num(ID_R2));
  // Probe on WB_PC[11:0]
  Multiplexer #(.width(32), .enable("false")) multiplexer_5 (
    .in0(bit_extender_3_out), .in1(bit_extender_2_out), .out(multiplexer_5_out), .sel(SignedExt));
  not not_4 (not_4_out, Ena);
  and and_3 (and_3_out, \数据相关 , not_4_out);
  Counter #(.width(16), .max('hffff)) counter_2 (
    .D(\无条件分支数 ), .count(J_success), .Q(\无条件分支数 ), .clk(CLK), .clr(RST));  // open: load, carry
  ID_EX id_ex_1 (
    .Memtoreg(MemToReg), .Syscall(syscall), .Bne(bne), .Srlv(ID_SRLV), .Memwrite(Memwrite), .Jr(jr),
    .Srav(ID_SRAV), .Alusrc(alusrc), .Regdst(redgdst), .Jmp(jmp), .Lh(ID_LH), .Regwrite(regwrite), .Beq(beq),
    .Jal(jal), .Blez(ID_BLEZ), .clk(CLK), .\使能端_低电平有效_stall_高电平有效 (and_2_out), .\同步清零_气泡_高电平有效 (or_10_out),
    .IMM(multiplexer_5_out), .IR({ID_OP, IR, ID_Func}), .PC(ID_PC), .memtoreg_2(id_ex_1_memtoreg_2),
    .syscall_2(id_ex_1_syscall_2), .bne_2(id_ex_1_bne_2), .srlv_2(EX_SRLV), .memwrite_2(id_ex_1_memwrite_2),
    .jr_2(id_ex_1_jr_2), .srav_2(EX_SRAV), .alusrc_2(id_ex_1_alusrc_2), .regdst_2(EX_regdst),
    .jmp_2(id_ex_1_jmp_2), .lh_2(EX_lh), .regwrite_2(EX_Regwrite), .beq_2(id_ex_1_beq_2), .jal_2(EX_jal),
    .blez_2(id_ex_1_blez_2), .imm_2(id_ex_1_imm_2), .ir_2(id_ex_1_ir_2), .pc_2(EX_PC), .Aluop(aluop),
    .aluop_2(id_ex_1_aluop_2), .R1(mips_regifile_1_r1), .r1_2(EX_R1), .R2(mips_regifile_1_r2), .r2_2(Alu_B),
    .PC_4(adder_2_out), .PC_4_2(id_ex_1_pc_4_2), .rt(IR[20:16]), .rt_2(EX_rt), .rd(IR[15:11]), .rd_2(EX_rd),
    .shamt(IR[10:6]), .shamt_2(shamt), .Jimm(shifter_1_out), .JIMM_2(id_ex_1_jimm_2));  // open: R1_num, R2_num, R1_num_2, R2_num_2, EX_matchnum, EX_match, EX_matchnum_2, EX_match_2
  or or_10 (or_10_out, or_5_out, and_3_out);
  // Probe on id_ex_1_ir_2
  or or_11 (J_success, id_ex_1_jmp_2, EX_jal, id_ex_1_jr_2);
  Multiplexer #(.width(32), .enable("false")) multiplexer_6 (
    .in0(multiplexer_7_out), .in1(EX_R1), .out(multiplexer_6_out), .sel(id_ex_1_jr_2));
  Counter #(.width(16), .max('hffff)) counter_3 (
    .D(\插入气泡数 ), .count(and_3_out), .Q(\插入气泡数 ), .clk(CLK), .clr(RST));  // open: load, carry
  or or_12 (or_12_out, id_ex_1_jmp_2, EX_jal);
  Multiplexer #(.width(32), .enable("false")) multiplexer_7 (
    .in0(multiplexer_10_out), .in1(id_ex_1_jimm_2), .out(multiplexer_7_out), .sel(or_12_out));
  Counter #(.width(16), .max('hffff)) counter_4 (
    .D(\条件分支成功数 ), .count(B_success), .Q(\条件分支成功数 ), .clk(CLK), .clr(RST));  // open: load, carry
  // Probe on EX_R1
  Multiplexer #(.width(32), .enable("false")) multiplexer_8 (
    .in0(Alu_B), .in1(id_ex_1_imm_2), .out(multiplexer_8_out), .sel(id_ex_1_alusrc_2));
  Multiplexer #(.width(32), .enable("false")) multiplexer_9 (
    .in0(multiplexer_8_out), .in1(32'h22), .out(multiplexer_9_out), .sel(id_ex_1_syscall_2));
  Shifter #(.width(32)) shifter_2 (.in(id_ex_1_imm_2), .\dist (5'b00010), .out(shifter_2_out));
  Multiplexer #(.width(32), .enable("false")) multiplexer_10 (
    .in0(next_pc), .in1(adder_3_out), .out(multiplexer_10_out), .sel(B_success));
  and and_4 (and_4_out, id_ex_1_syscall_2, mips_alu_1_equal);
  not not_5 (not_5_out, mips_alu_1_equal);
  and and_5 (and_5_out, id_ex_1_beq_2, mips_alu_1_equal);
  MIPS_ALU mips_alu_1 (
    .X(EX_R1), .Y(multiplexer_9_out), .AluOP(id_ex_1_aluop_2), .Equal(mips_alu_1_equal),
    .Result(mips_alu_1_result), .shamt(multiplexer_11_out));  // open: Result_2
  // Probe on multiplexer_9_out
  Adder #(.width(32)) adder_3 (.a(shifter_2_out), .b(id_ex_1_pc_4_2), .out(adder_3_out));  // open: cin, cout
  // Probe on multiplexer_11_out
  Register #(.width(32)) register_1 (.D(Alu_B), .en(and_4_out), .Q(LedData), .clk(CLK));  // open: clr
  // AND_Gate and_6 has open pins: in0=id_ex_1_syscall_2, in1=not_6_out, out=open
  not not_6 (not_6_out, mips_alu_1_equal);
  Bit_Extender #(.in_width(32), .out_width(1), .\type ("sign")) bit_extender_4 (
    .in(mips_alu_1_result), .out(bit_extender_4_out));
  // Probe on EX_R1
  // Probe on multiplexer_9_out
  Multiplexer #(.width(5), .enable("false")) multiplexer_11 (
    .in0(shamt), .in1(EX_R1[4:0]), .out(multiplexer_11_out), .sel(or_14_out));
  and and_7 (and_7_out, id_ex_1_blez_2, or_13_out);
  or or_13 (or_13_out, mips_alu_1_equal, bit_extender_4_out);
  and and_8 (and_8_out, not_5_out, id_ex_1_bne_2);
  or or_14 (or_14_out, EX_SRAV, EX_SRLV);
  // Probe on mips_alu_1_result
  // Probe on Alu_B
  EX_MEM ex_mem_1 (
    .Memtoreg(id_ex_1_memtoreg_2), .Syscall(id_ex_1_syscall_2), .Memwrite(id_ex_1_memwrite_2),
    .equal(mips_alu_1_equal), .Regdst(EX_regdst), .Lh(EX_lh), .Regwrite(EX_Regwrite), .Jal(EX_jal),
    .clk(CLK), .\使能端_低电平有效_stall_高电平有效 (and_2_out), .\同步清零_气泡_高电平有效 (RST), .result(mips_alu_1_result),
    .IR(id_ex_1_ir_2), .PC(EX_PC), .ALUB(Alu_B), .memtoreg_2(ex_mem_1_memtoreg_2),
    .syscall_2(ex_mem_1_syscall_2), .memwrite_2(ex_mem_1_memwrite_2), .equal_2(ex_mem_1_equal_2),
    .regdst_2(ex_mem_1_regdst_2), .lh_2(ex_mem_1_lh_2), .regwrite_2(MEM_Regwrite), .jal_2(ex_mem_1_jal_2),
    .result_2(ex_mem_1_result_2), .ir_2(ex_mem_1_ir_2), .PC_2(MEM_PC), .ALUB_2(ex_mem_1_alub_2), .rt(EX_rt),
    .rd(EX_rd), .rt_2(ex_mem_1_rt_2), .rd_2(ex_mem_1_rd_2));  // open: Srlv, Jr, Jmp, 传输状态In_表明当前传输数据有效, srlv_2, jr_2, jmp_2, 传输状态Out_表明当前传输数据有效
  or or_15 (B_success, and_8_out, and_7_out, and_5_out);
  // Probe on ex_mem_1_ir_2
  Multiplexer #(.width(5), .enable("false")) multiplexer_12 (
    .in0(ex_mem_1_rt_2), .in1(ex_mem_1_rd_2), .out(multiplexer_12_out), .sel(ex_mem_1_regdst_2));
  // Probe on ex_mem_1_alub_2
  // Probe on ex_mem_1_result_2
  Multiplexer #(.width(5), .enable("false")) multiplexer_13 (
    .in0(multiplexer_12_out), .in1({5{1'b1}}), .out(MEM_Regwrite_num), .sel(ex_mem_1_jal_2));
  // MIPS_RAM mips_ram_1: pin names not known; wires that end beside it: ex_mem_1_result_2[21:2], ex_mem_1_alub_2, ex_mem_1_memwrite_2, CLK, RST, mips_ram_1_p6
  MEM_WB mem_wb_1 (
    .Memtoreg(ex_mem_1_memtoreg_2), .Syscall(ex_mem_1_syscall_2), .equal(ex_mem_1_equal_2),
    .Regdst(ex_mem_1_regdst_2), .Lh(ex_mem_1_lh_2), .Regwrite(MEM_Regwrite), .Jal(ex_mem_1_jal_2), .clk(CLK),
    .\使能端_低电平有效_stall_高电平有效 (and_2_out), .\同步清零_气泡_高电平有效 (RST), .result(ex_mem_1_result_2),
    .IR(ex_mem_1_ir_2), .PC(MEM_PC), .memdata(mips_ram_1_p6), .memtoreg_2(mem_wb_1_memtoreg_2),
    .syscall_2(mem_wb_1_syscall_2), .equal_2(mem_wb_1_equal_2), .regdst_2(mem_wb_1_regdst_2), .lh_2(MEM_LH),
    .regwrite_2(mem_wb_1_regwrite_2), .jal_2(mem_wb_1_jal_2),
    .result_2({mem_wb_1_result_2[31:2], LH_Address, mem_wb_1_result_2[0]}), .PC_2(WB_PC),
    .memdata_2(mem_wb_1_memdata_2), .rt(ex_mem_1_rt_2), .rd(ex_mem_1_rd_2), .rt_2(mem_wb_1_rt_2),
    .rd_2(mem_wb_1_rd_2));  // open: Srlv, Jr, Jmp, srlv_2, jr_2, jmp_2, ir_2, 传输状态Out_表明当前传输数据有效, 传输状态In_表明当前传输数据有效
  not not_7 (not_7_out, mem_wb_1_equal_2);
  Multiplexer #(.width(32), .enable("false")) multiplexer_14 (
    .in0({mem_wb_1_result_2[31:2], LH_Address, mem_wb_1_result_2[0]}), .in1(mem_wb_1_memdata_2),
    .out(multiplexer_14_out), .sel(mem_wb_1_memtoreg_2));
  Adder #(.width(32)) adder_4 (.a(WB_PC), .b(32'h4), .out(adder_4_out));  // open: cin, cout
  Multiplexer #(.width(5), .enable("false")) multiplexer_15 (
    .in0(mem_wb_1_rt_2), .in1(mem_wb_1_rd_2), .out(multiplexer_15_out), .sel(mem_wb_1_regdst_2));
  Multiplexer #(.width(32), .enable("false")) multiplexer_16 (
    .in0(multiplexer_14_out), .in1(adder_4_out), .out(multiplexer_16_out), .sel(mem_wb_1_jal_2));
  and and_9 (Ena, mem_wb_1_syscall_2, not_7_out);
  Multiplexer #(.width(5), .enable("false")) multiplexer_17 (
    .in0(multiplexer_15_out), .in1({5{1'b1}}), .out(multiplexer_17_out), .sel(mem_wb_1_jal_2));
  Multiplexer #(.width(32), .enable("false")) multiplexer_18 (
    .in0(multiplexer_16_out), .in1(bit_extender_5_out), .out(multiplexer_18_out), .sel(MEM_LH));
  Multiplexer #(.width(16), .enable("false")) multiplexer_19 (
    .in0(mem_wb_1_memdata_2[15:0]), .in1(mem_wb_1_memdata_2[31:16]), .out(multiplexer_19_out),
    .sel(LH_Address));
  assign bit_extender_5_out = {{16{multiplexer_19_out[15]}}, multiplexer_19_out};  // Bit_Extender bit_extender_5

  // Other names for the same wires on the sheet: IR (some bits) = {ID_OP, ID_Func}; rd[4:0] = IR[15:11];
  //   rt[4:0] = IR[20:16]

  // Notes on the sheet:
  //   中断源
  //   中断等待指示
  //   数码管输出
  //   contents of rom_1 (hex, n*v repeats v):
  //   20110001 8100005 20110001 20120002 20130003 8100009 20110001 20120002 20130003 810000d 20110001
  //   20120002 20130003 8100011 20110001 20120002 20130003 c1000fc 20100001 20110001 118fc0 112020
  //   20020022 c 118882 12200001 8100015 112020 20020022 c 20110001 118880 112020 20020022 c 12200001
  //   810001f 20110001 118fc0 112020 20020022 c 1188c3 112020 20020022 c 118903 112020 20020022 c 118903
  //   112020 20020022 c 118903 112020 20020022 c 118903 112020 20020022 c 118903 112020 20020022 c 118903
  //   112020 20020022 c 118903 112020 20020022 c 20100001 109fc0 139fc3 8021 2012000c 24160003 26100001
  //   3210000f 20080008 20090001 139900 2709825 132020 20020022 c 1094022 1500fff9 22100001 2018000f
  //   2188024 108700 20080008 20090001 139902 2709825 132021 20020022 c 1094022 1500fff9 108702 2c9b022
  //   12c00001 8100050 4020 1084027 84400 3508ffff 82021 20020022 c 2010ffff 20110000 ae300000 22100001
  //   22310004 ae300000 22100001 22310004 ae300000 22100001 22310004 ae300000 22100001 22310004 ae300000
  //   22100001 22310004 ae300000 22100001 22310004 ae300000 22100001 22310004 ae300000 22100001 22310004
  //   ae300000 22100001 22310004 ae300000 22100001 22310004 ae300000 22100001 22310004 ae300000 22100001
  //   22310004 ae300000 22100001 22310004 ae300000 22100001 22310004 ae300000 22100001 22310004 ae300000
  //   22100001 22310004 22100001 8020 2011003c 8e130000 8e340000 274402a 11000002 ae330000 ae140000
  //   2231fffc 1611fff8 102020 20020022 c 22100004 2011003c 1611fff2 20020032 c 20080001 20090003 20110876
  //   118d00 112020 20020022 c 200b0008 1118806 1318806 112020 20020022 c 216bffff 1560fff9 2002000a c
  //   20080001 20090003 20110876 118d00 112020 20020022 c 200b0008 1118807 1318807 112020 20020022 c
  //   216bffff 1560fff9 2002000a c 20090000 200b0010 34118483 20120404 118c00 129400 36318281 22520404
  //   ad310000 2328820 21290004 216bffff 1560fffb 200b0020 20090000 85310000 112020 20020022 c 21290002
  //   216bffff 1560fff9 2002000a c 2011fff1 112020 20020022 c 22310001 1a20fffb 2002000a c 2002000a c
  //   20100000 22100001 102020 20020022 c 22100002 102020 20020022 c 22100003 102020 20020022 c 22100004
  //   102020 20020022 c 22100005 102020 20020022 c 22100006 102020 20020022 c 22100007 102020 20020022 c
  //   22100008 102020 20020022 20020022 c 3e00008
  //   指令字
  //   OP
  //   Func
  //   rs
  //   rt
  //   rd
  //   shamt
  //   imm
  //   PC+4
  //   流水调试日志用
endmodule

module \重定向流水线  (
);

  wire alusrc, and_1_out, and_2_out, and_3_out, and_4_out, and_5_out, and_6_out, B_success, beq,
       bit_extender_4_out, bne, CLK, Ena, EX_jal, EX_lh, ex_mem_1_equal_2, ex_mem_1_jal_2, ex_mem_1_lh_2,
       ex_mem_1_memtoreg_2, ex_mem_1_memwrite_2, ex_mem_1_regdst_2, ex_mem_1_syscall_2, EX_regdst,
       EX_Regwrite, EX_SRAV, EX_SRLV, Go, ID_alusrc, ID_BLEZ, id_ex_1_alusrc_2, id_ex_1_beq_2,
       id_ex_1_blez_2, id_ex_1_bne_2, id_ex_1_jmp_2, id_ex_1_jr_2, id_ex_1_memtoreg_2, id_ex_1_memwrite_2,
       id_ex_1_syscall_2, ID_LH, ID_MemToReg, ID_redgdst, ID_regwrite, ID_signedext, ID_SRAV, ID_SRLV, IR1,
       IR2, IR3, J_success, jal, jmp, jr, LH_Address, LoadUse, MEM_Regwrite, mem_wb_1_equal_2,
       mem_wb_1_jal_2, mem_wb_1_memtoreg_2, mem_wb_1_regdst_2, mem_wb_1_syscall_2, MemToReg, Memwrite,
       mips_alu_1_equal, \n4控制信号_1_alusrc , \n4控制信号_1_memtoreg , \n4控制信号_1_regdst , \n4控制信号_1_regwrite ,
       \n4控制信号_1_signedext , not_1_out, not_2_out, not_3_out, not_4_out, not_5_out, or_1_out, or_2_out,
       or_3_out, or_7_out, or_12_out, or_13_out, or_14_out, redgdst, regwrite, RST, SignedExt, syscall, W1,
       W2, W3, WB_LH, WB_regwrite;
  wire [1:0] R1_forward, R2_forward;
  wire [3:0] aluop, ID_aluop, id_ex_1_aluop_2, \n4控制信号_1_alu_op ;
  wire [4:0] ex_mem_1_rd_2, ex_mem_1_rt_2, EX_R1_t, EX_R2, EX_rd, EX_rt, ID_R1, ID_R2, MEM_Regwrite_num,
       mem_wb_1_rd_2, mem_wb_1_rt_2, multiplexer_8_out, multiplexer_10_out, multiplexer_13_out,
       multiplexer_14_out, multiplexer_16_out, shamt, WB_regwrite_num;
  wire [5:0] ID_Func, ID_OP;
  wire [15:0] \LoadUse次数 , multiplexer_21_out, \总周期数 , \无条件分支数 , \条件分支成功数 , \气泡次数 ;
  wire [25:6] IR;
  wire [31:0] adder_2_out, adder_3_out, adder_4_out, Alu_B, bit_extender_1_out, bit_extender_2_out,
       bit_extender_3_out, bit_extender_5_out, EX_IR, ex_mem_1_alub_2, EX_PC, EX_R1, id_ex_1_imm_2,
       id_ex_1_jimm_2, id_ex_1_pc_4_2, id_ex_1_r1_2, id_ex_1_r2_2, ID_PC, IF_PC, LedData, MEM_ALUResult,
       MEM_IR, MEM_PC, mem_wb_1_memdata_2, mips_alu_1_result, mips_ram_1_p6, mips_regifile_1_r1,
       mips_regifile_1_r2, multiplexer_3_out, multiplexer_6_out, multiplexer_7_out, multiplexer_9_out,
       multiplexer_11_out, multiplexer_12_out, multiplexer_17_out, multiplexer_18_out, multiplexer_20_out,
       next_pc, rom_1_data, shifter_1_out, shifter_2_out, WB_ALUResult, WB_IR, WB_MEMData, WB_PC;

  Button \u_总复位  (.out(RST));
  Button _1 (.out(IR1));
  Button _2 (.out(IR2));
  Button _3 (.out(IR3));
  Button \u_继续运行  (.out(Go));
  LED led_1 (.in(W1));
  LED led_2 (.in(W2));
  LED led_3 (.in(W3));
  not not_1 (not_1_out, Ena);
  not not_2 (not_2_out, LoadUse);
  or or_1 (or_1_out, not_1_out, Go);
  and and_1 (and_1_out, not_2_out, or_1_out);
  Hex_Digit_Display hex_digit_display_1 (.value(LedData[31:28]));  // open: dp
  Register #(.width(32)) PC (.D(multiplexer_6_out), .en(and_1_out), .Q(IF_PC), .clk(CLK));  // open: clr
  not not_3 (not_3_out, Go);
  Hex_Digit_Display hex_digit_display_2 (.value(LedData[27:24]));  // open: dp
  Hex_Digit_Display hex_digit_display_3 (.value(LedData[23:20]));  // open: dp
  // Probe on IF_PC
  or or_2 (or_2_out, RST, B_success, J_success);
  \重定向forward  \u_重定向forward_1  (
    .WB_WriteReg_num(WB_regwrite_num), .WB_RegWrite(WB_regwrite), .ID_R1_num(EX_R1_t), .ID_R2_num(EX_R2),
    .MEM_WriteReg_num(MEM_Regwrite_num), .MEM_RegWrite(MEM_Regwrite), .MEM_OP(MEM_IR[31:26]),
    .MEM_Func(MEM_IR[5:0]), .WB_OP(WB_IR[31:26]), .WB_Func(WB_IR[5:0]), .EX_OP(EX_IR[31:26]),
    .EX_Func(EX_IR[5:0]), .R1_Forward(R1_forward), .R2_Forward(R2_forward));
  Hex_Digit_Display hex_digit_display_4 (.value(LedData[19:16]));  // open: dp
  Hex_Digit_Display hex_digit_display_5 (.value(LedData[15:12]));  // open: dp
  Counter #(.width(16), .max('hffff)) counter_1 (
    .D(\总周期数 ), .count(not_1_out), .Q(\总周期数 ), .clk(CLK), .clr(RST));  // open: load, carry
  Adder #(.width(32)) adder_1 (.a(32'h4), .b(IF_PC), .out(next_pc));  // open: cin, cout
  ROM #(.addrWidth(10), .dataWidth(32)) rom_1 (.addr(IF_PC[11:2]), .data(rom_1_data));  // open: sel
  and and_2 (and_2_out, not_3_out, Ena);
  Hex_Digit_Display hex_digit_display_6 (.value(LedData[7:4]));  // open: dp
  Hex_Digit_Display hex_digit_display_7 (.value(LedData[11:8]));  // open: dp
  Clock clock_1 (.out(CLK));
  IF_ID if_id_1 (
    .clk(CLK), .\使能端_低电平有效_stall_高电平有效 (or_3_out), .\同步清零_气泡_高电平有效 (or_2_out), .IR(rom_1_data),
    .ir_2({ID_OP, IR, ID_Func}), .PC(IF_PC), .pc_2(ID_PC));  // open: 传输状态Out_表明当前传输数据有效, 传输状态In_表明当前传输数据有效, IF_matchnum, IF_match, IF_matchnum_2, IF_match_2
  or or_3 (or_3_out, LoadUse, and_2_out);
  Hex_Digit_Display hex_digit_display_8 (.value(LedData[3:0]));  // open: dp
  // Probe on {ID_OP, IR, ID_Func}
  // Probe on R1_forward
  // Probe on R2_forward
  // Probe on \总周期数 
  // Probe on \无条件分支数 
  // Probe on \条件分支成功数 
  // Probe on \气泡次数 
  // Probe on \LoadUse次数 
  \硬布线控制器  \u_硬布线控制器_1  (
    .Func(ID_Func), .OP(ID_OP), .ALU_OP(ID_aluop), .MemToReg(ID_MemToReg), .MemWrite(Memwrite),
    .ALU_SRC(ID_alusrc), .RegWrite(ID_regwrite), .SysCALL(syscall), .SignedExt(ID_signedext),
    .RegDst(ID_redgdst), .JR(jr), .JMP(jmp), .Beq(beq), .JAL(jal), .Bne(bne));
  assign bit_extender_1_out = {{6{1'b0}}, {IR, ID_Func}};  // Bit_Extender bit_extender_1
  assign bit_extender_2_out = {{16{IR[15]}}, {IR[15:6], ID_Func}};  // Bit_Extender bit_extender_2
  Adder #(.width(32)) adder_2 (.a(ID_PC), .b(32'h4), .out(adder_2_out));  // open: cin, cout
  // Probe on IF_PC[11:0]
  Multiplexer #(.width(5), .enable("false")) multiplexer_1 (
    .in0(IR[25:21]), .in1(5'b00010), .out(ID_R1), .sel(syscall));
  Multiplexer #(.width(5), .enable("false")) multiplexer_2 (
    .in0(IR[20:16]), .in1(5'b00100), .out(ID_R2), .sel(syscall));
  // Probe on WB_regwrite_num
  // Probe on ID_PC[11:0]
  Shifter #(.width(32)) shifter_1 (.in(bit_extender_1_out), .\dist (5'b00010), .out(shifter_1_out));
  assign bit_extender_3_out = {{16{1'b0}}, {IR[15:6], ID_Func}};  // Bit_Extender bit_extender_3
  // Probe on multiplexer_20_out
  // Probe on EX_PC[11:0]
  // Probe on MEM_PC[11:0]
  MIPS_Regifile mips_regifile_1 (
    .Din(multiplexer_20_out), .Clk(CLK), .R1(mips_regifile_1_r1), .R2(mips_regifile_1_r2), .WE(WB_regwrite),
    .W_num(WB_regwrite_num), .R1_num(ID_R1), .R2_num(ID_R2));
  \LoadUse检测  \loaduse检测_1  (
    .\LoadUse相关 (LoadUse), .ID_OP(ID_OP), .ID_Func(ID_Func), .EX_OP(EX_IR[31:26]), .ID_R1_num(ID_R1),
    .ID_R2_num(ID_R2), .EX_R_WB(multiplexer_10_out));
  // Probe on WB_PC[11:0]
  Multiplexer #(.width(32), .enable("false")) multiplexer_3 (
    .in0(bit_extender_3_out), .in1(bit_extender_2_out), .out(multiplexer_3_out), .sel(SignedExt));
  assign aluop = \n4控制信号_1_alu_op  | ID_aluop;  // OR_Gate or_4, 4 bits wide
  or or_5 (redgdst, \n4控制信号_1_regdst , ID_redgdst);
  or or_6 (regwrite, \n4控制信号_1_regwrite , ID_regwrite);
  // Probe on {ID_OP, IR, ID_Func}
  \_4控制信号  \u_4控制信号_1  (
    .OP(ID_OP), .Func(ID_Func), .ALU_OP(\n4控制信号_1_alu_op ), .RegDst(\n4控制信号_1_regdst ),
    .RegWrite(\n4控制信号_1_regwrite ), .MemToReg(\n4控制信号_1_memtoreg ), .AluSrc(\n4控制信号_1_alusrc ),
    .SignedExt(\n4控制信号_1_signedext ), .SRLV(ID_SRLV), .SRAV(ID_SRAV), .LH(ID_LH), .BLEZ(ID_BLEZ));
  Counter #(.width(16), .max('hffff)) counter_2 (
    .D(\无条件分支数 ), .count(J_success), .Q(\无条件分支数 ), .clk(CLK), .clr(RST));  // open: load, carry
  ID_EX id_ex_1 (
    .Memtoreg(MemToReg), .Syscall(syscall), .Bne(bne), .Srlv(ID_SRLV), .Memwrite(Memwrite), .Jr(jr),
    .Srav(ID_SRAV), .Alusrc(alusrc), .Regdst(redgdst), .Jmp(jmp), .Lh(ID_LH), .Regwrite(regwrite), .Beq(beq),
    .Jal(jal), .Blez(ID_BLEZ), .clk(CLK), .\使能端_低电平有效_stall_高电平有效 (and_2_out), .\同步清零_气泡_高电平有效 (or_7_out),
    .IMM(multiplexer_3_out), .IR({ID_OP, IR, ID_Func}), .PC(ID_PC), .memtoreg_2(id_ex_1_memtoreg_2),
    .syscall_2(id_ex_1_syscall_2), .bne_2(id_ex_1_bne_2), .srlv_2(EX_SRLV), .memwrite_2(id_ex_1_memwrite_2),
    .jr_2(id_ex_1_jr_2), .srav_2(EX_SRAV), .alusrc_2(id_ex_1_alusrc_2), .regdst_2(EX_regdst),
    .jmp_2(id_ex_1_jmp_2), .lh_2(EX_lh), .regwrite_2(EX_Regwrite), .beq_2(id_ex_1_beq_2), .jal_2(EX_jal),
    .blez_2(id_ex_1_blez_2), .imm_2(id_ex_1_imm_2), .ir_2(EX_IR), .pc_2(EX_PC), .Aluop(aluop),
    .aluop_2(id_ex_1_aluop_2), .R1(mips_regifile_1_r1), .r1_2(id_ex_1_r1_2), .R2(mips_regifile_1_r2),
    .r2_2(id_ex_1_r2_2), .PC_4(adder_2_out), .PC_4_2(id_ex_1_pc_4_2), .rt(IR[20:16]), .rt_2(EX_rt),
    .rd(IR[15:11]), .rd_2(EX_rd), .shamt(IR[10:6]), .shamt_2(shamt), .Jimm(shifter_1_out),
    .JIMM_2(id_ex_1_jimm_2), .R1_num(ID_R1), .R2_num(ID_R2), .R1_num_2(EX_R1_t), .R2_num_2(EX_R2));  // open: EX_matchnum, EX_match, EX_matchnum_2, EX_match_2
  or or_7 (or_7_out, or_2_out, LoadUse);
  Counter #(.width(16), .max('hffff)) counter_3 (
    .D(\LoadUse次数 ), .count(LoadUse), .Q(\LoadUse次数 ), .clk(CLK), .clr(RST));  // open: load, carry
  or or_8 (J_success, id_ex_1_jmp_2, EX_jal, id_ex_1_jr_2);
  Multiplexer #(.select(2), .width(32), .enable("false")) multiplexer_4 (
    .in0(id_ex_1_r2_2), .in1(MEM_ALUResult), .in2(WB_MEMData),
    .in3({WB_ALUResult[31:2], LH_Address, WB_ALUResult[0]}), .out(Alu_B), .sel(R2_forward));
  or or_9 (SignedExt, \n4控制信号_1_signedext , ID_signedext);
  or or_10 (alusrc, \n4控制信号_1_alusrc , ID_alusrc);
  or or_11 (MemToReg, \n4控制信号_1_memtoreg , ID_MemToReg);
  Counter #(.width(16), .max('hffff)) counter_4 (
    .D(\条件分支成功数 ), .count(B_success), .Q(\条件分支成功数 ), .clk(CLK), .clr(RST));  // open: load, carry
  Multiplexer #(.select(2), .width(32), .enable("false")) multiplexer_5 (
    .in0(id_ex_1_r1_2), .in1(MEM_ALUResult), .in2(WB_MEMData),
    .in3({WB_ALUResult[31:2], LH_Address, WB_ALUResult[0]}), .out(EX_R1), .sel(R1_forward));
  Multiplexer #(.width(32), .enable("false")) multiplexer_6 (
    .in0(multiplexer_7_out), .in1(EX_R1), .out(multiplexer_6_out), .sel(id_ex_1_jr_2));
  // Probe on multiplexer_7_out
  or or_12 (or_12_out, id_ex_1_jmp_2, EX_jal);
  Multiplexer #(.width(32), .enable("false")) multiplexer_7 (
    .in0(multiplexer_12_out), .in1(id_ex_1_jimm_2), .out(multiplexer_7_out), .sel(or_12_out));
  Multiplexer #(.width(5), .enable("false")) multiplexer_8 (
    .in0(EX_rt), .in1(EX_rd), .out(multiplexer_8_out), .sel(EX_regdst));
  Multiplexer #(.width(32), .enable("false")) multiplexer_9 (
    .in0(Alu_B), .in1(id_ex_1_imm_2), .out(multiplexer_9_out), .sel(id_ex_1_alusrc_2));
  // Probe on id_ex_1_imm_2
  // Probe on id_ex_1_jimm_2
  Multiplexer #(.width(5), .enable("false")) multiplexer_10 (
    .in0(multiplexer_8_out), .in1({5{1'b1}}), .out(multiplexer_10_out), .sel(EX_jal));
  // Probe on EX_PC
  // Probe on EX_R1
  Multiplexer #(.width(32), .enable("false")) multiplexer_11 (
    .in0(multiplexer_9_out), .in1(32'h22), .out(multiplexer_11_out), .sel(id_ex_1_syscall_2));
  Shifter #(.width(32)) shifter_2 (.in(id_ex_1_imm_2), .\dist (5'b00010), .out(shifter_2_out));
  // Probe on EX_IR
  and and_3 (and_3_out, id_ex_1_syscall_2, mips_alu_1_equal);
  // Probe on multiplexer_11_out
  Multiplexer #(.width(32), .enable("false")) multiplexer_12 (
    .in0(next_pc), .in1(adder_3_out), .out(multiplexer_12_out), .sel(B_success));
  Register #(.width(32)) register_1 (.D(Alu_B), .en(and_3_out), .Q(LedData), .clk(CLK));  // open: clr
  not not_4 (not_4_out, mips_alu_1_equal);
  and and_4 (and_4_out, id_ex_1_beq_2, mips_alu_1_equal);
  MIPS_ALU mips_alu_1 (
    .X(EX_R1), .Y(multiplexer_11_out), .AluOP(id_ex_1_aluop_2), .Equal(mips_alu_1_equal),
    .Result(mips_alu_1_result), .shamt(multiplexer_13_out));  // open: Result_2
  Adder #(.width(32)) adder_3 (.a(shifter_2_out), .b(id_ex_1_pc_4_2), .out(adder_3_out));  // open: cin, cout
  // Probe on multiplexer_13_out
  Bit_Extender #(.in_width(32), .out_width(1), .\type ("sign")) bit_extender_4 (
    .in(mips_alu_1_result), .out(bit_extender_4_out));
  // Probe on mips_alu_1_result
  Multiplexer #(.width(5), .enable("false")) multiplexer_13 (
    .in0(shamt), .in1(EX_R1[4:0]), .out(multiplexer_13_out), .sel(or_14_out));
  and and_5 (and_5_out, id_ex_1_blez_2, or_13_out);
  or or_13 (or_13_out, mips_alu_1_equal, bit_extender_4_out);
  and and_6 (and_6_out, not_4_out, id_ex_1_bne_2);
  or or_14 (or_14_out, EX_SRAV, EX_SRLV);
  // Probe on Alu_B
  EX_MEM ex_mem_1 (
    .Memtoreg(id_ex_1_memtoreg_2), .Syscall(id_ex_1_syscall_2), .Memwrite(id_ex_1_memwrite_2),
    .equal(mips_alu_1_equal), .Regdst(EX_regdst), .Lh(EX_lh), .Regwrite(EX_Regwrite), .Jal(EX_jal),
    .clk(CLK), .\使能端_低电平有效_stall_高电平有效 (and_2_out), .\同步清零_气泡_高电平有效 (RST), .result(mips_alu_1_result),
    .IR(EX_IR), .PC(EX_PC), .ALUB(Alu_B), .memtoreg_2(ex_mem_1_memtoreg_2), .syscall_2(ex_mem_1_syscall_2),
    .memwrite_2(ex_mem_1_memwrite_2), .equal_2(ex_mem_1_equal_2), .regdst_2(ex_mem_1_regdst_2),
    .lh_2(ex_mem_1_lh_2), .regwrite_2(MEM_Regwrite), .jal_2(ex_mem_1_jal_2), .result_2(MEM_ALUResult),
    .ir_2(MEM_IR), .PC_2(MEM_PC), .ALUB_2(ex_mem_1_alub_2), .rt(EX_rt), .rd(EX_rd), .rt_2(ex_mem_1_rt_2),
    .rd_2(ex_mem_1_rd_2));  // open: Srlv, Jr, Jmp, 传输状态In_表明当前传输数据有效, srlv_2, jr_2, jmp_2, 传输状态Out_表明当前传输数据有效
  or or_15 (B_success, and_6_out, and_5_out, and_4_out);
  // Probe on mips_alu_1_result
  // Probe on MEM_IR
  // Probe on ex_mem_1_alub_2
  Multiplexer #(.width(5), .enable("false")) multiplexer_14 (
    .in0(ex_mem_1_rt_2), .in1(ex_mem_1_rd_2), .out(multiplexer_14_out), .sel(ex_mem_1_regdst_2));
  // Probe on MEM_ALUResult
  // Probe on MEM_ALUResult
  Multiplexer #(.width(5), .enable("false")) multiplexer_15 (
    .in0(multiplexer_14_out), .in1({5{1'b1}}), .out(MEM_Regwrite_num), .sel(ex_mem_1_jal_2));
  // Probe on MEM_Regwrite_num
  // MIPS_RAM mips_ram_1: pin names not known; wires that end beside it: MEM_ALUResult[21:2], ex_mem_1_alub_2, ex_mem_1_memwrite_2, CLK, RST, mips_ram_1_p6
  MEM_WB mem_wb_1 (
    .Memtoreg(ex_mem_1_memtoreg_2), .Syscall(ex_mem_1_syscall_2), .equal(ex_mem_1_equal_2),
    .Regdst(ex_mem_1_regdst_2), .Lh(ex_mem_1_lh_2), .Regwrite(MEM_Regwrite), .Jal(ex_mem_1_jal_2), .clk(CLK),
    .\使能端_低电平有效_stall_高电平有效 (and_2_out), .\同步清零_气泡_高电平有效 (RST), .result(MEM_ALUResult), .IR(MEM_IR),
    .PC(MEM_PC), .memdata(mips_ram_1_p6), .memtoreg_2(mem_wb_1_memtoreg_2), .syscall_2(mem_wb_1_syscall_2),
    .equal_2(mem_wb_1_equal_2), .regdst_2(mem_wb_1_regdst_2), .lh_2(WB_LH), .regwrite_2(WB_regwrite),
    .jal_2(mem_wb_1_jal_2), .result_2({WB_ALUResult[31:2], LH_Address, WB_ALUResult[0]}), .ir_2(WB_IR),
    .PC_2(WB_PC), .memdata_2(mem_wb_1_memdata_2), .rt(ex_mem_1_rt_2), .rd(ex_mem_1_rd_2),
    .rt_2(mem_wb_1_rt_2), .rd_2(mem_wb_1_rd_2));  // open: Srlv, Jr, Jmp, srlv_2, jr_2, jmp_2, 传输状态Out_表明当前传输数据有效, 传输状态In_表明当前传输数据有效
  // Probe on WB_IR
  not not_5 (not_5_out, mem_wb_1_equal_2);
  Multiplexer #(.width(5), .enable("false")) multiplexer_16 (
    .in0(mem_wb_1_rt_2), .in1(mem_wb_1_rd_2), .out(multiplexer_16_out), .sel(mem_wb_1_regdst_2));
  Multiplexer #(.width(32), .enable("false")) multiplexer_17 (
    .in0({WB_ALUResult[31:2], LH_Address, WB_ALUResult[0]}), .in1(mem_wb_1_memdata_2),
    .out(multiplexer_17_out), .sel(mem_wb_1_memtoreg_2));
  Adder #(.width(32)) adder_4 (.a(WB_PC), .b(32'h4), .out(adder_4_out));  // open: cin, cout
  and and_7 (Ena, mem_wb_1_syscall_2, not_5_out);
  Multiplexer #(.width(32), .enable("false")) multiplexer_18 (
    .in0(multiplexer_17_out), .in1(adder_4_out), .out(multiplexer_18_out), .sel(mem_wb_1_jal_2));
  // Probe on {WB_ALUResult[31:2], LH_Address, WB_ALUResult[0]}
  Multiplexer #(.width(5), .enable("false")) multiplexer_19 (
    .in0(multiplexer_16_out), .in1({5{1'b1}}), .out(WB_regwrite_num), .sel(mem_wb_1_jal_2));
  Multiplexer #(.width(32), .enable("false")) multiplexer_20 (
    .in0(multiplexer_18_out), .in1(bit_extender_5_out), .out(multiplexer_20_out), .sel(WB_LH));
  // Probe on WB_regwrite_num
  // Probe on mem_wb_1_memdata_2
  Multiplexer #(.width(16), .enable("false")) multiplexer_21 (
    .in0(mem_wb_1_memdata_2[15:0]), .in1(mem_wb_1_memdata_2[31:16]), .out(multiplexer_21_out),
    .sel(LH_Address));
  // Probe on multiplexer_20_out
  assign bit_extender_5_out = {{16{multiplexer_21_out[15]}}, multiplexer_21_out};  // Bit_Extender bit_extender_5
  Multiplexer #(.width(32), .enable("false")) multiplexer_22 (
    .in0(mem_wb_1_memdata_2), .in1(bit_extender_5_out), .out(WB_MEMData), .sel(WB_LH));

  // Other names for the same wires on the sheet: IR (some bits) = {ID_OP, ID_Func}; rd[4:0] = IR[15:11];
  //   rt[4:0] = IR[20:16]; WB_ALUResult[1] = LH_Address

  // Notes on the sheet:
  //   中断源
  //   中断等待指示
  //   OP
  //   Func
  //   OP
  //   Func
  //   OP
  //   Func
  //   数码管输出
  //   contents of rom_1 (hex, n*v repeats v):
  //   20110001 8100005 20110001 20120002 20130003 8100009 20110001 20120002 20130003 810000d 20110001
  //   20120002 20130003 8100011 20110001 20120002 20130003 c1000fc 20100001 20110001 118fc0 112020
  //   20020022 c 118882 12200001 8100015 112020 20020022 c 20110001 118880 112020 20020022 c 12200001
  //   810001f 20110001 118fc0 112020 20020022 c 1188c3 112020 20020022 c 118903 112020 20020022 c 118903
  //   112020 20020022 c 118903 112020 20020022 c 118903 112020 20020022 c 118903 112020 20020022 c 118903
  //   112020 20020022 c 118903 112020 20020022 c 20100001 109fc0 139fc3 8021 2012000c 24160003 26100001
  //   3210000f 20080008 20090001 139900 2709825 132020 20020022 c 1094022 1500fff9 22100001 2018000f
  //   2188024 108700 20080008 20090001 139902 2709825 132021 20020022 c 1094022 1500fff9 108702 2c9b022
  //   12c00001 8100050 4020 1084027 84400 3508ffff 82021 20020022 c 2010ffff 20110000 ae300000 22100001
  //   22310004 ae300000 22100001 22310004 ae300000 22100001 22310004 ae300000 22100001 22310004 ae300000
  //   22100001 22310004 ae300000 22100001 22310004 ae300000 22100001 22310004 ae300000 22100001 22310004
  //   ae300000 22100001 22310004 ae300000 22100001 22310004 ae300000 22100001 22310004 ae300000 22100001
  //   22310004 ae300000 22100001 22310004 ae300000 22100001 22310004 ae300000 22100001 22310004 ae300000
  //   22100001 22310004 22100001 8020 2011003c 8e130000 8e340000 274402a 11000002 ae330000 ae140000
  //   2231fffc 1611fff8 102020 20020022 c 22100004 2011003c 1611fff2 20020032 c 20080001 20090003 20110876
  //   118d00 112020 20020022 c 200b0008 1118806 1318806 112020 20020022 c 216bffff 1560fff9 2002000a c
  //   20080001 20090003 20110876 118d00 112020 20020022 c 200b0008 1118807 1318807 112020 20020022 c
  //   216bffff 1560fff9 2002000a c 20090000 200b0010 34118483 20120404 118c00 129400 36318281 22520404
  //   ad310000 2328820 21290004 216bffff 1560fffb 200b0020 20090000 85310000 112020 20020022 c 21290002
  //   216bffff 1560fff9 2002000a c 2011fff1 112020 20020022 c 22310001 1a20fffb 2002000a c 2002000a c
  //   20100000 22100001 102020 20020022 c 22100002 102020 20020022 c 22100003 102020 20020022 c 22100004
  //   102020 20020022 c 22100005 102020 20020022 c 22100006 102020 20020022 c 22100007 102020 20020022 c
  //   22100008 102020 20020022 20020022 c 3e00008
  //   指令字
  //   OP
  //   Func
  //   rs
  //   rt
  //   rd
  //   shamt
  //   imm
  //   2
  //   PC+4
  //   1
  //   流水调试日志用
  //   22
  //   3
  //   4
  //   10
  //   20
  //   9
  //   21
  //   5
  //   6
  //   8
  //   7
  //   11
  //   12
  //   15
  //   13
  //   16
  //   14
  //   19
  //   17
  //   18
endmodule

module \_4控制信号  (
  input  [5:0] OP,
  input  [5:0] Func,
  output [3:0] ALU_OP,
  output RegDst,
  output RegWrite,
  output MemToReg,
  output AluSrc,
  output SignedExt,
  output SRLV,
  output SRAV,
  output LH,
  output BLEZ
);

  wire comparator_3_eq, comparator_4_eq, comparator_5_eq;
  wire [3:0] multiplexer_1_out, multiplexer_2_out, multiplexer_3_out;

  or or_1 (RegDst, SRLV, SRAV);
  Comparator #(.width(6)) comparator_1 (.a(OP), .b(6'b100001), .eq(AluSrc));  // open: gt, lt
  Comparator #(.width(6)) comparator_2 (.a(OP), .b(6'b000110), .eq(BLEZ));  // open: gt, lt
  Comparator #(.width(6)) comparator_3 (.a(OP), .b({6{1'b0}}), .eq(comparator_3_eq));  // open: gt, lt
  or or_2 (RegWrite, SRLV, SRAV, AluSrc);
  Comparator #(.width(6)) comparator_4 (.a(Func), .b(6'b000110), .eq(comparator_4_eq));  // open: gt, lt
  Comparator #(.width(6)) comparator_5 (.a(Func), .b(6'b000111), .eq(comparator_5_eq));  // open: gt, lt
  and and_1 (SRLV, comparator_4_eq, comparator_3_eq);
  and and_2 (SRAV, comparator_5_eq, comparator_3_eq);
  Multiplexer #(.width(4), .enable("false")) multiplexer_1 (
    .in0(4'b0000), .in1(4'b0010), .out(multiplexer_1_out), .sel(SRLV));
  Multiplexer #(.width(4), .enable("false")) multiplexer_2 (
    .in0(multiplexer_1_out), .in1(4'b0001), .out(multiplexer_2_out), .sel(SRAV));
  Multiplexer #(.width(4), .enable("false")) multiplexer_3 (
    .in0(multiplexer_2_out), .in1(4'b0101), .out(multiplexer_3_out), .sel(AluSrc));
  Multiplexer #(.width(4), .enable("false")) multiplexer_4 (
    .in0(multiplexer_3_out), .in1(4'b1011), .out(ALU_OP), .sel(BLEZ));

  assign LH = AluSrc;
  assign MemToReg = AluSrc;
  assign SignedExt = AluSrc;

  // Notes on the sheet:
  //   指令译码信号
  //   控制信号
endmodule

module \LoadUse检测  (
  input  [5:0] ID_OP,
  input  [5:0] EX_OP,
  input  [4:0] ID_R1_num,
  input  [4:0] EX_R_WB,
  input  [5:0] ID_Func,
  input  [4:0] ID_R2_num,
  output \LoadUse相关 
);

  wire comparator_1_eq, comparator_2_eq, comparator_3_eq, comparator_4_eq, or_1_out, or_2_out;

  Comparator #(.width(6)) comparator_1 (.a(EX_OP), .b(6'b100001), .eq(comparator_1_eq));  // open: gt, lt
  Comparator #(.width(6)) comparator_2 (.a(EX_OP), .b(6'b100011), .eq(comparator_2_eq));  // open: gt, lt
  or or_1 (or_1_out, comparator_1_eq, comparator_2_eq);
  Comparator #(.width(5)) comparator_3 (.a(ID_R1_num), .b(EX_R_WB), .eq(comparator_3_eq));  // open: gt, lt
  Comparator #(.width(5)) comparator_4 (.a(EX_R_WB), .b(ID_R2_num), .eq(comparator_4_eq));  // open: gt, lt
  or or_2 (or_2_out, comparator_3_eq, comparator_4_eq);
  and and_1 (\LoadUse相关 , or_1_out, or_2_out);

  // Other names for the same wires on the sheet: EX_R1_num[4:0] = EX_R_WB
endmodule

module \重定向数据相关检测  (
  input  [5:0] OP,
  input  [4:0] WB_WriteReg_num,
  input  WB_RegWrite,
  input  [4:0] MEM_WriteReg_num,
  input  MEM_RegWrite,
  input  [5:0] Func,
  input  [4:0] ID_R1_num,
  input  [4:0] ID_R2_num,
  output \R1数据相关 ,
  output \R2数据相关 ,
  output \R1_WB数据相关 ,
  output \R2_WB数据相关 
);

  wire and_1_out, and_2_out, and_3_out, and_4_out, and_5_out, and_6_out, and_7_out, and_8_out,
       comparator_1_eq, comparator_2_eq, comparator_3_eq, comparator_4_eq, comparator_5_eq, comparator_6_eq,
       comparator_7_eq, comparator_8_eq, comparator_9_eq, comparator_10_eq, not_1_out, not_2_out, not_3_out,
       not_4_out, or_1_out, or_2_out, \源寄存器使用情况_1_r1_used , \源寄存器使用情况_1_r2_used , \源寄存器使用情况_2_r1_used ,
       \源寄存器使用情况_2_r2_used ;

  \源寄存器使用情况  \u_源寄存器使用情况_1  (
    .OP0(OP[0]), .OP1(OP[1]), .OP2(OP[2]), .OP3(OP[3]), .OP4(OP[4]), .OP5(OP[5]), .F0(Func[0]), .F1(Func[1]),
    .F2(Func[2]), .F3(Func[3]), .F4(Func[4]), .F5(Func[5]), .R1_Used(\源寄存器使用情况_1_r1_used ),
    .R2_Used(\源寄存器使用情况_1_r2_used ));
  \源寄存器使用情况  \u_源寄存器使用情况_2  (
    .OP0(OP[0]), .OP1(OP[1]), .OP2(OP[2]), .OP3(OP[3]), .OP4(OP[4]), .OP5(OP[5]), .F0(Func[0]), .F1(Func[1]),
    .F2(Func[2]), .F3(Func[3]), .F4(Func[4]), .F5(Func[5]), .R1_Used(\源寄存器使用情况_2_r1_used ),
    .R2_Used(\源寄存器使用情况_2_r2_used ));
  Comparator #(.width(5)) comparator_1 (.a(ID_R1_num), .b({5{1'b0}}), .eq(comparator_1_eq));  // open: gt, lt
  Comparator #(.width(5)) comparator_2 (.a(ID_R1_num), .b(WB_WriteReg_num), .eq(comparator_2_eq));  // open: gt, lt
  Comparator #(.width(5)) comparator_3 (.a(ID_R1_num), .b(MEM_WriteReg_num), .eq(comparator_3_eq));  // open: gt, lt
  Comparator #(.width(5)) comparator_4 (.a(ID_R2_num), .b(WB_WriteReg_num), .eq(comparator_4_eq));  // open: gt, lt
  Comparator #(.width(5)) comparator_5 (.a(ID_R2_num), .b(MEM_WriteReg_num), .eq(comparator_5_eq));  // open: gt, lt
  Comparator #(.width(5)) comparator_6 (.a(ID_R2_num), .b({5{1'b0}}), .eq(comparator_6_eq));  // open: gt, lt
  Comparator #(.width(5)) comparator_7 (.a(ID_R1_num), .b({5{1'b0}}), .eq(comparator_7_eq));  // open: gt, lt
  Comparator #(.width(5)) comparator_8 (.a(ID_R1_num), .b(WB_WriteReg_num), .eq(comparator_8_eq));  // open: gt, lt
  Comparator #(.width(5)) comparator_9 (.a(ID_R2_num), .b({5{1'b0}}), .eq(comparator_9_eq));  // open: gt, lt
  Comparator #(.width(5)) comparator_10 (.a(ID_R2_num), .b(WB_WriteReg_num), .eq(comparator_10_eq));  // open: gt, lt
  not not_1 (not_1_out, comparator_1_eq);
  and and_1 (and_1_out, comparator_2_eq, WB_RegWrite);
  and and_2 (and_2_out, comparator_3_eq, MEM_RegWrite);
  and and_3 (and_3_out, comparator_4_eq, WB_RegWrite);
  and and_4 (and_4_out, comparator_5_eq, MEM_RegWrite);
  not not_2 (not_2_out, comparator_6_eq);
  not not_3 (not_3_out, comparator_7_eq);
  and and_5 (and_5_out, comparator_8_eq, WB_RegWrite);
  not not_4 (not_4_out, comparator_9_eq);
  and and_6 (and_6_out, comparator_10_eq, WB_RegWrite);
  and and_7 (and_7_out, not_1_out, or_1_out);
  or or_1 (or_1_out, and_1_out, and_2_out);
  or or_2 (or_2_out, and_3_out, and_4_out);
  and and_8 (and_8_out, or_2_out, not_2_out);
  and and_9 (\R1_WB数据相关 , not_3_out, \源寄存器使用情况_2_r1_used , and_5_out);
  and and_10 (\R2_WB数据相关 , not_4_out, \源寄存器使用情况_2_r2_used , and_6_out);
  and and_11 (\R1数据相关 , \源寄存器使用情况_1_r1_used , and_7_out);
  and and_12 (\R2数据相关 , \源寄存器使用情况_1_r2_used , and_8_out);

  // Other names for the same wires on the sheet: OP_CODE[5:0] = OP

  // Notes on the sheet:
  //   1
  //   2
  //   1
  //   2
  //   2
  //   3
  //   3
  //   2
  //   1
  //   1
endmodule

module \重定向MEMtoEX  (
  input  OP0,
  input  OP1,
  input  OP2,
  input  OP3,
  input  OP4,
  input  OP5,
  input  F0,
  input  F1,
  input  F2,
  input  F3,
  input  F4,
  input  F5,
  output MemAluResult
);

  wire and_1_out, and_2_out, and_3_out, and_4_out, and_5_out, and_6_out, and_7_out, and_8_out, and_9_out,
       and_10_out, and_11_out, and_12_out, and_13_out, and_14_out, and_15_out, and_16_out, and_17_out,
       and_18_out, and_19_out, not_1_out, not_2_out, not_3_out, not_4_out, not_5_out, not_6_out, not_7_out,
       not_8_out, not_9_out, not_10_out, not_11_out, not_12_out, not_13_out, not_14_out, not_15_out,
       not_16_out, not_17_out, not_18_out, not_19_out, not_20_out, not_21_out, not_22_out, not_23_out,
       not_24_out, not_25_out, not_26_out, not_27_out, not_28_out, not_29_out, not_30_out, not_31_out,
       not_32_out, not_33_out, not_34_out, not_35_out, not_36_out, not_37_out, not_38_out, not_39_out,
       not_40_out, not_41_out, not_42_out, not_43_out, not_44_out, not_45_out, not_46_out, not_47_out,
       not_48_out, not_49_out, not_50_out, not_51_out, not_52_out, not_53_out, not_54_out, not_55_out,
       not_56_out, not_57_out, not_58_out, not_59_out, not_60_out, not_61_out, not_62_out, not_63_out,
       not_64_out, not_65_out, not_66_out, not_67_out, not_68_out, not_69_out, not_70_out, not_71_out,
       not_72_out, not_73_out, not_74_out, not_75_out, not_76_out, not_77_out, not_78_out, not_79_out,
       not_80_out, not_81_out, not_82_out, not_83_out, not_84_out, not_85_out, not_86_out, not_87_out,
       not_88_out, not_89_out, not_90_out, not_91_out, not_92_out, not_93_out, not_94_out, not_95_out,
       not_96_out, not_97_out, not_98_out, not_99_out, not_100_out, not_101_out, not_102_out, not_103_out,
       not_104_out, not_105_out, not_106_out, not_107_out, not_108_out, not_109_out, not_110_out,
       not_111_out, not_112_out, not_113_out, not_114_out, not_115_out, not_116_out, not_117_out,
       not_118_out, not_119_out, not_120_out, not_121_out, not_122_out, not_123_out, not_124_out,
       not_125_out, not_126_out, not_127_out, not_128_out, not_129_out, not_130_out, not_131_out,
       not_132_out, not_133_out, not_134_out, not_135_out, not_136_out, not_137_out, not_138_out,
       not_139_out, not_140_out, not_141_out, not_142_out, not_143_out, not_144_out, not_145_out,
       not_146_out, not_147_out, not_148_out, not_149_out, not_150_out, not_151_out;

  not not_1 (not_1_out, OP5);
  not not_2 (not_2_out, OP4);
  not not_3 (not_3_out, OP3);
  not not_4 (not_4_out, OP2);
  not not_5 (not_5_out, OP1);
  not not_6 (not_6_out, OP0);
  not not_7 (not_7_out, F5);
  not not_8 (not_8_out, F4);
  not not_9 (not_9_out, F3);
  not not_10 (not_10_out, F2);
  not not_11 (not_11_out, F1);
  not not_12 (not_12_out, F0);
  not not_13 (not_13_out, OP5);
  not not_14 (not_14_out, OP4);
  not not_15 (not_15_out, OP3);
  not not_16 (not_16_out, OP2);
  not not_17 (not_17_out, OP1);
  not not_18 (not_18_out, OP0);
  not not_19 (not_19_out, F5);
  not not_20 (not_20_out, F4);
  not not_21 (not_21_out, F3);
  not not_22 (not_22_out, F2);
  not not_23 (not_23_out, OP5);
  not not_24 (not_24_out, OP4);
  not not_25 (not_25_out, OP3);
  not not_26 (not_26_out, OP2);
  not not_27 (not_27_out, OP1);
  not not_28 (not_28_out, OP0);
  not not_29 (not_29_out, F5);
  not not_30 (not_30_out, F4);
  not not_31 (not_31_out, F3);
  not not_32 (not_32_out, F2);
  not not_33 (not_33_out, F0);
  not not_34 (not_34_out, OP5);
  not not_35 (not_35_out, OP4);
  not not_36 (not_36_out, OP3);
  not not_37 (not_37_out, OP2);
  not not_38 (not_38_out, OP1);
  not not_39 (not_39_out, OP0);
  not not_40 (not_40_out, F4);
  not not_41 (not_41_out, F3);
  not not_42 (not_42_out, F2);
  not not_43 (not_43_out, F1);
  not not_44 (not_44_out, F0);
  not not_45 (not_45_out, OP5);
  not not_46 (not_46_out, OP4);
  not not_47 (not_47_out, OP3);
  not not_48 (not_48_out, OP2);
  not not_49 (not_49_out, OP1);
  not not_50 (not_50_out, OP0);
  not not_51 (not_51_out, F4);
  not not_52 (not_52_out, F3);
  not not_53 (not_53_out, F2);
  not not_54 (not_54_out, F1);
  not not_55 (not_55_out, OP5);
  not not_56 (not_56_out, OP4);
  not not_57 (not_57_out, OP3);
  not not_58 (not_58_out, OP2);
  not not_59 (not_59_out, OP1);
  not not_60 (not_60_out, OP0);
  not not_61 (not_61_out, F4);
  not not_62 (not_62_out, F3);
  not not_63 (not_63_out, F2);
  not not_64 (not_64_out, F0);
  not not_65 (not_65_out, OP5);
  not not_66 (not_66_out, OP4);
  not not_67 (not_67_out, OP3);
  not not_68 (not_68_out, OP2);
  not not_69 (not_69_out, OP1);
  not not_70 (not_70_out, OP0);
  not not_71 (not_71_out, F4);
  not not_72 (not_72_out, F3);
  not not_73 (not_73_out, F1);
  not not_74 (not_74_out, F0);
  not not_75 (not_75_out, OP5);
  not not_76 (not_76_out, OP4);
  not not_77 (not_77_out, OP3);
  not not_78 (not_78_out, OP2);
  not not_79 (not_79_out, OP1);
  not not_80 (not_80_out, OP0);
  not not_81 (not_81_out, F4);
  not not_82 (not_82_out, F3);
  not not_83 (not_83_out, F1);
  not not_84 (not_84_out, OP5);
  not not_85 (not_85_out, OP4);
  not not_86 (not_86_out, OP3);
  not not_87 (not_87_out, OP2);
  not not_88 (not_88_out, OP1);
  not not_89 (not_89_out, OP0);
  not not_90 (not_90_out, F4);
  not not_91 (not_91_out, F3);
  not not_92 (not_92_out, OP5);
  not not_93 (not_93_out, OP4);
  not not_94 (not_94_out, OP3);
  not not_95 (not_95_out, OP2);
  not not_96 (not_96_out, OP1);
  not not_97 (not_97_out, OP0);
  not not_98 (not_98_out, F4);
  not not_99 (not_99_out, F2);
  not not_100 (not_100_out, F0);
  not not_101 (not_101_out, OP5);
  not not_102 (not_102_out, OP4);
  not not_103 (not_103_out, OP3);
  not not_104 (not_104_out, OP2);
  not not_105 (not_105_out, OP1);
  not not_106 (not_106_out, OP0);
  not not_107 (not_107_out, F4);
  not not_108 (not_108_out, F2);
  not not_109 (not_109_out, OP5);
  not not_110 (not_110_out, OP4);
  not not_111 (not_111_out, OP3);
  not not_112 (not_112_out, OP2);
  not not_113 (not_113_out, OP5);
  not not_114 (not_114_out, OP4);
  not not_115 (not_115_out, OP2);
  not not_116 (not_116_out, OP1);
  not not_117 (not_117_out, OP0);
  not not_118 (not_118_out, OP5);
  not not_119 (not_119_out, OP4);
  not not_120 (not_120_out, OP1);
  not not_121 (not_121_out, OP0);
  not not_122 (not_122_out, OP5);
  not not_123 (not_123_out, OP4);
  not not_124 (not_124_out, OP2);
  not not_125 (not_125_out, OP1);
  not not_126 (not_126_out, OP5);
  not not_127 (not_127_out, OP4);
  not not_128 (not_128_out, OP2);
  not not_129 (not_129_out, OP0);
  not not_130 (not_130_out, OP5);
  not not_131 (not_131_out, OP4);
  not not_132 (not_132_out, OP1);
  not not_133 (not_133_out, OP5);
  not not_134 (not_134_out, OP4);
  not not_135 (not_135_out, OP3);
  not not_136 (not_136_out, OP2);
  not not_137 (not_137_out, OP1);
  not not_138 (not_138_out, OP0);
  not not_139 (not_139_out, F5);
  not not_140 (not_140_out, F4);
  not not_141 (not_141_out, F3);
  not not_142 (not_142_out, OP5);
  not not_143 (not_143_out, OP4);
  not not_144 (not_144_out, OP3);
  not not_145 (not_145_out, OP2);
  not not_146 (not_146_out, OP1);
  not not_147 (not_147_out, OP0);
  not not_148 (not_148_out, F5);
  not not_149 (not_149_out, F4);
  not not_150 (not_150_out, F3);
  not not_151 (not_151_out, F0);
  and and_1 (and_1_out, not_1_out, not_2_out, not_3_out, not_4_out, not_5_out, not_6_out, not_7_out, not_8_out, not_9_out, not_10_out, not_11_out, not_12_out);
  and and_2 (and_2_out, not_13_out, not_14_out, not_15_out, not_16_out, not_17_out, not_18_out, not_19_out, not_20_out, not_21_out, not_22_out, F1, F0);
  and and_3 (and_3_out, not_23_out, not_24_out, not_25_out, not_26_out, not_27_out, not_28_out, not_29_out, not_30_out, not_31_out, not_32_out, F1, not_33_out);
  and and_4 (and_4_out, not_34_out, not_35_out, not_36_out, not_37_out, not_38_out, not_39_out, F5, not_40_out, not_41_out, not_42_out, not_43_out, not_44_out);
  and and_5 (and_5_out, not_45_out, not_46_out, not_47_out, not_48_out, not_49_out, not_50_out, F5, not_51_out, not_52_out, not_53_out, not_54_out, F0);
  and and_6 (and_6_out, not_55_out, not_56_out, not_57_out, not_58_out, not_59_out, not_60_out, F5, not_61_out, not_62_out, not_63_out, F1, not_64_out);
  and and_7 (and_7_out, not_65_out, not_66_out, not_67_out, not_68_out, not_69_out, not_70_out, F5, not_71_out, not_72_out, F2, not_73_out, not_74_out);
  and and_8 (and_8_out, not_75_out, not_76_out, not_77_out, not_78_out, not_79_out, not_80_out, F5, not_81_out, not_82_out, F2, not_83_out, F0);
  and and_9 (and_9_out, not_84_out, not_85_out, not_86_out, not_87_out, not_88_out, not_89_out, F5, not_90_out, not_91_out, F2, F1, F0);
  and and_10 (and_10_out, not_92_out, not_93_out, not_94_out, not_95_out, not_96_out, not_97_out, F5, not_98_out, F3, not_99_out, F1, not_100_out);
  and and_11 (and_11_out, not_101_out, not_102_out, not_103_out, not_104_out, not_105_out, not_106_out, F5, not_107_out, F3, not_108_out, F1, F0);
  and and_12 (and_12_out, not_109_out, not_110_out, not_111_out, not_112_out, OP1, OP0);
  and and_13 (and_13_out, not_113_out, not_114_out, OP3, not_115_out, not_116_out, not_117_out);
  and and_14 (and_14_out, not_118_out, not_119_out, OP3, OP2, not_120_out, not_121_out);
  and and_15 (and_15_out, not_122_out, not_123_out, OP3, not_124_out, not_125_out, OP0);
  and and_16 (and_16_out, not_126_out, not_127_out, OP3, not_128_out, OP1, not_129_out);
  and and_17 (and_17_out, not_130_out, not_131_out, OP3, OP2, not_132_out, OP0);
  and and_18 (and_18_out, not_133_out, not_134_out, not_135_out, not_136_out, not_137_out, not_138_out, not_139_out, not_140_out, not_141_out, F2, F1, F0);
  and and_19 (and_19_out, not_142_out, not_143_out, not_144_out, not_145_out, not_146_out, not_147_out, not_148_out, not_149_out, not_150_out, F2, F1, not_151_out);
  or or_1 (MemAluResult, and_1_out, and_2_out, and_3_out, and_4_out, and_5_out, and_6_out, and_7_out, and_8_out, and_9_out, and_10_out, and_11_out, and_12_out, and_13_out, and_14_out, and_15_out, and_16_out, and_17_out, and_18_out, and_19_out);
endmodule

module \重定向WBtoEX  (
  input  OP0,
  input  OP1,
  input  OP2,
  input  OP3,
  input  OP4,
  input  OP5,
  input  F0,
  input  F1,
  input  F2,
  input  F3,
  input  F4,
  input  F5,
  output WBAluResult,
  output WBMemData
);

  wire and_1_out, and_2_out, and_3_out, and_4_out, and_5_out, and_6_out, and_7_out, and_8_out, and_9_out,
       and_10_out, and_11_out, and_12_out, and_13_out, and_14_out, and_15_out, and_16_out, and_17_out,
       and_18_out, and_19_out, and_20_out, and_21_out, not_1_out, not_2_out, not_3_out, not_4_out, not_5_out,
       not_6_out, not_7_out, not_8_out, not_9_out, not_10_out, not_11_out, not_12_out, not_13_out,
       not_14_out, not_15_out, not_16_out, not_17_out, not_18_out, not_19_out, not_20_out, not_21_out,
       not_22_out, not_23_out, not_24_out, not_25_out, not_26_out, not_27_out, not_28_out, not_29_out,
       not_30_out, not_31_out, not_32_out, not_33_out, not_34_out, not_35_out, not_36_out, not_37_out,
       not_38_out, not_39_out, not_40_out, not_41_out, not_42_out, not_43_out, not_44_out, not_45_out,
       not_46_out, not_47_out, not_48_out, not_49_out, not_50_out, not_51_out, not_52_out, not_53_out,
       not_54_out, not_55_out, not_56_out, not_57_out, not_58_out, not_59_out, not_60_out, not_61_out,
       not_62_out, not_63_out, not_64_out, not_65_out, not_66_out, not_67_out, not_68_out, not_69_out,
       not_70_out, not_71_out, not_72_out, not_73_out, not_74_out, not_75_out, not_76_out, not_77_out,
       not_78_out, not_79_out, not_80_out, not_81_out, not_82_out, not_83_out, not_84_out, not_85_out,
       not_86_out, not_87_out, not_88_out, not_89_out, not_90_out, not_91_out, not_92_out, not_93_out,
       not_94_out, not_95_out, not_96_out, not_97_out, not_98_out, not_99_out, not_100_out, not_101_out,
       not_102_out, not_103_out, not_104_out, not_105_out, not_106_out, not_107_out, not_108_out,
       not_109_out, not_110_out, not_111_out, not_112_out, not_113_out, not_114_out, not_115_out,
       not_116_out, not_117_out, not_118_out, not_119_out, not_120_out, not_121_out, not_122_out,
       not_123_out, not_124_out, not_125_out, not_126_out, not_127_out, not_128_out, not_129_out,
       not_130_out, not_131_out, not_132_out, not_133_out, not_134_out, not_135_out, not_136_out,
       not_137_out, not_138_out, not_139_out, not_140_out, not_141_out, not_142_out, not_143_out,
       not_144_out, not_145_out, not_146_out, not_147_out, not_148_out, not_149_out, not_150_out,
       not_151_out, not_152_out, not_153_out, not_154_out, not_155_out, not_156_out, not_157_out, not_158_out;

  not not_1 (not_1_out, OP5);
  not not_2 (not_2_out, OP4);
  not not_3 (not_3_out, OP3);
  not not_4 (not_4_out, OP2);
  not not_5 (not_5_out, OP1);
  not not_6 (not_6_out, OP0);
  not not_7 (not_7_out, F5);
  not not_8 (not_8_out, F4);
  not not_9 (not_9_out, F3);
  not not_10 (not_10_out, F2);
  not not_11 (not_11_out, F1);
  not not_12 (not_12_out, F0);
  not not_13 (not_13_out, OP5);
  not not_14 (not_14_out, OP4);
  not not_15 (not_15_out, OP3);
  not not_16 (not_16_out, OP2);
  not not_17 (not_17_out, OP1);
  not not_18 (not_18_out, OP0);
  not not_19 (not_19_out, F5);
  not not_20 (not_20_out, F4);
  not not_21 (not_21_out, F3);
  not not_22 (not_22_out, F2);
  not not_23 (not_23_out, OP5);
  not not_24 (not_24_out, OP4);
  not not_25 (not_25_out, OP3);
  not not_26 (not_26_out, OP2);
  not not_27 (not_27_out, OP1);
  not not_28 (not_28_out, OP0);
  not not_29 (not_29_out, F5);
  not not_30 (not_30_out, F4);
  not not_31 (not_31_out, F3);
  not not_32 (not_32_out, F2);
  not not_33 (not_33_out, F0);
  not not_34 (not_34_out, OP5);
  not not_35 (not_35_out, OP4);
  not not_36 (not_36_out, OP3);
  not not_37 (not_37_out, OP2);
  not not_38 (not_38_out, OP1);
  not not_39 (not_39_out, OP0);
  not not_40 (not_40_out, F4);
  not not_41 (not_41_out, F3);
  not not_42 (not_42_out, F2);
  not not_43 (not_43_out, F1);
  not not_44 (not_44_out, F0);
  not not_45 (not_45_out, OP5);
  not not_46 (not_46_out, OP4);
  not not_47 (not_47_out, OP3);
  not not_48 (not_48_out, OP2);
  not not_49 (not_49_out, OP1);
  not not_50 (not_50_out, OP0);
  not not_51 (not_51_out, F4);
  not not_52 (not_52_out, F3);
  not not_53 (not_53_out, F2);
  not not_54 (not_54_out, F1);
  not not_55 (not_55_out, OP5);
  not not_56 (not_56_out, OP4);
  not not_57 (not_57_out, OP3);
  not not_58 (not_58_out, OP2);
  not not_59 (not_59_out, OP1);
  not not_60 (not_60_out, OP0);
  not not_61 (not_61_out, F4);
  not not_62 (not_62_out, F3);
  not not_63 (not_63_out, F2);
  not not_64 (not_64_out, F0);
  not not_65 (not_65_out, OP5);
  not not_66 (not_66_out, OP4);
  not not_67 (not_67_out, OP3);
  not not_68 (not_68_out, OP2);
  not not_69 (not_69_out, OP1);
  not not_70 (not_70_out, OP0);
  not not_71 (not_71_out, F4);
  not not_72 (not_72_out, F3);
  not not_73 (not_73_out, F1);
  not not_74 (not_74_out, F0);
  not not_75 (not_75_out, OP5);
  not not_76 (not_76_out, OP4);
  not not_77 (not_77_out, OP3);
  not not_78 (not_78_out, OP2);
  not not_79 (not_79_out, OP1);
  not not_80 (not_80_out, OP0);
  not not_81 (not_81_out, F4);
  not not_82 (not_82_out, F3);
  not not_83 (not_83_out, F1);
  not not_84 (not_84_out, OP5);
  not not_85 (not_85_out, OP4);
  not not_86 (not_86_out, OP3);
  not not_87 (not_87_out, OP2);
  not not_88 (not_88_out, OP1);
  not not_89 (not_89_out, OP0);
  not not_90 (not_90_out, F4);
  not not_91 (not_91_out, F3);
  not not_92 (not_92_out, OP5);
  not not_93 (not_93_out, OP4);
  not not_94 (not_94_out, OP3);
  not not_95 (not_95_out, OP2);
  not not_96 (not_96_out, OP1);
  not not_97 (not_97_out, OP0);
  not not_98 (not_98_out, F4);
  not not_99 (not_99_out, F2);
  not not_100 (not_100_out, F0);
  not not_101 (not_101_out, OP5);
  not not_102 (not_102_out, OP4);
  not not_103 (not_103_out, OP3);
  not not_104 (not_104_out, OP2);
  not not_105 (not_105_out, OP1);
  not not_106 (not_106_out, OP0);
  not not_107 (not_107_out, F4);
  not not_108 (not_108_out, F2);
  not not_109 (not_109_out, OP5);
  not not_110 (not_110_out, OP4);
  not not_111 (not_111_out, OP3);
  not not_112 (not_112_out, OP2);
  not not_113 (not_113_out, OP5);
  not not_114 (not_114_out, OP4);
  not not_115 (not_115_out, OP2);
  not not_116 (not_116_out, OP1);
  not not_117 (not_117_out, OP0);
  not not_118 (not_118_out, OP5);
  not not_119 (not_119_out, OP4);
  not not_120 (not_120_out, OP1);
  not not_121 (not_121_out, OP0);
  not not_122 (not_122_out, OP5);
  not not_123 (not_123_out, OP4);
  not not_124 (not_124_out, OP2);
  not not_125 (not_125_out, OP1);
  not not_126 (not_126_out, OP5);
  not not_127 (not_127_out, OP4);
  not not_128 (not_128_out, OP2);
  not not_129 (not_129_out, OP0);
  not not_130 (not_130_out, OP5);
  not not_131 (not_131_out, OP4);
  not not_132 (not_132_out, OP1);
  not not_133 (not_133_out, OP5);
  not not_134 (not_134_out, OP4);
  not not_135 (not_135_out, OP3);
  not not_136 (not_136_out, OP2);
  not not_137 (not_137_out, OP1);
  not not_138 (not_138_out, OP0);
  not not_139 (not_139_out, F5);
  not not_140 (not_140_out, F4);
  not not_141 (not_141_out, F3);
  not not_142 (not_142_out, OP5);
  not not_143 (not_143_out, OP4);
  not not_144 (not_144_out, OP3);
  not not_145 (not_145_out, OP2);
  not not_146 (not_146_out, OP1);
  not not_147 (not_147_out, OP0);
  not not_148 (not_148_out, F5);
  not not_149 (not_149_out, F4);
  not not_150 (not_150_out, F3);
  not not_151 (not_151_out, F0);
  not not_152 (not_152_out, OP4);
  not not_153 (not_153_out, OP3);
  not not_154 (not_154_out, OP2);
  not not_155 (not_155_out, OP4);
  not not_156 (not_156_out, OP3);
  not not_157 (not_157_out, OP2);
  not not_158 (not_158_out, OP1);
  and and_1 (and_1_out, not_1_out, not_2_out, not_3_out, not_4_out, not_5_out, not_6_out, not_7_out, not_8_out, not_9_out, not_10_out, not_11_out, not_12_out);
  and and_2 (and_2_out, not_13_out, not_14_out, not_15_out, not_16_out, not_17_out, not_18_out, not_19_out, not_20_out, not_21_out, not_22_out, F1, F0);
  and and_3 (and_3_out, not_23_out, not_24_out, not_25_out, not_26_out, not_27_out, not_28_out, not_29_out, not_30_out, not_31_out, not_32_out, F1, not_33_out);
  and and_4 (and_4_out, not_34_out, not_35_out, not_36_out, not_37_out, not_38_out, not_39_out, F5, not_40_out, not_41_out, not_42_out, not_43_out, not_44_out);
  and and_5 (and_5_out, not_45_out, not_46_out, not_47_out, not_48_out, not_49_out, not_50_out, F5, not_51_out, not_52_out, not_53_out, not_54_out, F0);
  and and_6 (and_6_out, not_55_out, not_56_out, not_57_out, not_58_out, not_59_out, not_60_out, F5, not_61_out, not_62_out, not_63_out, F1, not_64_out);
  and and_7 (and_7_out, not_65_out, not_66_out, not_67_out, not_68_out, not_69_out, not_70_out, F5, not_71_out, not_72_out, F2, not_73_out, not_74_out);
  and and_8 (and_8_out, not_75_out, not_76_out, not_77_out, not_78_out, not_79_out, not_80_out, F5, not_81_out, not_82_out, F2, not_83_out, F0);
  and and_9 (and_9_out, not_84_out, not_85_out, not_86_out, not_87_out, not_88_out, not_89_out, F5, not_90_out, not_91_out, F2, F1, F0);
  and and_10 (and_10_out, not_92_out, not_93_out, not_94_out, not_95_out, not_96_out, not_97_out, F5, not_98_out, F3, not_99_out, F1, not_100_out);
  and and_11 (and_11_out, not_101_out, not_102_out, not_103_out, not_104_out, not_105_out, not_106_out, F5, not_107_out, F3, not_108_out, F1, F0);
  and and_12 (and_12_out, not_109_out, not_110_out, not_111_out, not_112_out, OP1, OP0);
  and and_13 (and_13_out, not_113_out, not_114_out, OP3, not_115_out, not_116_out, not_117_out);
  and and_14 (and_14_out, not_118_out, not_119_out, OP3, OP2, not_120_out, not_121_out);
  and and_15 (and_15_out, not_122_out, not_123_out, OP3, not_124_out, not_125_out, OP0);
  and and_16 (and_16_out, not_126_out, not_127_out, OP3, not_128_out, OP1, not_129_out);
  and and_17 (and_17_out, not_130_out, not_131_out, OP3, OP2, not_132_out, OP0);
  and and_18 (and_18_out, not_133_out, not_134_out, not_135_out, not_136_out, not_137_out, not_138_out, not_139_out, not_140_out, not_141_out, F2, F1, F0);
  and and_19 (and_19_out, not_142_out, not_143_out, not_144_out, not_145_out, not_146_out, not_147_out, not_148_out, not_149_out, not_150_out, F2, F1, not_151_out);
  and and_20 (and_20_out, OP5, not_152_out, not_153_out, not_154_out, OP1, OP0);
  and and_21 (and_21_out, OP5, not_155_out, not_156_out, not_157_out, not_158_out, OP0);
  or or_1 (WBMemData, and_20_out, and_21_out);
  or or_2 (WBAluResult, and_1_out, and_2_out, and_3_out, and_4_out, and_5_out, and_6_out, and_7_out, and_8_out, and_9_out, and_10_out, and_11_out, and_12_out, and_13_out, and_14_out, and_15_out, and_16_out, and_17_out, and_18_out, and_19_out);
endmodule

module \重定向forward  (
  input  [5:0] MEM_OP,
  input  [5:0] MEM_Func,
  input  [5:0] WB_OP,
  input  [5:0] WB_Func,
  input  [5:0] EX_OP,
  input  [5:0] EX_Func,
  input  [4:0] WB_WriteReg_num,
  input  WB_RegWrite,
  input  [4:0] ID_R1_num,
  input  [4:0] ID_R2_num,
  input  [4:0] MEM_WriteReg_num,
  input  MEM_RegWrite,
  output [1:0] R1_Forward,
  output [1:0] R2_Forward
);

  wire and_1_out, and_2_out, and_3_out, and_4_out, and_5_out, and_6_out, comparator_1_eq, comparator_2_eq,
       comparator_3_eq, MEMAlu, not_1_out, not_2_out, not_3_out, or_1_out, or_2_out, \r1_WB数据相关 , \r1数据相关 ,
       \r2_WB数据相关 , \r2数据相关 , WBAlu;

  \重定向MEMtoEX  \u_重定向memtoex_1  (
    .OP0(MEM_OP[0]), .OP1(MEM_OP[1]), .OP2(MEM_OP[2]), .OP3(MEM_OP[3]), .OP4(MEM_OP[4]), .OP5(MEM_OP[5]),
    .F0(MEM_Func[0]), .F1(MEM_Func[1]), .F2(MEM_Func[2]), .F3(MEM_Func[3]), .F4(MEM_Func[4]),
    .F5(MEM_Func[5]), .MemAluResult(MEMAlu));
  \重定向WBtoEX  \u_重定向wbtoex_1  (
    .OP0(WB_OP[0]), .OP1(WB_OP[1]), .OP2(WB_OP[2]), .OP3(WB_OP[3]), .OP4(WB_OP[4]), .OP5(WB_OP[5]),
    .F0(WB_Func[0]), .F1(WB_Func[1]), .F2(WB_Func[2]), .F3(WB_Func[3]), .F4(WB_Func[4]), .F5(WB_Func[5]),
    .WBAluResult(WBAlu));  // open: WBMemData
  \重定向数据相关检测  \u_重定向数据相关检测_1  (
    .OP(EX_OP), .WB_WriteReg_num(WB_WriteReg_num), .WB_RegWrite(WB_RegWrite),
    .MEM_WriteReg_num(MEM_WriteReg_num), .MEM_RegWrite(MEM_RegWrite), .Func(EX_Func), .ID_R1_num(ID_R1_num),
    .ID_R2_num(ID_R2_num), .\R1数据相关 (\r1数据相关 ), .\R2数据相关 (\r2数据相关 ), .\R1_WB数据相关 (\r1_WB数据相关 ),
    .\R2_WB数据相关 (\r2_WB数据相关 ));
  Comparator #(.width(5)) comparator_1 (
    .a(WB_WriteReg_num), .b(MEM_WriteReg_num), .eq(comparator_1_eq));  // open: gt, lt
  Comparator #(.width(5)) comparator_2 (.a(ID_R2_num), .b(MEM_WriteReg_num), .eq(comparator_2_eq));  // open: gt, lt
  Comparator #(.width(5)) comparator_3 (.a(WB_WriteReg_num), .b(ID_R2_num), .eq(comparator_3_eq));  // open: gt, lt
  not not_1 (not_1_out, \r2_WB数据相关 );
  and and_1 (and_1_out, comparator_1_eq, comparator_2_eq, comparator_3_eq);
  not not_2 (not_2_out, \r1_WB数据相关 );
  and and_2 (and_2_out, MEMAlu, not_1_out);
  and and_3 (and_3_out, WBAlu, \r2_WB数据相关 );
  and and_4 (and_4_out, and_1_out, \r2数据相关 );
  and and_5 (and_5_out, MEMAlu, not_2_out);
  and and_6 (and_6_out, WBAlu, \r1_WB数据相关 );
  not not_3 (not_3_out, and_4_out);
  or or_1 (or_1_out, and_2_out, and_3_out);
  or or_2 (or_2_out, and_5_out, and_6_out);
  and and_7 (R2_Forward[0], or_1_out, \r2数据相关 );
  and and_8 (R2_Forward[1], \r2数据相关 , not_3_out, \r2_WB数据相关 );
  and and_9 (R1_Forward[0], or_2_out, \r1数据相关 );
  and and_10 (R1_Forward[1], \r1数据相关 , \r1_WB数据相关 );
  // Probe on R2_Forward
  // Probe on R1_Forward
endmodule
module \重定向源寄存器使用情况  (
  input  OP0,
  input  OP1,
  input  OP2,
  input  OP3,
  input  OP4,
  input  OP5,
  input  F0,
  input  F1,
  input  F2,
  input  F3,
  input  F4,
  input  F5,
  output R1_Used,
  output R2_Used
);

  wire and_1_out, and_2_out, and_3_out, and_4_out, and_5_out, and_6_out, and_7_out, and_8_out, and_9_out,
       and_10_out, and_11_out, and_12_out, and_13_out, and_14_out, and_15_out, and_16_out, and_17_out,
       and_18_out, and_19_out, and_20_out, and_21_out, and_22_out, and_23_out, and_24_out, and_25_out,
       and_26_out, and_27_out, and_28_out, and_29_out, and_30_out, and_31_out, and_32_out, and_33_out,
       and_34_out, and_35_out, and_36_out, and_37_out, and_38_out, not_1_out, not_2_out, not_3_out,
       not_4_out, not_5_out, not_6_out, not_7_out, not_8_out, not_9_out, not_10_out, not_11_out, not_12_out,
       not_13_out, not_14_out, not_15_out, not_16_out, not_17_out, not_18_out, not_19_out, not_20_out,
       not_21_out, not_22_out, not_23_out, not_24_out, not_25_out, not_26_out, not_27_out, not_28_out,
       not_29_out, not_30_out, not_31_out, not_32_out, not_33_out, not_34_out, not_35_out, not_36_out,
       not_37_out, not_38_out, not_39_out, not_40_out, not_41_out, not_42_out, not_43_out, not_44_out,
       not_45_out, not_46_out, not_47_out, not_48_out, not_49_out, not_50_out, not_51_out, not_52_out,
       not_53_out, not_54_out, not_55_out, not_56_out, not_57_out, not_58_out, not_59_out, not_60_out,
       not_61_out, not_62_out, not_63_out, not_64_out, not_65_out, not_66_out, not_67_out, not_68_out,
       not_69_out, not_70_out, not_71_out, not_72_out, not_73_out, not_74_out, not_75_out, not_76_out,
       not_77_out, not_78_out, not_79_out, not_80_out, not_81_out, not_82_out, not_83_out, not_84_out,
       not_85_out, not_86_out, not_87_out, not_88_out, not_89_out, not_90_out, not_91_out, not_92_out,
       not_93_out, not_94_out, not_95_out, not_96_out, not_97_out, not_98_out, not_99_out, not_100_out,
       not_101_out, not_102_out, not_103_out, not_104_out, not_105_out, not_106_out, not_107_out,
       not_108_out, not_109_out, not_110_out, not_111_out, not_112_out, not_113_out, not_114_out,
       not_115_out, not_116_out, not_117_out, not_118_out, not_119_out, not_120_out, not_121_out,
       not_122_out, not_123_out, not_124_out, not_125_out, not_126_out, not_127_out, not_128_out,
       not_129_out, not_130_out, not_131_out, not_132_out, not_133_out, not_134_out, not_135_out,
       not_136_out, not_137_out, not_138_out, not_139_out, not_140_out, not_141_out, not_142_out,
       not_143_out, not_144_out, not_145_out, not_146_out, not_147_out, not_148_out, not_149_out,
       not_150_out, not_151_out, not_152_out, not_153_out, not_154_out, not_155_out, not_156_out,
       not_157_out, not_158_out, not_159_out, not_160_out, not_161_out, not_162_out, not_163_out,
       not_164_out, not_165_out, not_166_out, not_167_out, not_168_out, not_169_out, not_170_out,
       not_171_out, not_172_out, not_173_out, not_174_out, not_175_out, not_176_out, not_177_out,
       not_178_out, not_179_out, not_180_out, not_181_out, not_182_out, not_183_out, not_184_out,
       not_185_out, not_186_out, not_187_out, not_188_out, not_189_out, not_190_out, not_191_out,
       not_192_out, not_193_out, not_194_out, not_195_out, not_196_out, not_197_out, not_198_out,
       not_199_out, not_200_out, not_201_out, not_202_out, not_203_out, not_204_out, not_205_out,
       not_206_out, not_207_out, not_208_out, not_209_out, not_210_out, not_211_out, not_212_out,
       not_213_out, not_214_out, not_215_out, not_216_out, not_217_out, not_218_out, not_219_out,
       not_220_out, not_221_out, not_222_out, not_223_out, not_224_out, not_225_out, not_226_out,
       not_227_out, not_228_out, not_229_out, not_230_out, not_231_out, not_232_out, not_233_out,
       not_234_out, not_235_out, not_236_out, not_237_out, not_238_out, not_239_out, not_240_out,
       not_241_out, not_242_out, not_243_out, not_244_out, not_245_out, not_246_out, not_247_out,
       not_248_out, not_249_out, not_250_out, not_251_out, not_252_out, not_253_out, not_254_out,
       not_255_out, not_256_out, not_257_out, not_258_out, not_259_out, not_260_out, not_261_out,
       not_262_out, not_263_out, not_264_out, not_265_out, not_266_out, not_267_out, not_268_out,
       not_269_out, not_270_out, not_271_out, not_272_out, not_273_out, not_274_out, not_275_out,
       not_276_out, not_277_out, not_278_out, not_279_out, not_280_out, not_281_out, not_282_out,
       not_283_out, not_284_out, not_285_out, not_286_out, not_287_out, not_288_out, not_289_out,
       not_290_out, not_291_out, not_292_out, not_293_out, not_294_out, not_295_out, not_296_out,
       not_297_out, not_298_out, not_299_out, not_300_out, not_301_out;

  not not_1 (not_1_out, OP5);
  not not_2 (not_2_out, OP4);
  not not_3 (not_3_out, OP3);
  not not_4 (not_4_out, OP2);
  not not_5 (not_5_out, OP1);
  not not_6 (not_6_out, OP0);
  not not_7 (not_7_out, F4);
  not not_8 (not_8_out, F3);
  not not_9 (not_9_out, F2);
  not not_10 (not_10_out, F1);
  not not_11 (not_11_out, F0);
  not not_12 (not_12_out, OP5);
  not not_13 (not_13_out, OP4);
  not not_14 (not_14_out, OP3);
  not not_15 (not_15_out, OP2);
  not not_16 (not_16_out, OP1);
  not not_17 (not_17_out, OP0);
  not not_18 (not_18_out, F4);
  not not_19 (not_19_out, F3);
  not not_20 (not_20_out, F2);
  not not_21 (not_21_out, F1);
  not not_22 (not_22_out, OP5);
  not not_23 (not_23_out, OP4);
  not not_24 (not_24_out, OP3);
  not not_25 (not_25_out, OP2);
  not not_26 (not_26_out, OP1);
  not not_27 (not_27_out, OP0);
  not not_28 (not_28_out, F4);
  not not_29 (not_29_out, F3);
  not not_30 (not_30_out, F2);
  not not_31 (not_31_out, F0);
  not not_32 (not_32_out, OP5);
  not not_33 (not_33_out, OP4);
  not not_34 (not_34_out, OP3);
  not not_35 (not_35_out, OP2);
  not not_36 (not_36_out, OP1);
  not not_37 (not_37_out, OP0);
  not not_38 (not_38_out, F4);
  not not_39 (not_39_out, F3);
  not not_40 (not_40_out, F1);
  not not_41 (not_41_out, F0);
  not not_42 (not_42_out, OP5);
  not not_43 (not_43_out, OP4);
  not not_44 (not_44_out, OP3);
  not not_45 (not_45_out, OP2);
  not not_46 (not_46_out, OP1);
  not not_47 (not_47_out, OP0);
  not not_48 (not_48_out, F4);
  not not_49 (not_49_out, F3);
  not not_50 (not_50_out, F1);
  not not_51 (not_51_out, OP5);
  not not_52 (not_52_out, OP4);
  not not_53 (not_53_out, OP3);
  not not_54 (not_54_out, OP2);
  not not_55 (not_55_out, OP1);
  not not_56 (not_56_out, OP0);
  not not_57 (not_57_out, F4);
  not not_58 (not_58_out, F3);
  not not_59 (not_59_out, OP5);
  not not_60 (not_60_out, OP4);
  not not_61 (not_61_out, OP3);
  not not_62 (not_62_out, OP2);
  not not_63 (not_63_out, OP1);
  not not_64 (not_64_out, OP0);
  not not_65 (not_65_out, F4);
  not not_66 (not_66_out, F2);
  not not_67 (not_67_out, F0);
  not not_68 (not_68_out, OP5);
  not not_69 (not_69_out, OP4);
  not not_70 (not_70_out, OP3);
  not not_71 (not_71_out, OP2);
  not not_72 (not_72_out, OP1);
  not not_73 (not_73_out, OP0);
  not not_74 (not_74_out, F4);
  not not_75 (not_75_out, F2);
  not not_76 (not_76_out, OP5);
  not not_77 (not_77_out, OP4);
  not not_78 (not_78_out, OP3);
  not not_79 (not_79_out, OP2);
  not not_80 (not_80_out, OP1);
  not not_81 (not_81_out, OP0);
  not not_82 (not_82_out, F5);
  not not_83 (not_83_out, F4);
  not not_84 (not_84_out, F2);
  not not_85 (not_85_out, F1);
  not not_86 (not_86_out, F0);
  not not_87 (not_87_out, OP5);
  not not_88 (not_88_out, OP4);
  not not_89 (not_89_out, OP3);
  not not_90 (not_90_out, OP2);
  not not_91 (not_91_out, OP1);
  not not_92 (not_92_out, OP0);
  not not_93 (not_93_out, F5);
  not not_94 (not_94_out, F4);
  not not_95 (not_95_out, F1);
  not not_96 (not_96_out, F0);
  not not_97 (not_97_out, OP5);
  not not_98 (not_98_out, OP4);
  not not_99 (not_99_out, OP3);
  not not_100 (not_100_out, OP1);
  not not_101 (not_101_out, OP0);
  not not_102 (not_102_out, OP5);
  not not_103 (not_103_out, OP4);
  not not_104 (not_104_out, OP3);
  not not_105 (not_105_out, OP1);
  not not_106 (not_106_out, OP5);
  not not_107 (not_107_out, OP4);
  not not_108 (not_108_out, OP2);
  not not_109 (not_109_out, OP1);
  not not_110 (not_110_out, OP0);
  not not_111 (not_111_out, OP5);
  not not_112 (not_112_out, OP4);
  not not_113 (not_113_out, OP1);
  not not_114 (not_114_out, OP0);
  not not_115 (not_115_out, OP5);
  not not_116 (not_116_out, OP4);
  not not_117 (not_117_out, OP2);
  not not_118 (not_118_out, OP1);
  not not_119 (not_119_out, OP5);
  not not_120 (not_120_out, OP4);
  not not_121 (not_121_out, OP2);
  not not_122 (not_122_out, OP0);
  not not_123 (not_123_out, OP5);
  not not_124 (not_124_out, OP4);
  not not_125 (not_125_out, OP1);
  not not_126 (not_126_out, OP4);
  not not_127 (not_127_out, OP3);
  not not_128 (not_128_out, OP2);
  not not_129 (not_129_out, OP5);
  not not_130 (not_130_out, OP4);
  not not_131 (not_131_out, OP3);
  not not_132 (not_132_out, OP2);
  not not_133 (not_133_out, OP1);
  not not_134 (not_134_out, OP0);
  not not_135 (not_135_out, F5);
  not not_136 (not_136_out, F4);
  not not_137 (not_137_out, F3);
  not not_138 (not_138_out, OP5);
  not not_139 (not_139_out, OP4);
  not not_140 (not_140_out, OP3);
  not not_141 (not_141_out, OP2);
  not not_142 (not_142_out, OP1);
  not not_143 (not_143_out, OP0);
  not not_144 (not_144_out, F5);
  not not_145 (not_145_out, F4);
  not not_146 (not_146_out, F3);
  not not_147 (not_147_out, F0);
  not not_148 (not_148_out, OP5);
  not not_149 (not_149_out, OP4);
  not not_150 (not_150_out, OP3);
  not not_151 (not_151_out, OP0);
  not not_152 (not_152_out, OP5);
  not not_153 (not_153_out, OP4);
  not not_154 (not_154_out, OP3);
  not not_155 (not_155_out, OP2);
  not not_156 (not_156_out, OP1);
  not not_157 (not_157_out, OP0);
  not not_158 (not_158_out, F5);
  not not_159 (not_159_out, F4);
  not not_160 (not_160_out, F3);
  not not_161 (not_161_out, F2);
  not not_162 (not_162_out, F1);
  not not_163 (not_163_out, F0);
  not not_164 (not_164_out, OP5);
  not not_165 (not_165_out, OP4);
  not not_166 (not_166_out, OP3);
  not not_167 (not_167_out, OP2);
  not not_168 (not_168_out, OP1);
  not not_169 (not_169_out, OP0);
  not not_170 (not_170_out, F5);
  not not_171 (not_171_out, F4);
  not not_172 (not_172_out, F3);
  not not_173 (not_173_out, F2);
  not not_174 (not_174_out, OP5);
  not not_175 (not_175_out, OP4);
  not not_176 (not_176_out, OP3);
  not not_177 (not_177_out, OP2);
  not not_178 (not_178_out, OP1);
  not not_179 (not_179_out, OP0);
  not not_180 (not_180_out, F5);
  not not_181 (not_181_out, F4);
  not not_182 (not_182_out, F3);
  not not_183 (not_183_out, F2);
  not not_184 (not_184_out, F0);
  not not_185 (not_185_out, OP5);
  not not_186 (not_186_out, OP4);
  not not_187 (not_187_out, OP3);
  not not_188 (not_188_out, OP2);
  not not_189 (not_189_out, OP1);
  not not_190 (not_190_out, OP0);
  not not_191 (not_191_out, F4);
  not not_192 (not_192_out, F3);
  not not_193 (not_193_out, F2);
  not not_194 (not_194_out, F1);
  not not_195 (not_195_out, F0);
  not not_196 (not_196_out, OP5);
  not not_197 (not_197_out, OP4);
  not not_198 (not_198_out, OP3);
  not not_199 (not_199_out, OP2);
  not not_200 (not_200_out, OP1);
  not not_201 (not_201_out, OP0);
  not not_202 (not_202_out, F4);
  not not_203 (not_203_out, F3);
  not not_204 (not_204_out, F2);
  not not_205 (not_205_out, F1);
  not not_206 (not_206_out, OP5);
  not not_207 (not_207_out, OP4);
  not not_208 (not_208_out, OP3);
  not not_209 (not_209_out, OP2);
  not not_210 (not_210_out, OP1);
  not not_211 (not_211_out, OP0);
  not not_212 (not_212_out, F4);
  not not_213 (not_213_out, F3);
  not not_214 (not_214_out, F2);
  not not_215 (not_215_out, F0);
  not not_216 (not_216_out, OP5);
  not not_217 (not_217_out, OP4);
  not not_218 (not_218_out, OP3);
  not not_219 (not_219_out, OP2);
  not not_220 (not_220_out, OP1);
  not not_221 (not_221_out, OP0);
  not not_222 (not_222_out, F4);
  not not_223 (not_223_out, F3);
  not not_224 (not_224_out, F1);
  not not_225 (not_225_out, F0);
  not not_226 (not_226_out, OP5);
  not not_227 (not_227_out, OP4);
  not not_228 (not_228_out, OP3);
  not not_229 (not_229_out, OP2);
  not not_230 (not_230_out, OP1);
  not not_231 (not_231_out, OP0);
  not not_232 (not_232_out, F4);
  not not_233 (not_233_out, F3);
  not not_234 (not_234_out, F1);
  not not_235 (not_235_out, OP5);
  not not_236 (not_236_out, OP4);
  not not_237 (not_237_out, OP3);
  not not_238 (not_238_out, OP2);
  not not_239 (not_239_out, OP1);
  not not_240 (not_240_out, OP0);
  not not_241 (not_241_out, F4);
  not not_242 (not_242_out, F3);
  not not_243 (not_243_out, OP5);
  not not_244 (not_244_out, OP4);
  not not_245 (not_245_out, OP3);
  not not_246 (not_246_out, OP2);
  not not_247 (not_247_out, OP1);
  not not_248 (not_248_out, OP0);
  not not_249 (not_249_out, F4);
  not not_250 (not_250_out, F2);
  not not_251 (not_251_out, F0);
  not not_252 (not_252_out, OP5);
  not not_253 (not_253_out, OP4);
  not not_254 (not_254_out, OP3);
  not not_255 (not_255_out, OP2);
  not not_256 (not_256_out, OP1);
  not not_257 (not_257_out, OP0);
  not not_258 (not_258_out, F4);
  not not_259 (not_259_out, F2);
  not not_260 (not_260_out, OP5);
  not not_261 (not_261_out, OP4);
  not not_262 (not_262_out, OP3);
  not not_263 (not_263_out, OP2);
  not not_264 (not_264_out, OP1);
  not not_265 (not_265_out, OP0);
  not not_266 (not_266_out, F5);
  not not_267 (not_267_out, F4);
  not not_268 (not_268_out, F1);
  not not_269 (not_269_out, F0);
  not not_270 (not_270_out, OP5);
  not not_271 (not_271_out, OP4);
  not not_272 (not_272_out, OP3);
  not not_273 (not_273_out, OP1);
  not not_274 (not_274_out, OP0);
  not not_275 (not_275_out, OP5);
  not not_276 (not_276_out, OP4);
  not not_277 (not_277_out, OP3);
  not not_278 (not_278_out, OP1);
  not not_279 (not_279_out, OP5);
  not not_280 (not_280_out, OP4);
  not not_281 (not_281_out, OP3);
  not not_282 (not_282_out, OP2);
  not not_283 (not_283_out, OP1);
  not not_284 (not_284_out, OP0);
  not not_285 (not_285_out, F5);
  not not_286 (not_286_out, F4);
  not not_287 (not_287_out, F3);
  not not_288 (not_288_out, OP5);
  not not_289 (not_289_out, OP4);
  not not_290 (not_290_out, OP3);
  not not_291 (not_291_out, OP2);
  not not_292 (not_292_out, OP1);
  not not_293 (not_293_out, OP0);
  not not_294 (not_294_out, F5);
  not not_295 (not_295_out, F4);
  not not_296 (not_296_out, F3);
  not not_297 (not_297_out, F0);
  not not_298 (not_298_out, OP5);
  not not_299 (not_299_out, OP4);
  not not_300 (not_300_out, OP3);
  not not_301 (not_301_out, OP0);
  and and_1 (and_1_out, not_1_out, not_2_out, not_3_out, not_4_out, not_5_out, not_6_out, F5, not_7_out, not_8_out, not_9_out, not_10_out, not_11_out);
  and and_2 (and_2_out, not_12_out, not_13_out, not_14_out, not_15_out, not_16_out, not_17_out, F5, not_18_out, not_19_out, not_20_out, not_21_out, F0);
  and and_3 (and_3_out, not_22_out, not_23_out, not_24_out, not_25_out, not_26_out, not_27_out, F5, not_28_out, not_29_out, not_30_out, F1, not_31_out);
  and and_4 (and_4_out, not_32_out, not_33_out, not_34_out, not_35_out, not_36_out, not_37_out, F5, not_38_out, not_39_out, F2, not_40_out, not_41_out);
  and and_5 (and_5_out, not_42_out, not_43_out, not_44_out, not_45_out, not_46_out, not_47_out, F5, not_48_out, not_49_out, F2, not_50_out, F0);
  and and_6 (and_6_out, not_51_out, not_52_out, not_53_out, not_54_out, not_55_out, not_56_out, F5, not_57_out, not_58_out, F2, F1, F0);
  and and_7 (and_7_out, not_59_out, not_60_out, not_61_out, not_62_out, not_63_out, not_64_out, F5, not_65_out, F3, not_66_out, F1, not_67_out);
  and and_8 (and_8_out, not_68_out, not_69_out, not_70_out, not_71_out, not_72_out, not_73_out, F5, not_74_out, F3, not_75_out, F1, F0);
  and and_9 (and_9_out, not_76_out, not_77_out, not_78_out, not_79_out, not_80_out, not_81_out, not_82_out, not_83_out, F3, not_84_out, not_85_out, not_86_out);
  and and_10 (and_10_out, not_87_out, not_88_out, not_89_out, not_90_out, not_91_out, not_92_out, not_93_out, not_94_out, F3, F2, not_95_out, not_96_out);
  and and_11 (and_11_out, not_97_out, not_98_out, not_99_out, OP2, not_100_out, not_101_out);
  and and_12 (and_12_out, not_102_out, not_103_out, not_104_out, OP2, not_105_out, OP0);
  and and_13 (and_13_out, not_106_out, not_107_out, OP3, not_108_out, not_109_out, not_110_out);
  and and_14 (and_14_out, not_111_out, not_112_out, OP3, OP2, not_113_out, not_114_out);
  and and_15 (and_15_out, not_115_out, not_116_out, OP3, not_117_out, not_118_out, OP0);
  and and_16 (and_16_out, not_119_out, not_120_out, OP3, not_121_out, OP1, not_122_out);
  and and_17 (and_17_out, not_123_out, not_124_out, OP3, OP2, not_125_out, OP0);
  and and_18 (and_18_out, OP5, not_126_out, not_127_out, not_128_out, OP1, OP0);
  and and_19 (and_19_out, not_129_out, not_130_out, not_131_out, not_132_out, not_133_out, not_134_out, not_135_out, not_136_out, not_137_out, F2, F1, F0);
  and and_20 (and_20_out, not_138_out, not_139_out, not_140_out, not_141_out, not_142_out, not_143_out, not_144_out, not_145_out, not_146_out, F2, F1, not_147_out);
  and and_21 (and_21_out, not_148_out, not_149_out, not_150_out, OP2, OP1, not_151_out);
  and and_22 (and_22_out, not_152_out, not_153_out, not_154_out, not_155_out, not_156_out, not_157_out, not_158_out, not_159_out, not_160_out, not_161_out, not_162_out, not_163_out);
  and and_23 (and_23_out, not_164_out, not_165_out, not_166_out, not_167_out, not_168_out, not_169_out, not_170_out, not_171_out, not_172_out, not_173_out, F1, F0);
  and and_24 (and_24_out, not_174_out, not_175_out, not_176_out, not_177_out, not_178_out, not_179_out, not_180_out, not_181_out, not_182_out, not_183_out, F1, not_184_out);
  and and_25 (and_25_out, not_185_out, not_186_out, not_187_out, not_188_out, not_189_out, not_190_out, F5, not_191_out, not_192_out, not_193_out, not_194_out, not_195_out);
  and and_26 (and_26_out, not_196_out, not_197_out, not_198_out, not_199_out, not_200_out, not_201_out, F5, not_202_out, not_203_out, not_204_out, not_205_out, F0);
  and and_27 (and_27_out, not_206_out, not_207_out, not_208_out, not_209_out, not_210_out, not_211_out, F5, not_212_out, not_213_out, not_214_out, F1, not_215_out);
  and and_28 (and_28_out, not_216_out, not_217_out, not_218_out, not_219_out, not_220_out, not_221_out, F5, not_222_out, not_223_out, F2, not_224_out, not_225_out);
  and and_29 (and_29_out, not_226_out, not_227_out, not_228_out, not_229_out, not_230_out, not_231_out, F5, not_232_out, not_233_out, F2, not_234_out, F0);
  and and_30 (and_30_out, not_235_out, not_236_out, not_237_out, not_238_out, not_239_out, not_240_out, F5, not_241_out, not_242_out, F2, F1, F0);
  and and_31 (and_31_out, not_243_out, not_244_out, not_245_out, not_246_out, not_247_out, not_248_out, F5, not_249_out, F3, not_250_out, F1, not_251_out);
  and and_32 (and_32_out, not_252_out, not_253_out, not_254_out, not_255_out, not_256_out, not_257_out, F5, not_258_out, F3, not_259_out, F1, F0);
  and and_33 (and_33_out, not_260_out, not_261_out, not_262_out, not_263_out, not_264_out, not_265_out, not_266_out, not_267_out, F3, F2, not_268_out, not_269_out);
  and and_34 (and_34_out, not_270_out, not_271_out, not_272_out, OP2, not_273_out, not_274_out);
  and and_35 (and_35_out, not_275_out, not_276_out, not_277_out, OP2, not_278_out, OP0);
  and and_36 (and_36_out, not_279_out, not_280_out, not_281_out, not_282_out, not_283_out, not_284_out, not_285_out, not_286_out, not_287_out, F2, F1, F0);
  and and_37 (and_37_out, not_288_out, not_289_out, not_290_out, not_291_out, not_292_out, not_293_out, not_294_out, not_295_out, not_296_out, F2, F1, not_297_out);
  and and_38 (and_38_out, not_298_out, not_299_out, not_300_out, OP2, OP1, not_301_out);
  or or_1 (R1_Used, and_1_out, and_2_out, and_3_out, and_4_out, and_5_out, and_6_out, and_7_out, and_8_out, and_9_out, and_10_out, and_11_out, and_12_out, and_13_out, and_14_out, and_15_out, and_16_out, and_17_out, and_18_out, and_19_out, and_20_out, and_21_out);
  or or_2 (R2_Used, and_22_out, and_23_out, and_24_out, and_25_out, and_26_out, and_27_out, and_28_out, and_29_out, and_30_out, and_31_out, and_32_out, and_33_out, and_34_out, and_35_out, and_36_out, and_37_out, and_38_out);
endmodule

module \分支预测流水线  (
);

  wire alusrc, and_1_out, and_2_out, and_3_out, and_4_out, and_6_out, and_7_out, and_8_out, B_success, beq,
       bit_extender_5_out, bne, CLK, Ena, EX_jal, EX_lh, ex_mem_1_equal_2, ex_mem_1_jal_2, ex_mem_1_lh_2,
       ex_mem_1_memtoreg_2, ex_mem_1_memwrite_2, ex_mem_1_regdst_2, ex_mem_1_syscall_2, EX_regdst,
       EX_Regwrite, EX_SRAV, EX_SRLV, Fail_Miss, Go, ID_alusrc, ID_BLEZ, id_ex_1_alusrc_2, id_ex_1_beq_2,
       id_ex_1_blez_2, id_ex_1_bne_2, id_ex_1_jmp_2, id_ex_1_jr_2, id_ex_1_memtoreg_2, id_ex_1_memwrite_2,
       id_ex_1_syscall_2, ID_LH, ID_MemToReg, ID_redgdst, ID_regwrite, ID_signedext, ID_SRAV, ID_SRLV, IR1,
       IR2, IR3, J_success, jal, jmp, jr, LH_Address, LoadUse, MEM_Regwrite, mem_wb_1_jal_2,
       mem_wb_1_memtoreg_2, mem_wb_1_regdst_2, MemToReg, Memwrite, mips_alu_1_equal, \n4控制信号_1_alusrc ,
       \n4控制信号_1_memtoreg , \n4控制信号_1_regdst , \n4控制信号_1_regwrite , \n4控制信号_1_signedext , not_1_out,
       not_2_out, not_3_out, not_4_out, not_5_out, or_1_out, or_2_out, or_3_out, or_5_out, or_6_out,
       or_11_out, or_15_out, or_16_out, redgdst, regwrite, RST, SignedExt, syscall, W1, W2, W3, WB_LH,
       WB_regwrite, \分支预测转换电路_1_fail , \分支预测转换电路_1_miss , \分支预测转换电路_1_predict , \分支预测转换电路_1_success ;
  wire [1:0] R1_forward, R2_forward;
  wire [3:0] aluop, ID_aluop, id_ex_1_aluop_2, \n4控制信号_1_alu_op ;
  wire [4:0] ex_mem_1_rd_2, ex_mem_1_rt_2, EX_R1_t, EX_R2, EX_rd, EX_rt, ID_R1, ID_R2, MEM_Regwrite_num,
       mem_wb_1_rd_2, mem_wb_1_rt_2, multiplexer_15_out, multiplexer_16_out, multiplexer_18_out,
       multiplexer_24_out, multiplexer_26_out, shamt, WB_regwrite_num;
  wire [5:0] ID_Func, ID_OP;
  wire [15:0] \LoadUse次数 , multiplexer_23_out, \分支预测转换电路_1_pcout , \命中次数 , \总周期数 , \无条件分支数 , \条件分支成功数 ,
       \预测失败次数 , \预测成功次数 ;
  wire [25:6] IR;
  wire [31:0] adder_2_out, adder_3_out, adder_5_out, Alu_B, Before_PC, bit_extender_1_out,
       bit_extender_2_out, bit_extender_3_out, bit_extender_4_out, bit_extender_6_out, EX_IR, EX_JBPC,
       ex_mem_1_alub_2, EX_PC, EX_R1, id_ex_1_imm_2, id_ex_1_jimm_2, id_ex_1_pc_4_2, id_ex_1_r1_2,
       id_ex_1_r2_2, ID_PC, IF_IR, IF_PC, LedData, MEM_ALUResult, MEM_IR, MEM_PC, mem_wb_1_memdata_2,
       mips_alu_1_result, mips_ram_1_p6, mips_regifile_1_r1, mips_regifile_1_r2, multiplexer_3_out,
       multiplexer_4_out, multiplexer_5_out, multiplexer_7_out, multiplexer_11_out, multiplexer_12_out,
       multiplexer_13_out, multiplexer_14_out, multiplexer_19_out, multiplexer_20_out, multiplexer_22_out,
       next_pc, PC_In, shifter_1_out, shifter_2_out, WB_ALUResult, WB_IR, WB_MEMData, WB_PC;

  Button \u_总复位  (.out(RST));
  Button _1 (.out(IR1));
  Button _2 (.out(IR2));
  Button _3 (.out(IR3));
  Button \u_继续运行  (.out(Go));
  LED led_1 (.in(W1));
  LED led_2 (.in(W2));
  LED led_3 (.in(W3));
  not not_1 (not_1_out, Ena);
  or or_1 (or_1_out, not_1_out, Go);
  not not_2 (not_2_out, LoadUse);
  and and_1 (and_1_out, not_2_out, or_1_out);
  Hex_Digit_Display hex_digit_display_1 (.value(LedData[31:28]));  // open: dp
  Register #(.width(32)) PC (.D(PC_In), .en(and_1_out), .Q(IF_PC), .clk(CLK));  // open: clr
  not not_3 (not_3_out, Go);
  Hex_Digit_Display hex_digit_display_2 (.value(LedData[27:24]));  // open: dp
  Hex_Digit_Display hex_digit_display_3 (.value(LedData[23:20]));  // open: dp
  // Probe on IF_PC
  or or_2 (or_2_out, RST, Fail_Miss);
  Hex_Digit_Display hex_digit_display_4 (.value(LedData[19:16]));  // open: dp
  Hex_Digit_Display hex_digit_display_5 (.value(LedData[15:12]));  // open: dp
  Counter #(.width(16), .max('hffff)) counter_1 (
    .D(\总周期数 ), .count(not_1_out), .Q(\总周期数 ), .clk(CLK), .clr(RST));  // open: load, carry
  Adder #(.width(32)) adder_1 (.a(32'h4), .b(IF_PC), .out(next_pc));  // open: cin, cout
  ROM #(.addrWidth(10), .dataWidth(32)) rom_1 (.addr(IF_PC[11:2]), .data(IF_IR));  // open: sel
  and and_2 (and_2_out, not_3_out, Ena);
  \分支预测转换电路  \u_分支预测转换电路_1  (
    .IR(IF_IR), .pcaddr(IF_PC[15:0]), .clk(CLK), .rst(RST), .pastpc(EX_PC[15:0]),
    .pcaddrmux(Before_PC[15:0]), .pastop(EX_IR[31:26]), .pastfunct(EX_IR[5:0]),
    .predict(\分支预测转换电路_1_predict ), .pcout(\分支预测转换电路_1_pcout ), .success(\分支预测转换电路_1_success ),
    .miss(\分支预测转换电路_1_miss ), .fail(\分支预测转换电路_1_fail ));  // open: pastpredict
  Hex_Digit_Display hex_digit_display_6 (.value(LedData[7:4]));  // open: dp
  Hex_Digit_Display hex_digit_display_7 (.value(LedData[11:8]));  // open: dp
  Clock clock_1 (.out(CLK));
  IF_ID if_id_1 (
    .clk(CLK), .\使能端_低电平有效_stall_高电平有效 (or_3_out), .\同步清零_气泡_高电平有效 (or_2_out), .IR(IF_IR),
    .ir_2({ID_OP, IR, ID_Func}), .PC(IF_PC), .pc_2(ID_PC));  // open: 传输状态Out_表明当前传输数据有效, 传输状态In_表明当前传输数据有效, IF_matchnum, IF_match, IF_matchnum_2, IF_match_2
  or or_3 (or_3_out, LoadUse, and_2_out);
  Hex_Digit_Display hex_digit_display_8 (.value(LedData[3:0]));  // open: dp
  Counter #(.width(16), .max('hffff)) counter_2 (
    .D(\预测失败次数 ), .count(\分支预测转换电路_1_fail ), .Q(\预测失败次数 ), .clk(CLK), .clr(RST));  // open: load, carry
  // Probe on {ID_OP, IR, ID_Func}
  // Probe on \总周期数 
  // Probe on \无条件分支数 
  // Probe on \条件分支成功数 
  // Probe on \LoadUse次数 
  // Probe on \命中次数 
  // Probe on \预测成功次数 
  \硬布线控制器  \u_硬布线控制器_1  (
    .Func(ID_Func), .OP(ID_OP), .ALU_OP(ID_aluop), .MemToReg(ID_MemToReg), .MemWrite(Memwrite),
    .ALU_SRC(ID_alusrc), .RegWrite(ID_regwrite), .SysCALL(syscall), .SignedExt(ID_signedext),
    .RegDst(ID_redgdst), .JR(jr), .JMP(jmp), .Beq(beq), .JAL(jal), .Bne(bne));
  assign bit_extender_1_out = {{6{1'b0}}, {IR, ID_Func}};  // Bit_Extender bit_extender_1
  assign bit_extender_2_out = {{16{IR[15]}}, {IR[15:6], ID_Func}};  // Bit_Extender bit_extender_2
  Adder #(.width(32)) adder_2 (.a(ID_PC), .b(32'h4), .out(adder_2_out));  // open: cin, cout
  // Probe on IF_PC[11:0]
  Multiplexer #(.width(5), .enable("false")) multiplexer_1 (
    .in0(IR[25:21]), .in1(5'b00010), .out(ID_R1), .sel(syscall));
  Multiplexer #(.width(5), .enable("false")) multiplexer_2 (
    .in0(IR[20:16]), .in1(5'b00100), .out(ID_R2), .sel(syscall));
  // Probe on WB_regwrite_num
  Multiplexer #(.width(32), .enable("false")) multiplexer_3 (
    .in0(Before_PC), .in1(next_pc), .out(multiplexer_3_out), .sel(\分支预测转换电路_1_success ));
  // Probe on ID_PC[11:0]
  Shifter #(.width(32)) shifter_1 (.in(bit_extender_1_out), .\dist (5'b00010), .out(shifter_1_out));
  assign bit_extender_3_out = {{16{1'b0}}, {IR[15:6], ID_Func}};  // Bit_Extender bit_extender_3
  // Probe on multiplexer_22_out
  assign bit_extender_4_out = {{16{1'b0}}, \分支预测转换电路_1_pcout };  // Bit_Extender bit_extender_4
  or or_4 (Fail_Miss, \分支预测转换电路_1_miss , \分支预测转换电路_1_fail );
  or or_5 (or_5_out, \分支预测转换电路_1_fail , \分支预测转换电路_1_success );
  // Probe on EX_PC[11:0]
  // Probe on MEM_PC[11:0]
  // Probe on \预测失败次数 
  MIPS_Regifile mips_regifile_1 (
    .Din(multiplexer_22_out), .Clk(CLK), .R1(mips_regifile_1_r1), .R2(mips_regifile_1_r2), .WE(WB_regwrite),
    .W_num(WB_regwrite_num), .R1_num(ID_R1), .R2_num(ID_R2));
  Multiplexer #(.width(32), .enable("false")) multiplexer_4 (
    .in0(multiplexer_3_out), .in1(bit_extender_4_out), .out(multiplexer_4_out), .sel(\分支预测转换电路_1_predict ));
  Counter #(.width(16), .max('hffff)) counter_3 (
    .D(\命中次数 ), .count(or_5_out), .Q(\命中次数 ), .clk(CLK), .clr(RST));  // open: load, carry
  Counter #(.width(16), .max('hffff)) counter_4 (
    .D(\预测成功次数 ), .count(\分支预测转换电路_1_success ), .Q(\预测成功次数 ), .clk(CLK), .clr(RST));  // open: load, carry
  // Probe on WB_PC[11:0]
  Multiplexer #(.width(32), .enable("false")) multiplexer_5 (
    .in0(bit_extender_3_out), .in1(bit_extender_2_out), .out(multiplexer_5_out), .sel(SignedExt));
  Multiplexer #(.width(32), .enable("false")) multiplexer_6 (
    .in0(multiplexer_4_out), .in1(multiplexer_7_out), .out(PC_In), .sel(and_3_out));
  and and_3 (and_3_out, Fail_Miss, ~J_success);  // AND_Gate
  // Probe on {ID_OP, IR, ID_Func}
  Counter #(.width(16), .max('hffff)) counter_5 (
    .D(\无条件分支数 ), .count(J_success), .Q(\无条件分支数 ), .clk(CLK), .clr(RST));  // open: load, carry
  ID_EX id_ex_1 (
    .Memtoreg(MemToReg), .Syscall(syscall), .Bne(bne), .Srlv(ID_SRLV), .Memwrite(Memwrite), .Jr(jr),
    .Srav(ID_SRAV), .Alusrc(alusrc), .Regdst(redgdst), .Jmp(jmp), .Lh(ID_LH), .Regwrite(regwrite), .Beq(beq),
    .Jal(jal), .Blez(ID_BLEZ), .clk(CLK), .\使能端_低电平有效_stall_高电平有效 (and_2_out), .\同步清零_气泡_高电平有效 (or_6_out),
    .IMM(multiplexer_5_out), .IR({ID_OP, IR, ID_Func}), .PC(ID_PC), .memtoreg_2(id_ex_1_memtoreg_2),
    .syscall_2(id_ex_1_syscall_2), .bne_2(id_ex_1_bne_2), .srlv_2(EX_SRLV), .memwrite_2(id_ex_1_memwrite_2),
    .jr_2(id_ex_1_jr_2), .srav_2(EX_SRAV), .alusrc_2(id_ex_1_alusrc_2), .regdst_2(EX_regdst),
    .jmp_2(id_ex_1_jmp_2), .lh_2(EX_lh), .regwrite_2(EX_Regwrite), .beq_2(id_ex_1_beq_2), .jal_2(EX_jal),
    .blez_2(id_ex_1_blez_2), .imm_2(id_ex_1_imm_2), .ir_2(EX_IR), .pc_2(EX_PC), .Aluop(aluop),
    .aluop_2(id_ex_1_aluop_2), .R1(mips_regifile_1_r1), .r1_2(id_ex_1_r1_2), .R2(mips_regifile_1_r2),
    .r2_2(id_ex_1_r2_2), .PC_4(adder_2_out), .PC_4_2(id_ex_1_pc_4_2), .rt(IR[20:16]), .rt_2(EX_rt),
    .rd(IR[15:11]), .rd_2(EX_rd), .shamt(IR[10:6]), .shamt_2(shamt), .Jimm(shifter_1_out),
    .JIMM_2(id_ex_1_jimm_2), .R1_num(ID_R1), .R2_num(ID_R2), .R1_num_2(EX_R1_t), .R2_num_2(EX_R2));  // open: EX_matchnum, EX_match, EX_matchnum_2, EX_match_2
  or or_6 (or_6_out, or_2_out, LoadUse);
  Multiplexer #(.width(32), .enable("false")) multiplexer_7 (
    .in0(adder_3_out), .in1(EX_JBPC), .out(multiplexer_7_out), .sel(B_success));
  Adder #(.width(32)) adder_3 (.a(32'h4), .b(EX_PC), .out(adder_3_out));  // open: cin, cout
  // Probe on EX_R2
  // Probe on EX_R1_t
  assign aluop = \n4控制信号_1_alu_op  | ID_aluop;  // OR_Gate or_7, 4 bits wide
  or or_8 (redgdst, \n4控制信号_1_regdst , ID_redgdst);
  or or_9 (regwrite, \n4控制信号_1_regwrite , ID_regwrite);
  or or_10 (J_success, id_ex_1_jmp_2, EX_jal, id_ex_1_jr_2);
  Multiplexer #(.select(2), .width(32), .enable("false")) multiplexer_8 (
    .in0(id_ex_1_r2_2), .in1(MEM_ALUResult), .in2(WB_MEMData),
    .in3({WB_ALUResult[31:2], LH_Address, WB_ALUResult[0]}), .out(Alu_B), .sel(R2_forward));
  \_4控制信号  \u_4控制信号_1  (
    .OP(ID_OP), .Func(ID_Func), .ALU_OP(\n4控制信号_1_alu_op ), .RegDst(\n4控制信号_1_regdst ),
    .RegWrite(\n4控制信号_1_regwrite ), .MemToReg(\n4控制信号_1_memtoreg ), .AluSrc(\n4控制信号_1_alusrc ),
    .SignedExt(\n4控制信号_1_signedext ), .SRLV(ID_SRLV), .SRAV(ID_SRAV), .LH(ID_LH), .BLEZ(ID_BLEZ));
  Counter #(.width(16), .max('hffff)) counter_6 (
    .D(\条件分支成功数 ), .count(B_success), .Q(\条件分支成功数 ), .clk(CLK), .clr(RST));  // open: load, carry
  Multiplexer #(.select(2), .width(32), .enable("false")) multiplexer_9 (
    .in0(id_ex_1_r1_2), .in1(MEM_ALUResult), .in2(WB_MEMData),
    .in3({WB_ALUResult[31:2], LH_Address, WB_ALUResult[0]}), .out(EX_R1), .sel(R1_forward));
  Multiplexer #(.width(32), .enable("false")) multiplexer_10 (
    .in0(multiplexer_11_out), .in1(EX_R1), .out(Before_PC), .sel(id_ex_1_jr_2));
  or or_11 (or_11_out, id_ex_1_jmp_2, EX_jal);
  Multiplexer #(.width(32), .enable("false")) multiplexer_11 (
    .in0(multiplexer_14_out), .in1(id_ex_1_jimm_2), .out(multiplexer_11_out), .sel(or_11_out));
  Multiplexer #(.width(32), .enable("false")) multiplexer_12 (
    .in0(Alu_B), .in1(id_ex_1_imm_2), .out(multiplexer_12_out), .sel(id_ex_1_alusrc_2));
  // Probe on id_ex_1_imm_2
  // Probe on id_ex_1_jimm_2
  // Probe on multiplexer_11_out
  // Probe on EX_PC
  or or_12 (SignedExt, \n4控制信号_1_signedext , ID_signedext);
  or or_13 (alusrc, \n4控制信号_1_alusrc , ID_alusrc);
  or or_14 (MemToReg, \n4控制信号_1_memtoreg , ID_MemToReg);
  // Probe on EX_R1
  Multiplexer #(.width(32), .enable("false")) multiplexer_13 (
    .in0(multiplexer_12_out), .in1(32'h22), .out(multiplexer_13_out), .sel(id_ex_1_syscall_2));
  Shifter #(.width(32)) shifter_2 (.in(id_ex_1_imm_2), .\dist (5'b00010), .out(shifter_2_out));
  // Probe on EX_IR
  and and_4 (and_4_out, id_ex_1_syscall_2, mips_alu_1_equal);
  and and_5 (Ena, id_ex_1_syscall_2, not_4_out);
  not not_4 (not_4_out, mips_alu_1_equal);
  // Probe on multiplexer_13_out
  Multiplexer #(.width(32), .enable("false")) multiplexer_14 (
    .in0(next_pc), .in1(EX_JBPC), .out(multiplexer_14_out), .sel(B_success));
  Register #(.width(32)) register_1 (.D(Alu_B), .en(and_4_out), .Q(LedData), .clk(CLK));  // open: clr
  not not_5 (not_5_out, mips_alu_1_equal);
  and and_6 (and_6_out, id_ex_1_beq_2, mips_alu_1_equal);
  MIPS_ALU mips_alu_1 (
    .X(EX_R1), .Y(multiplexer_13_out), .AluOP(id_ex_1_aluop_2), .Equal(mips_alu_1_equal),
    .Result(mips_alu_1_result), .shamt(multiplexer_15_out));  // open: Result_2
  Adder #(.width(32)) adder_4 (.a(shifter_2_out), .b(id_ex_1_pc_4_2), .out(EX_JBPC));  // open: cin, cout
  // Probe on multiplexer_15_out
  Bit_Extender #(.in_width(32), .out_width(1), .\type ("sign")) bit_extender_5 (
    .in(mips_alu_1_result), .out(bit_extender_5_out));
  // Probe on mips_alu_1_result
  Multiplexer #(.width(5), .enable("false")) multiplexer_15 (
    .in0(shamt), .in1(EX_R1[4:0]), .out(multiplexer_15_out), .sel(or_16_out));
  \重定向forward  \u_重定向forward_1  (
    .WB_WriteReg_num(WB_regwrite_num), .WB_RegWrite(WB_regwrite), .ID_R1_num(EX_R1_t), .ID_R2_num(EX_R2),
    .MEM_WriteReg_num(MEM_Regwrite_num), .MEM_RegWrite(MEM_Regwrite), .MEM_OP(MEM_IR[31:26]),
    .MEM_Func(MEM_IR[5:0]), .WB_OP(WB_IR[31:26]), .WB_Func(WB_IR[5:0]), .EX_OP(EX_IR[31:26]),
    .EX_Func(EX_IR[5:0]), .R1_Forward(R1_forward), .R2_Forward(R2_forward));
  and and_7 (and_7_out, id_ex_1_blez_2, or_15_out);
  or or_15 (or_15_out, mips_alu_1_equal, bit_extender_5_out);
  and and_8 (and_8_out, not_5_out, id_ex_1_bne_2);
  or or_16 (or_16_out, EX_SRAV, EX_SRLV);
  // Probe on Alu_B
  EX_MEM ex_mem_1 (
    .Memtoreg(id_ex_1_memtoreg_2), .Syscall(id_ex_1_syscall_2), .Memwrite(id_ex_1_memwrite_2),
    .equal(mips_alu_1_equal), .Regdst(EX_regdst), .Lh(EX_lh), .Regwrite(EX_Regwrite), .Jal(EX_jal),
    .clk(CLK), .\使能端_低电平有效_stall_高电平有效 (and_2_out), .\同步清零_气泡_高电平有效 (RST), .result(mips_alu_1_result),
    .IR(EX_IR), .PC(EX_PC), .ALUB(Alu_B), .memtoreg_2(ex_mem_1_memtoreg_2), .syscall_2(ex_mem_1_syscall_2),
    .memwrite_2(ex_mem_1_memwrite_2), .equal_2(ex_mem_1_equal_2), .regdst_2(ex_mem_1_regdst_2),
    .lh_2(ex_mem_1_lh_2), .regwrite_2(MEM_Regwrite), .jal_2(ex_mem_1_jal_2), .result_2(MEM_ALUResult),
    .ir_2(MEM_IR), .PC_2(MEM_PC), .ALUB_2(ex_mem_1_alub_2), .rt(EX_rt), .rd(EX_rd), .rt_2(ex_mem_1_rt_2),
    .rd_2(ex_mem_1_rd_2));  // open: Srlv, Jr, Jmp, 传输状态In_表明当前传输数据有效, srlv_2, jr_2, jmp_2, 传输状态Out_表明当前传输数据有效
  or or_17 (B_success, and_8_out, and_7_out, and_6_out);
  // Probe on mips_alu_1_result
  // Probe on R1_forward
  // Probe on R2_forward
  // Probe on MEM_IR
  // Probe on ex_mem_1_alub_2
  Multiplexer #(.width(5), .enable("false")) multiplexer_16 (
    .in0(ex_mem_1_rt_2), .in1(ex_mem_1_rd_2), .out(multiplexer_16_out), .sel(ex_mem_1_regdst_2));
  // Probe on MEM_ALUResult
  // Probe on MEM_ALUResult
  Multiplexer #(.width(5), .enable("false")) multiplexer_17 (
    .in0(multiplexer_16_out), .in1({5{1'b1}}), .out(MEM_Regwrite_num), .sel(ex_mem_1_jal_2));
  // Probe on MEM_Regwrite_num
  // MIPS_RAM mips_ram_1: pin names not known; wires that end beside it: MEM_ALUResult[21:2], ex_mem_1_alub_2, ex_mem_1_memwrite_2, CLK, RST, mips_ram_1_p6
  \LoadUse检测  \loaduse检测_1  (
    .\LoadUse相关 (LoadUse), .ID_OP(ID_OP), .ID_Func(ID_Func), .EX_OP(EX_IR[31:26]), .ID_R1_num(ID_R1),
    .ID_R2_num(ID_R2), .EX_R_WB(multiplexer_26_out));
  MEM_WB mem_wb_1 (
    .Memtoreg(ex_mem_1_memtoreg_2), .Syscall(ex_mem_1_syscall_2), .equal(ex_mem_1_equal_2),
    .Regdst(ex_mem_1_regdst_2), .Lh(ex_mem_1_lh_2), .Regwrite(MEM_Regwrite), .Jal(ex_mem_1_jal_2), .clk(CLK),
    .\使能端_低电平有效_stall_高电平有效 (and_2_out), .\同步清零_气泡_高电平有效 (RST), .result(MEM_ALUResult), .IR(MEM_IR),
    .PC(MEM_PC), .memdata(mips_ram_1_p6), .memtoreg_2(mem_wb_1_memtoreg_2), .regdst_2(mem_wb_1_regdst_2),
    .lh_2(WB_LH), .regwrite_2(WB_regwrite), .jal_2(mem_wb_1_jal_2),
    .result_2({WB_ALUResult[31:2], LH_Address, WB_ALUResult[0]}), .ir_2(WB_IR), .PC_2(WB_PC),
    .memdata_2(mem_wb_1_memdata_2), .rt(ex_mem_1_rt_2), .rd(ex_mem_1_rd_2), .rt_2(mem_wb_1_rt_2),
    .rd_2(mem_wb_1_rd_2));  // open: Srlv, Jr, Jmp, syscall_2, srlv_2, jr_2, equal_2, jmp_2, 传输状态Out_表明当前传输数据有效, 传输状态In_表明当前传输数据有效
  // Probe on WB_IR
  Multiplexer #(.width(5), .enable("false")) multiplexer_18 (
    .in0(mem_wb_1_rt_2), .in1(mem_wb_1_rd_2), .out(multiplexer_18_out), .sel(mem_wb_1_regdst_2));
  Multiplexer #(.width(32), .enable("false")) multiplexer_19 (
    .in0({WB_ALUResult[31:2], LH_Address, WB_ALUResult[0]}), .in1(mem_wb_1_memdata_2),
    .out(multiplexer_19_out), .sel(mem_wb_1_memtoreg_2));
  Adder #(.width(32)) adder_5 (.a(WB_PC), .b(32'h4), .out(adder_5_out));  // open: cin, cout
  Multiplexer #(.width(32), .enable("false")) multiplexer_20 (
    .in0(multiplexer_19_out), .in1(adder_5_out), .out(multiplexer_20_out), .sel(mem_wb_1_jal_2));
  // Probe on {WB_ALUResult[31:2], LH_Address, WB_ALUResult[0]}
  Counter #(.width(16), .max('hffff)) counter_7 (
    .D(\LoadUse次数 ), .count(LoadUse), .Q(\LoadUse次数 ), .clk(CLK), .clr(RST));  // open: load, carry
  Multiplexer #(.width(5), .enable("false")) multiplexer_21 (
    .in0(multiplexer_18_out), .in1({5{1'b1}}), .out(WB_regwrite_num), .sel(mem_wb_1_jal_2));
  Multiplexer #(.width(32), .enable("false")) multiplexer_22 (
    .in0(multiplexer_20_out), .in1(bit_extender_6_out), .out(multiplexer_22_out), .sel(WB_LH));
  // Probe on WB_regwrite_num
  // Probe on mem_wb_1_memdata_2
  Multiplexer #(.width(16), .enable("false")) multiplexer_23 (
    .in0(mem_wb_1_memdata_2[15:0]), .in1(mem_wb_1_memdata_2[31:16]), .out(multiplexer_23_out),
    .sel(LH_Address));
  // Probe on multiplexer_22_out
  assign bit_extender_6_out = {{16{multiplexer_23_out[15]}}, multiplexer_23_out};  // Bit_Extender bit_extender_6
  Multiplexer #(.width(5), .enable("false")) multiplexer_24 (
    .in0(EX_rt), .in1(EX_rd), .out(multiplexer_24_out), .sel(EX_regdst));
  Multiplexer #(.width(32), .enable("false")) multiplexer_25 (
    .in0(mem_wb_1_memdata_2), .in1(bit_extender_6_out), .out(WB_MEMData), .sel(WB_LH));
  Multiplexer #(.width(5), .enable("false")) multiplexer_26 (
    .in0(multiplexer_24_out), .in1({5{1'b1}}), .out(multiplexer_26_out), .sel(EX_jal));

  // Other names for the same wires on the sheet: IR (some bits) = {ID_OP, ID_Func}; rd[4:0] = IR[15:11];
  //   rt[4:0] = IR[20:16]; WB_ALUResult[1] = LH_Address

  // Notes on the sheet:
  //   中断源
  //   中断等待指示
  //   OP
  //   Func
  //   数码管输出
  //   contents of rom_1 (hex, n*v repeats v):
  //   20110001 8100005 20110001 20120002 20130003 8100009 20110001 20120002 20130003 810000d 20110001
  //   20120002 20130003 8100011 20110001 20120002 20130003 c1000fc 20100001 20110001 118fc0 112020
  //   20020022 c 118882 12200001 8100015 112020 20020022 c 20110001 118880 112020 20020022 c 12200001
  //   810001f 20110001 118fc0 112020 20020022 c 1188c3 112020 20020022 c 118903 112020 20020022 c 118903
  //   112020 20020022 c 118903 112020 20020022 c 118903 112020 20020022 c 118903 112020 20020022 c 118903
  //   112020 20020022 c 118903 112020 20020022 c 20100001 109fc0 139fc3 8021 2012000c 24160003 26100001
  //   3210000f 20080008 20090001 139900 2709825 132020 20020022 c 1094022 1500fff9 22100001 2018000f
  //   2188024 108700 20080008 20090001 139902 2709825 132021 20020022 c 1094022 1500fff9 108702 2c9b022
  //   12c00001 8100050 4020 1084027 84400 3508ffff 82021 20020022 c 2010ffff 20110000 ae300000 22100001
  //   22310004 ae300000 22100001 22310004 ae300000 22100001 22310004 ae300000 22100001 22310004 ae300000
  //   22100001 22310004 ae300000 22100001 22310004 ae300000 22100001 22310004 ae300000 22100001 22310004
  //   ae300000 22100001 22310004 ae300000 22100001 22310004 ae300000 22100001 22310004 ae300000 22100001
  //   22310004 ae300000 22100001 22310004 ae300000 22100001 22310004 ae300000 22100001 22310004 ae300000
  //   22100001 22310004 22100001 8020 2011003c 8e130000 8e340000 274402a 11000002 ae330000 ae140000
  //   2231fffc 1611fff8 102020 20020022 c 22100004 2011003c 1611fff2 20020032 c 20080001 20090003 20110876
  //   118d00 112020 20020022 c 200b0008 1118806 1318806 112020 20020022 c 216bffff 1560fff9 2002000a c
  //   20080001 20090003 20110876 118d00 112020 20020022 c 200b0008 1118807 1318807 112020 20020022 c
  //   216bffff 1560fff9 2002000a c 20090000 200b0010 34118483 20120404 118c00 129400 36318281 22520404
  //   ad310000 2328820 21290004 216bffff 1560fffb 200b0020 20090000 85310000 112020 20020022 c 21290002
  //   216bffff 1560fff9 2002000a c 2011fff1 112020 20020022 c 22310001 1a20fffb 2002000a c 2002000a c
  //   20100000 22100001 102020 20020022 c 22100002 102020 20020022 c 22100003 102020 20020022 c 22100004
  //   102020 20020022 c 22100005 102020 20020022 c 22100006 102020 20020022 c 22100007 102020 20020022 c
  //   22100008 102020 20020022 20020022 c 3e00008
  //   指令字
  //   OP
  //   Func
  //   rs
  //   rt
  //   rd
  //   shamt
  //   imm
  //   2
  //   PC+4
  //   1
  //   流水调试日志用
  //   22
  //   3
  //   4
  //   10
  //   9
  //   5
  //   6
  //   8
  //   OP
  //   Func
  //   OP
  //   Func
  //   7
  //   OP
  //   Func
  //   11
  //   12
  //   15
  //   13
  //   16
  //   14
  //   19
  //   17
  //   20
  //   21
  //   18
endmodule

module \分支预测转换电路  (
  input  [31:0] IR,
  input  [15:0] pastpc,
  input  [15:0] pcaddrmux,
  input  [5:0] pastop,
  input  [15:0] pcaddr,
  input  [5:0] pastfunct,
  input  clk,
  input  rst,
  output success,
  output pastpredict,
  output miss,
  output fail,
  output predict,
  output [15:0] pcout
);

  wire adder_1_cout, adder_2_cout, adder_3_cout, adder_4_cout, adder_5_cout, adder_6_cout, adder_7_cout,
       adder_8_cout, adder_9_cout, adder_10_cout, adder_11_cout, adder_12_cout, adder_13_cout, adder_14_cout,
       adder_15_cout, adder_16_cout, addLRU0, addLRU1, addLRU2, addLRU3, addLRU4, addLRU5, addLRU6, addLRU7,
       and_1_out, and_2_out, and_3_out, and_4_out, and_5_out, and_6_out, and_7_out, and_8_out, and_9_out,
       and_10_out, and_11_out, and_12_out, and_13_out, and_14_out, and_15_out, and_16_out, and_17_out,
       and_18_out, and_54_out, and_55_out, and_56_out, and_57_out, and_58_out, and_59_out, and_60_out,
       and_61_out, and_62_out, and_63_out, and_64_out, and_65_out, and_66_out, and_67_out, and_68_out,
       and_69_out, beq, bltz, bne, catch0, catch1, catch2, catch3, catch4, catch5, catch6, catch7,
       comparator_1_eq, comparator_2_eq, comparator_3_eq, comparator_4_eq, comparator_5_eq, comparator_6_eq,
       comparator_7_eq, comparator_8_eq, comparator_9_eq, comparator_10_eq, comparator_11_eq,
       comparator_12_eq, comparator_13_eq, comparator_14_eq, comparator_15_eq, comparator_17_eq,
       comparator_18_eq, comparator_19_eq, comparator_25_eq, comparator_26_eq, comparator_27_eq,
       comparator_28_eq, comparator_29_eq, comparator_30_eq, comparator_31_eq, comparator_32_eq,
       decoder_2_out0, decoder_2_out1, decoder_2_out2, decoder_2_out3, decoder_2_out4, decoder_2_out5,
       decoder_2_out6, decoder_2_out7, decoder_3_out1, decoder_3_out2, decoder_3_out4, decoder_3_out8,
       decoder_4_out1, decoder_4_out2, decoder_4_out4, decoder_4_out8, eLRU0, eLRU1, eLRU2, eLRU3, eLRU4,
       eLRU5, eLRU6, eLRU7, j, jal, jr, multiplexer_56_out, multiplexer_57_out, multiplexer_58_out,
       multiplexer_60_out, multiplexer_61_out, multiplexer_63_out, multiplexer_64_out, multiplexer_65_out,
       multiplexer_67_out, not_1_out, not_2_out, not_3_out, not_4_out, not_5_out, not_6_out, not_7_out,
       not_8_out, not_9_out, not_10_out, not_11_out, not_12_out, not_13_out, not_14_out, not_15_out,
       not_16_out, not_17_out, not_18_out, not_19_out, not_20_out, not_21_out, not_22_out, not_23_out,
       not_24_out, not_25_out, not_26_out, not_27_out, not_28_out, not_29_out, not_30_out, not_31_out,
       not_32_out, not_33_out, not_34_out, not_35_out, not_36_out, not_37_out, not_38_out, not_39_out,
       not_40_out, not_41_out, not_42_out, or_1_out, or_2_out, or_3_out, or_4_out, or_5_out, or_6_out,
       or_7_out, or_8_out, or_9_out, or_10_out, or_11_out, or_12_out, or_13_out, or_14_out, or_15_out,
       or_16_out, or_17_out, or_18_out, or_19_out, or_20_out, or_21_out, or_22_out, or_23_out, or_24_out,
       or_25_out, or_27_out, or_28_out, or_29_out, or_30_out, or_31_out, or_32_out, or_33_out, or_34_out,
       or_35_out, or_44_out, or_45_out, replace0, replace1, replace2, replace3, replace4, replace5, replace6,
       replace7, subtractor_1_bout, subtractor_2_bout, subtractor_3_bout, subtractor_4_bout,
       subtractor_5_bout, subtractor_6_bout, subtractor_7_bout, subtractor_8_bout, sw0, sw1, sw2, sw3, sw4,
       sw5, sw6, sw7, vaild0, vaild1, vaild2, vaild3, vaild4, vaild5, vaild6, vaild7, \高位 , \高位等 , \高位预测 ;
  wire [0:0] multiplexer_62_out;
  wire [1:0] adder_1_out, adder_2_out, adder_3_out, adder_4_out, adder_5_out, adder_6_out, adder_7_out,
       adder_8_out, multiplexer_1_out, multiplexer_2_out, multiplexer_3_out, multiplexer_4_out,
       multiplexer_5_out, multiplexer_6_out, multiplexer_7_out, multiplexer_8_out, multiplexer_9_out,
       multiplexer_10_out, multiplexer_11_out, multiplexer_12_out, multiplexer_13_out, multiplexer_14_out,
       multiplexer_15_out, multiplexer_16_out, multiplexer_17_out, multiplexer_18_out, multiplexer_19_out,
       multiplexer_20_out, multiplexer_21_out, multiplexer_22_out, multiplexer_23_out, multiplexer_24_out,
       multiplexer_68_out, multiplexer_72_out, multiplexer_73_out, Npred0, Npred1, Npred2, Npred3, Npred4,
       Npred5, Npred6, Npred7, pred0, pred1, pred2, pred3, pred4, pred5, pred6, pred7, subtractor_1_out,
       subtractor_2_out, subtractor_3_out, subtractor_4_out, subtractor_5_out, subtractor_6_out,
       subtractor_7_out, subtractor_8_out;
  wire [2:0] max3_1_max_num, max3_2_max_num, max3_3_max_num, max3_4_max_num, max3_5_max_num, max3_6_max_num,
       max3_7_max_num, multiplexer_49_out, multiplexer_50_out, multiplexer_51_out, multiplexer_52_out,
       multiplexer_53_out, multiplexer_54_out, multiplexer_55_out;
  wire [3:0] and_20_out, and_24_out, and_71_out, and_75_out;
  wire [15:0] adder_9_out, adder_10_out, adder_11_out, adder_12_out, adder_13_out, adder_14_out,
       adder_15_out, adder_16_out, addr0, addr1, addr2, addr3, addr4, addr5, addr6, addr7, LRU0, LRU1, LRU2,
       LRU3, LRU4, LRU5, LRU6, LRU7, max3_1_max, max3_2_max, max3_3_max, max3_4_max, max3_5_max, max3_6_max,
       multiplexer_33_out, multiplexer_34_out, multiplexer_35_out, multiplexer_36_out, multiplexer_37_out,
       multiplexer_38_out, multiplexer_39_out, multiplexer_40_out, multiplexer_59_out, multiplexer_66_out,
       multiplexer_70_out, multiplexer_71_out, NLRU0, NLRU1, NLRU2, NLRU3, NLRU4, NLRU5, NLRU6, NLRU7, pc0,
       pc1, pc2, pc3, pc4, pc5, pc6, pc7;

  Register #(.width(1)) register_1 (.D(1'b1), .en(replace0), .Q(vaild0), .clk(clk), .clr(rst));
  Register #(.width(1)) register_2 (.D(1'b1), .en(replace1), .Q(vaild1), .clk(clk), .clr(rst));
  Register #(.width(1)) register_3 (.D(1'b1), .en(replace2), .Q(vaild2), .clk(clk), .clr(rst));
  Register #(.width(1)) register_4 (.D(1'b1), .en(replace3), .Q(vaild3), .clk(clk), .clr(rst));
  Register #(.width(1)) register_5 (.D(1'b1), .en(replace4), .Q(vaild4), .clk(clk), .clr(rst));
  Register #(.width(1)) register_6 (.D(1'b1), .en(replace5), .Q(vaild5), .clk(clk), .clr(rst));
  Register #(.width(1)) register_7 (.D(1'b1), .en(replace6), .Q(vaild6), .clk(clk), .clr(rst));
  Register #(.width(1)) register_8 (.D(1'b1), .en(replace7), .Q(vaild7), .clk(clk), .clr(rst));
  Register #(.width(16)) register_9 (.D(pastpc), .en(replace0), .Q(pc0), .clk(clk), .clr(rst));
  Register #(.width(16)) register_10 (.D(pastpc), .en(replace1), .Q(pc1), .clk(clk), .clr(rst));
  Register #(.width(16)) register_11 (.D(pastpc), .en(replace2), .Q(pc2), .clk(clk), .clr(rst));
  Register #(.width(16)) register_12 (.D(pastpc), .en(replace3), .Q(pc3), .clk(clk), .clr(rst));
  Register #(.width(16)) register_13 (.D(pastpc), .en(replace4), .Q(pc4), .clk(clk), .clr(rst));
  Register #(.width(16)) register_14 (.D(pastpc), .en(replace5), .Q(pc5), .clk(clk), .clr(rst));
  Register #(.width(16)) register_15 (.D(pastpc), .en(replace6), .Q(pc6), .clk(clk), .clr(rst));
  Register #(.width(16)) register_16 (.D(pastpc), .en(replace7), .Q(pc7), .clk(clk), .clr(rst));
  Register #(.width(16)) register_17 (.D(pcaddrmux), .en(replace0), .Q(addr0), .clk(clk), .clr(rst));
  Register #(.width(16)) register_18 (.D(pcaddrmux), .en(replace1), .Q(addr1), .clk(clk), .clr(rst));
  Register #(.width(16)) register_19 (.D(pcaddrmux), .en(replace2), .Q(addr2), .clk(clk), .clr(rst));
  Register #(.width(16)) register_20 (.D(pcaddrmux), .en(replace3), .Q(addr3), .clk(clk), .clr(rst));
  Register #(.width(16)) register_21 (.D(pcaddrmux), .en(replace4), .Q(addr4), .clk(clk), .clr(rst));
  Register #(.width(16)) register_22 (.D(pcaddrmux), .en(replace5), .Q(addr5), .clk(clk), .clr(rst));
  Register #(.width(16)) register_23 (.D(pcaddrmux), .en(replace6), .Q(addr6), .clk(clk), .clr(rst));
  Register #(.width(16)) register_24 (.D(pcaddrmux), .en(replace7), .Q(addr7), .clk(clk), .clr(rst));
  or or_1 (or_1_out, replace0, catch0);
  or or_2 (or_2_out, replace1, catch1);
  or or_3 (or_3_out, replace2, catch2);
  or or_4 (or_4_out, replace3, catch3);
  or or_5 (or_5_out, replace4, catch4);
  or or_6 (or_6_out, replace5, catch5);
  or or_7 (or_7_out, replace6, catch6);
  or or_8 (or_8_out, replace7, catch7);
  Register #(.width(2)) register_25 (.D(Npred0), .en(or_1_out), .Q(pred0), .clk(clk), .clr(rst));
  Register #(.width(2)) register_26 (.D(Npred1), .en(or_2_out), .Q(pred1), .clk(clk), .clr(rst));
  Register #(.width(2)) register_27 (.D(Npred2), .en(or_3_out), .Q(pred2), .clk(clk), .clr(rst));
  Register #(.width(2)) register_28 (.D(Npred3), .en(or_4_out), .Q(pred3), .clk(clk), .clr(rst));
  Register #(.width(2)) register_29 (.D(Npred4), .en(or_5_out), .Q(pred4), .clk(clk), .clr(rst));
  Register #(.width(2)) register_30 (.D(Npred5), .en(or_6_out), .Q(pred5), .clk(clk), .clr(rst));
  Register #(.width(2)) register_31 (.D(Npred6), .en(or_7_out), .Q(pred6), .clk(clk), .clr(rst));
  Register #(.width(2)) register_32 (.D(Npred7), .en(or_8_out), .Q(pred7), .clk(clk), .clr(rst));
  or or_9 (or_9_out, replace0, addLRU0);
  or or_10 (or_10_out, replace1, addLRU1);
  or or_11 (or_11_out, replace2, addLRU2);
  or or_12 (or_12_out, replace3, addLRU3);
  or or_13 (or_13_out, replace4, addLRU4);
  or or_14 (or_14_out, replace5, addLRU5);
  or or_15 (or_15_out, replace6, addLRU6);
  or or_16 (or_16_out, replace7, addLRU7);
  Register #(.width(16)) register_33 (.D(NLRU0), .en(or_9_out), .Q(LRU0), .clk(clk), .clr(or_17_out));
  or or_17 (or_17_out, rst, eLRU0);
  Register #(.width(16)) register_34 (.D(NLRU1), .en(or_10_out), .Q(LRU1), .clk(clk), .clr(or_18_out));
  or or_18 (or_18_out, rst, eLRU1);
  Register #(.width(16)) register_35 (.D(NLRU2), .en(or_11_out), .Q(LRU2), .clk(clk), .clr(or_19_out));
  or or_19 (or_19_out, rst, eLRU2);
  Register #(.width(16)) register_36 (.D(NLRU3), .en(or_12_out), .Q(LRU3), .clk(clk), .clr(or_20_out));
  or or_20 (or_20_out, rst, eLRU3);
  Register #(.width(16)) register_37 (.D(NLRU4), .en(or_13_out), .Q(LRU4), .clk(clk), .clr(or_21_out));
  or or_21 (or_21_out, rst, eLRU4);
  Register #(.width(16)) register_38 (.D(NLRU5), .en(or_14_out), .Q(LRU5), .clk(clk), .clr(or_22_out));
  or or_22 (or_22_out, rst, eLRU5);
  Register #(.width(16)) register_39 (.D(NLRU6), .en(or_15_out), .Q(LRU6), .clk(clk), .clr(or_23_out));
  or or_23 (or_23_out, rst, eLRU6);
  Register #(.width(16)) register_40 (.D(NLRU7), .en(or_16_out), .Q(LRU7), .clk(clk), .clr(or_24_out));
  or or_24 (or_24_out, rst, eLRU7);
  Adder #(.width(2)) adder_1 (.a(pred0), .b(2'b01), .out(adder_1_out), .cout(adder_1_cout));  // open: cin
  not not_1 (not_1_out, adder_1_cout);
  Adder #(.width(2)) adder_2 (.a(pred1), .b(2'b01), .out(adder_2_out), .cout(adder_2_cout));  // open: cin
  not not_2 (not_2_out, adder_2_cout);
  Adder #(.width(2)) adder_3 (.a(pred2), .b(2'b01), .out(adder_3_out), .cout(adder_3_cout));  // open: cin
  not not_3 (not_3_out, adder_3_cout);
  Adder #(.width(2)) adder_4 (.a(pred3), .b(2'b01), .out(adder_4_out), .cout(adder_4_cout));  // open: cin
  not not_4 (not_4_out, adder_4_cout);
  Adder #(.width(2)) adder_5 (.a(pred4), .b(2'b01), .out(adder_5_out), .cout(adder_5_cout));  // open: cin
  not not_5 (not_5_out, adder_5_cout);
  Adder #(.width(2)) adder_6 (.a(pred5), .b(2'b01), .out(adder_6_out), .cout(adder_6_cout));  // open: cin
  not not_6 (not_6_out, adder_6_cout);
  Adder #(.width(2)) adder_7 (.a(pred6), .b(2'b01), .out(adder_7_out), .cout(adder_7_cout));  // open: cin
  not not_7 (not_7_out, adder_7_cout);
  Adder #(.width(2)) adder_8 (.a(pred7), .b(2'b01), .out(adder_8_out), .cout(adder_8_cout));  // open: cin
  not not_8 (not_8_out, adder_8_cout);
  Multiplexer #(.width(2), .enable("false")) multiplexer_1 (
    .in0(pred0), .in1(adder_1_out), .out(multiplexer_1_out), .sel(and_1_out));
  and and_1 (and_1_out, not_1_out, success);
  Multiplexer #(.width(2)) multiplexer_2 (
    .in0(pred1), .in1(adder_2_out), .out(multiplexer_2_out), .sel(and_2_out));  // open: en
  and and_2 (and_2_out, not_2_out, success);
  Multiplexer #(.width(2)) multiplexer_3 (
    .in0(pred2), .in1(adder_3_out), .out(multiplexer_3_out), .sel(and_3_out));  // open: en
  and and_3 (and_3_out, not_3_out, success);
  Multiplexer #(.width(2)) multiplexer_4 (
    .in0(pred3), .in1(adder_4_out), .out(multiplexer_4_out), .sel(and_4_out));  // open: en
  and and_4 (and_4_out, not_4_out, success);
  Multiplexer #(.width(2)) multiplexer_5 (
    .in0(pred4), .in1(adder_5_out), .out(multiplexer_5_out), .sel(and_5_out));  // open: en
  and and_5 (and_5_out, not_5_out, success);
  Multiplexer #(.width(2)) multiplexer_6 (
    .in0(pred5), .in1(adder_6_out), .out(multiplexer_6_out), .sel(and_6_out));  // open: en
  and and_6 (and_6_out, not_6_out, success);
  Multiplexer #(.width(2)) multiplexer_7 (
    .in0(pred6), .in1(adder_7_out), .out(multiplexer_7_out), .sel(and_7_out));  // open: en
  and and_7 (and_7_out, not_7_out, success);
  Multiplexer #(.width(2)) multiplexer_8 (
    .in0(pred7), .in1(adder_8_out), .out(multiplexer_8_out), .sel(and_8_out));  // open: en
  and and_8 (and_8_out, not_8_out, success);
  not not_9 (not_9_out, subtractor_6_bout);
  Subtractor #(.width(2)) subtractor_1 (
    .a(pred1), .b(2'b01), .out(subtractor_1_out), .bout(subtractor_1_bout));  // open: bin
  not not_10 (not_10_out, subtractor_1_bout);
  not not_11 (not_11_out, subtractor_7_bout);
  not not_12 (not_12_out, subtractor_8_bout);
  Subtractor #(.width(2)) subtractor_2 (
    .a(pred4), .b(2'b01), .out(subtractor_2_out), .bout(subtractor_2_bout));  // open: bin
  not not_13 (not_13_out, subtractor_2_bout);
  Subtractor #(.width(2)) subtractor_3 (
    .a(pred5), .b(2'b01), .out(subtractor_3_out), .bout(subtractor_3_bout));  // open: bin
  not not_14 (not_14_out, subtractor_3_bout);
  Subtractor #(.width(2)) subtractor_4 (
    .a(pred6), .b(2'b01), .out(subtractor_4_out), .bout(subtractor_4_bout));  // open: bin
  not not_15 (not_15_out, subtractor_4_bout);
  Subtractor #(.width(2)) subtractor_5 (
    .a(pred7), .b(2'b01), .out(subtractor_5_out), .bout(subtractor_5_bout));  // open: bin
  not not_16 (not_16_out, subtractor_5_bout);
  Subtractor #(.width(2)) subtractor_6 (
    .a(pred0), .b(2'b01), .out(subtractor_6_out), .bout(subtractor_6_bout));  // open: bin
  and and_9 (and_9_out, not_9_out, fail);
  Multiplexer #(.width(2), .enable("false")) multiplexer_9 (
    .in0(pred1), .in1(subtractor_1_out), .out(multiplexer_9_out), .sel(and_10_out));
  and and_10 (and_10_out, not_10_out, fail);
  Multiplexer #(.width(2), .enable("false")) multiplexer_10 (
    .in0(pred2), .in1(subtractor_7_out), .out(multiplexer_10_out), .sel(and_11_out));
  Subtractor #(.width(2)) subtractor_7 (
    .a(pred2), .b(2'b01), .out(subtractor_7_out), .bout(subtractor_7_bout));  // open: bin
  and and_11 (and_11_out, not_11_out, fail);
  Multiplexer #(.width(2), .enable("false")) multiplexer_11 (
    .in0(pred3), .in1(subtractor_8_out), .out(multiplexer_11_out), .sel(and_12_out));
  Subtractor #(.width(2)) subtractor_8 (
    .a(pred3), .b(2'b01), .out(subtractor_8_out), .bout(subtractor_8_bout));  // open: bin
  and and_12 (and_12_out, not_12_out, fail);
  Multiplexer #(.width(2), .enable("false")) multiplexer_12 (
    .in0(pred4), .in1(subtractor_2_out), .out(multiplexer_12_out), .sel(and_13_out));
  and and_13 (and_13_out, not_13_out, fail);
  Multiplexer #(.width(2), .enable("false")) multiplexer_13 (
    .in0(pred5), .in1(subtractor_3_out), .out(multiplexer_13_out), .sel(and_14_out));
  and and_14 (and_14_out, not_14_out, fail);
  Multiplexer #(.width(2), .enable("false")) multiplexer_14 (
    .in0(pred6), .in1(subtractor_4_out), .out(multiplexer_14_out), .sel(and_15_out));
  and and_15 (and_15_out, not_15_out, fail);
  Multiplexer #(.width(2), .enable("false")) multiplexer_15 (
    .in0(pred7), .in1(subtractor_5_out), .out(multiplexer_15_out), .sel(and_16_out));
  and and_16 (and_16_out, not_16_out, fail);
  Multiplexer #(.width(2), .enable("false")) multiplexer_16 (
    .in0(pred0), .in1(subtractor_6_out), .out(multiplexer_16_out), .sel(and_9_out));
  Multiplexer #(.width(2), .enable("false")) multiplexer_17 (
    .in0(2'b10), .in1(multiplexer_16_out), .out(multiplexer_17_out), .sel(fail));
  Multiplexer #(.width(2), .enable("false")) multiplexer_18 (
    .in0(2'b10), .in1(multiplexer_9_out), .out(multiplexer_18_out), .sel(fail));
  Multiplexer #(.width(2), .enable("false")) multiplexer_19 (
    .in0(2'b10), .in1(multiplexer_10_out), .out(multiplexer_19_out), .sel(fail));
  Multiplexer #(.width(2), .enable("false")) multiplexer_20 (
    .in0(2'b10), .in1(multiplexer_11_out), .out(multiplexer_20_out), .sel(fail));
  Multiplexer #(.width(2), .enable("false")) multiplexer_21 (
    .in0(2'b10), .in1(multiplexer_12_out), .out(multiplexer_21_out), .sel(fail));
  Multiplexer #(.width(2), .enable("false")) multiplexer_22 (
    .in0(2'b10), .in1(multiplexer_13_out), .out(multiplexer_22_out), .sel(fail));
  Multiplexer #(.width(2), .enable("false")) multiplexer_23 (
    .in0(2'b10), .in1(multiplexer_14_out), .out(multiplexer_23_out), .sel(fail));
  Multiplexer #(.width(2), .enable("false")) multiplexer_24 (
    .in0(2'b10), .in1(multiplexer_15_out), .out(multiplexer_24_out), .sel(fail));
  Multiplexer #(.width(2), .enable("false")) multiplexer_25 (
    .in0(multiplexer_17_out), .in1(multiplexer_1_out), .out(Npred0), .sel(success));
  Multiplexer #(.width(2), .enable("false")) multiplexer_26 (
    .in0(multiplexer_18_out), .in1(multiplexer_2_out), .out(Npred1), .sel(success));
  Multiplexer #(.width(2), .enable("false")) multiplexer_27 (
    .in0(multiplexer_19_out), .in1(multiplexer_3_out), .out(Npred2), .sel(success));
  Multiplexer #(.width(2), .enable("false")) multiplexer_28 (
    .in0(multiplexer_20_out), .in1(multiplexer_4_out), .out(Npred3), .sel(success));
  Multiplexer #(.width(2), .enable("false")) multiplexer_29 (
    .in0(multiplexer_21_out), .in1(multiplexer_5_out), .out(Npred4), .sel(success));
  Multiplexer #(.width(2), .enable("false")) multiplexer_30 (
    .in0(multiplexer_22_out), .in1(multiplexer_6_out), .out(Npred5), .sel(success));
  Multiplexer #(.width(2), .enable("false")) multiplexer_31 (
    .in0(multiplexer_23_out), .in1(multiplexer_7_out), .out(Npred6), .sel(success));
  Multiplexer #(.width(2), .enable("false")) multiplexer_32 (
    .in0(multiplexer_24_out), .in1(multiplexer_8_out), .out(Npred7), .sel(success));
  Adder #(.width(16)) adder_9 (.a(LRU0), .b(16'h1), .out(adder_9_out), .cout(adder_9_cout));  // open: cin
  Adder #(.width(16)) adder_10 (.a(LRU1), .b(16'h1), .out(adder_10_out), .cout(adder_10_cout));  // open: cin
  Adder #(.width(16)) adder_11 (.a(LRU2), .b(16'h1), .out(adder_11_out), .cout(adder_11_cout));  // open: cin
  Adder #(.width(16)) adder_12 (.a(LRU3), .b(16'h1), .out(adder_12_out), .cout(adder_12_cout));  // open: cin
  Adder #(.width(16)) adder_13 (.a(LRU4), .b(16'h1), .out(adder_13_out), .cout(adder_13_cout));  // open: cin
  Adder #(.width(16)) adder_14 (.a(LRU5), .b(16'h1), .out(adder_14_out), .cout(adder_14_cout));  // open: cin
  Adder #(.width(16)) adder_15 (.a(LRU6), .b(16'h1), .out(adder_15_out), .cout(adder_15_cout));  // open: cin
  Adder #(.width(16)) adder_16 (.a(LRU7), .b(16'h1), .out(adder_16_out), .cout(adder_16_cout));  // open: cin
  Multiplexer #(.width(16), .enable("false")) multiplexer_33 (
    .in0(LRU0), .in1(adder_9_out), .out(multiplexer_33_out), .sel(not_17_out));
  not not_17 (not_17_out, adder_9_cout);
  Multiplexer #(.width(16), .enable("false")) multiplexer_34 (
    .in0(LRU1), .in1(adder_10_out), .out(multiplexer_34_out), .sel(not_18_out));
  not not_18 (not_18_out, adder_10_cout);
  Multiplexer #(.width(16), .enable("false")) multiplexer_35 (
    .in0(LRU2), .in1(adder_11_out), .out(multiplexer_35_out), .sel(not_19_out));
  not not_19 (not_19_out, adder_11_cout);
  Multiplexer #(.width(16), .enable("false")) multiplexer_36 (
    .in0(LRU3), .in1(adder_12_out), .out(multiplexer_36_out), .sel(not_20_out));
  not not_20 (not_20_out, adder_12_cout);
  Multiplexer #(.width(16), .enable("false")) multiplexer_37 (
    .in0(LRU4), .in1(adder_13_out), .out(multiplexer_37_out), .sel(not_21_out));
  not not_21 (not_21_out, adder_13_cout);
  Multiplexer #(.width(16), .enable("false")) multiplexer_38 (
    .in0(LRU5), .in1(adder_14_out), .out(multiplexer_38_out), .sel(not_22_out));
  not not_22 (not_22_out, adder_14_cout);
  Multiplexer #(.width(16), .enable("false")) multiplexer_39 (
    .in0(LRU6), .in1(adder_15_out), .out(multiplexer_39_out), .sel(not_23_out));
  not not_23 (not_23_out, adder_15_cout);
  Multiplexer #(.width(16), .enable("false")) multiplexer_40 (
    .in0(LRU7), .in1(adder_16_out), .out(multiplexer_40_out), .sel(not_24_out));
  not not_24 (not_24_out, adder_16_cout);
  Multiplexer #(.width(16), .enable("false")) multiplexer_41 (
    .in0(multiplexer_33_out), .in1({16{1'b0}}), .out(NLRU0), .sel(replace0));
  Multiplexer #(.width(16), .enable("false")) multiplexer_42 (
    .in0(multiplexer_34_out), .in1({16{1'b0}}), .out(NLRU1), .sel(replace1));
  Multiplexer #(.width(16), .enable("false")) multiplexer_43 (
    .in0(multiplexer_35_out), .in1({16{1'b0}}), .out(NLRU2), .sel(replace2));
  Multiplexer #(.width(16), .enable("false")) multiplexer_44 (
    .in0(multiplexer_36_out), .in1({16{1'b0}}), .out(NLRU3), .sel(replace3));
  Multiplexer #(.width(16), .enable("false")) multiplexer_45 (
    .in0(multiplexer_37_out), .in1({16{1'b0}}), .out(NLRU4), .sel(replace4));
  Multiplexer #(.width(16), .enable("false")) multiplexer_46 (
    .in0(multiplexer_38_out), .in1({16{1'b0}}), .out(NLRU5), .sel(replace5));
  Multiplexer #(.width(16), .enable("false")) multiplexer_47 (
    .in0(multiplexer_39_out), .in1({16{1'b0}}), .out(NLRU6), .sel(replace6));
  Multiplexer #(.width(16), .enable("false")) multiplexer_48 (
    .in0(multiplexer_40_out), .in1({16{1'b0}}), .out(NLRU7), .sel(replace7));
  Max3 max3_1 (.Y(LRU1), .X(LRU0), .Y_num(3'b001), .X_num(3'b000), .MAX(max3_1_max), .Max_num(max3_1_max_num));
  Max3 max3_2 (.Y(LRU3), .X(LRU2), .Y_num(3'b011), .X_num(3'b010), .MAX(max3_2_max), .Max_num(max3_2_max_num));
  Max3 max3_3 (.Y(LRU5), .X(LRU4), .Y_num(3'b101), .X_num(3'b100), .MAX(max3_3_max), .Max_num(max3_3_max_num));
  Max3 max3_4 (.Y(LRU7), .X(LRU6), .Y_num(3'b111), .X_num(3'b110), .MAX(max3_4_max), .Max_num(max3_4_max_num));
  Multiplexer #(.width(3), .enable("false")) multiplexer_49 (
    .in0(3'b110), .in1(3'b111), .out(multiplexer_49_out), .sel(vaild6));
  Comparator #(.width(6)) comparator_1 (.a(pastop), .b({6{1'b0}}), .eq(comparator_1_eq));  // open: gt, lt
  Comparator #(.width(6)) comparator_2 (.a(pastfunct), .b(6'b001000), .eq(comparator_2_eq));  // open: gt, lt
  Max3 max3_5 (
    .Y(max3_2_max), .X(max3_1_max), .Y_num(max3_2_max_num), .X_num(max3_1_max_num), .MAX(max3_5_max),
    .Max_num(max3_5_max_num));
  Max3 max3_6 (
    .Y(max3_4_max), .X(max3_3_max), .Y_num(max3_4_max_num), .X_num(max3_3_max_num), .MAX(max3_6_max),
    .Max_num(max3_6_max_num));
  Multiplexer #(.width(3), .enable("false")) multiplexer_50 (
    .in0(3'b100), .in1(multiplexer_51_out), .out(multiplexer_50_out), .sel(vaild4));
  Multiplexer #(.width(3), .enable("false")) multiplexer_51 (
    .in0(3'b101), .in1(multiplexer_49_out), .out(multiplexer_51_out), .sel(vaild5));
  Comparator #(.width(6)) comparator_3 (.a(pastop), .b(6'b000001), .eq(comparator_3_eq));  // open: gt, lt
  Comparator #(.width(6)) comparator_4 (.a(pastop), .b(6'b000100), .eq(comparator_4_eq));  // open: gt, lt
  Comparator #(.width(6)) comparator_5 (.a(pastop), .b(6'b000101), .eq(comparator_5_eq));  // open: gt, lt
  Comparator #(.width(6)) comparator_6 (.a(pastop), .b(6'b000010), .eq(comparator_6_eq));  // open: gt, lt
  Comparator #(.width(6)) comparator_7 (.a(pastop), .b(6'b000011), .eq(comparator_7_eq));  // open: gt, lt
  and and_17 (and_17_out, comparator_1_eq, comparator_2_eq);
  Max3 max3_7 (
    .Y(max3_6_max), .X(max3_5_max), .Y_num(max3_6_max_num), .X_num(max3_5_max_num), .Max_num(max3_7_max_num));  // open: MAX
  and and_18 (and_18_out, vaild4, vaild5, vaild0, vaild1, vaild2, vaild3, vaild6, vaild7);
  Multiplexer #(.width(3), .enable("false")) multiplexer_52 (
    .in0(3'b001), .in1(multiplexer_53_out), .out(multiplexer_52_out), .sel(vaild1));
  Multiplexer #(.width(3), .enable("false")) multiplexer_53 (
    .in0(3'b010), .in1(multiplexer_54_out), .out(multiplexer_53_out), .sel(vaild2));
  Multiplexer #(.width(3), .enable("false")) multiplexer_54 (
    .in0(3'b011), .in1(multiplexer_50_out), .out(multiplexer_54_out), .sel(vaild3));
  Decoder #(.select(3), .enable("false")) decoder_1 (
    .out0(sw0), .out1(sw1), .out2(sw2), .out3(sw3), .out4(sw4), .out5(sw5), .out6(sw6), .out7(sw7),
    .sel(max3_7_max_num));
  Multiplexer #(.width(3), .enable("false")) multiplexer_55 (
    .in0(3'b000), .in1(multiplexer_52_out), .out(multiplexer_55_out), .sel(vaild0));
  or or_25 (or_25_out, comparator_3_eq, comparator_4_eq, comparator_5_eq, comparator_6_eq, comparator_7_eq, and_17_out);
  Decoder #(.select(3), .enable("false")) decoder_2 (
    .out0(decoder_2_out0), .out1(decoder_2_out1), .out2(decoder_2_out2), .out3(decoder_2_out3),
    .out4(decoder_2_out4), .out5(decoder_2_out5), .out6(decoder_2_out6), .out7(decoder_2_out7),
    .sel(multiplexer_55_out));
  and and_19 (miss, or_25_out, not_25_out);
  not not_25 (not_25_out, or_27_out);
  Multiplexer #(.enable("false")) multiplexer_56 (
    .in0(decoder_2_out0), .in1(sw0), .out(multiplexer_56_out), .sel(and_18_out));
  Comparator #(.width(16)) comparator_8 (.a(pastpc), .b(pc0), .eq(comparator_8_eq));  // open: gt, lt
  Comparator #(.width(16)) comparator_9 (.a(pastpc), .b(pc1), .eq(comparator_9_eq));  // open: gt, lt
  Comparator #(.width(16)) comparator_10 (.a(pastpc), .b(pc2), .eq(comparator_10_eq));  // open: gt, lt
  Comparator #(.width(16)) comparator_11 (.a(pastpc), .b(pc3), .eq(comparator_11_eq));  // open: gt, lt
  Comparator #(.width(16)) comparator_12 (.a(pastpc), .b(pc4), .eq(comparator_12_eq));  // open: gt, lt
  Comparator #(.width(16)) comparator_13 (.a(pastpc), .b(pc5), .eq(comparator_13_eq));  // open: gt, lt
  Comparator #(.width(16)) comparator_14 (.a(pastpc), .b(pc6), .eq(comparator_14_eq));  // open: gt, lt
  Comparator #(.width(16)) comparator_15 (.a(pastpc), .b(pc7), .eq(comparator_15_eq));  // open: gt, lt
  Multiplexer #(.enable("false")) multiplexer_57 (
    .in0(decoder_2_out1), .in1(sw1), .out(multiplexer_57_out), .sel(and_18_out));
  Multiplexer #(.enable("false")) multiplexer_58 (
    .in0(decoder_2_out2), .in1(sw2), .out(multiplexer_58_out), .sel(and_18_out));
  Multiplexer #(.select(4), .width(16), .disabled(0), .enable("false")) multiplexer_59 (
    .in0({16{1'b0}}), .in1(addr4), .in2(addr5), .in3({16{1'b0}}), .in4(addr6), .in5({16{1'b0}}),
    .in6({16{1'b0}}), .in7({16{1'b0}}), .in8(addr7), .in9({16{1'b0}}), .in10({16{1'b0}}), .in11({16{1'b0}}),
    .in12({16{1'b0}}), .in13({16{1'b0}}), .in14({16{1'b0}}), .in15({16{1'b0}}), .out(multiplexer_59_out),
    .sel(and_24_out));
  Multiplexer #(.enable("false")) multiplexer_60 (
    .in0(decoder_2_out3), .in1(sw3), .out(multiplexer_60_out), .sel(and_18_out));
  Multiplexer #(.enable("false")) multiplexer_61 (
    .in0(decoder_2_out4), .in1(sw4), .out(multiplexer_61_out), .sel(and_18_out));
  Multiplexer #(.select(4), .width(2), .disabled(0), .enable("false")) multiplexer_62 (
    .in0(2'b00), .in1(pred4), .in2(pred5), .in3(2'b00), .in4(pred6), .in5(2'b00), .in6(2'b00), .in7(2'b00),
    .in8(pred7), .in9(2'b00), .in10(2'b00), .in11(2'b00), .in12(2'b00), .in13(2'b00), .in14(2'b00),
    .in15(2'b00), .out({\高位预测 , multiplexer_62_out[0]}), .sel(and_24_out));
  Multiplexer #(.enable("false")) multiplexer_63 (
    .in0(decoder_2_out5), .in1(sw5), .out(multiplexer_63_out), .sel(and_18_out));
  Multiplexer #(.enable("false")) multiplexer_64 (
    .in0(decoder_2_out6), .in1(sw6), .out(multiplexer_64_out), .sel(and_18_out));
  and and_20 (and_20_out[0], comparator_8_eq, vaild0);
  and and_21 (and_20_out[1], comparator_9_eq, vaild1);
  and and_22 (and_20_out[2], comparator_10_eq, vaild2);
  and and_23 (and_20_out[3], comparator_11_eq, vaild3);
  or or_26 (\高位 , and_24_out[3], and_24_out[2], and_24_out[1], and_24_out[0]);
  and and_24 (and_24_out[0], comparator_12_eq, vaild4);
  and and_25 (and_24_out[1], comparator_13_eq, vaild5);
  and and_26 (and_24_out[2], comparator_14_eq, vaild6);
  and and_27 (and_24_out[3], comparator_15_eq, vaild7);
  Multiplexer #(.enable("false")) multiplexer_65 (
    .in0(decoder_2_out7), .in1(sw7), .out(multiplexer_65_out), .sel(and_18_out));
  Comparator #(.width(16)) comparator_16 (.a(multiplexer_59_out), .b(pcaddrmux), .eq(\高位等 ));  // open: gt, lt
  and and_28 (replace0, multiplexer_56_out, miss);
  and and_29 (replace1, multiplexer_57_out, miss);
  and and_30 (replace2, multiplexer_58_out, miss);
  and and_31 (replace3, multiplexer_60_out, miss);
  and and_32 (replace4, multiplexer_61_out, miss);
  and and_33 (replace5, multiplexer_63_out, miss);
  and and_34 (replace6, multiplexer_64_out, miss);
  and and_35 (replace7, multiplexer_65_out, miss);
  or or_27 (or_27_out, and_20_out[3], and_20_out[2], and_20_out[1], and_20_out[0], and_24_out[3], and_24_out[2], and_24_out[1], and_24_out[0]);
  Multiplexer #(.select(4), .width(16), .disabled(0), .enable("false")) multiplexer_66 (
    .in0({16{1'b0}}), .in1(addr0), .in2(addr1), .in3({16{1'b0}}), .in4(addr2), .in5({16{1'b0}}),
    .in6({16{1'b0}}), .in7({16{1'b0}}), .in8(addr3), .in9({16{1'b0}}), .in10({16{1'b0}}), .in11({16{1'b0}}),
    .in12({16{1'b0}}), .in13({16{1'b0}}), .in14({16{1'b0}}), .in15({16{1'b0}}), .out(multiplexer_66_out),
    .sel(and_20_out));
  Decoder #(.select(4)) decoder_3 (
    .out1(decoder_3_out1), .out2(decoder_3_out2), .out4(decoder_3_out4), .out8(decoder_3_out8),
    .sel(and_20_out));  // open: out0, out3, out5, out6, out7, out9, out10, out11, out12, out13, out14, out15, en
  Decoder #(.select(4)) decoder_4 (
    .out1(decoder_4_out1), .out2(decoder_4_out2), .out4(decoder_4_out4), .out8(decoder_4_out8),
    .sel(and_24_out));  // open: out0, out3, out5, out6, out7, out9, out10, out11, out12, out13, out14, out15, en
  or or_28 (or_28_out, success, fail);
  and and_36 (catch2, decoder_3_out4, or_28_out);
  or or_29 (or_29_out, success, fail);
  and and_37 (catch6, decoder_4_out4, or_29_out);
  Comparator #(.width(16)) comparator_17 (
    .a(multiplexer_66_out), .b(pcaddrmux), .eq(comparator_17_eq));  // open: gt, lt
  Multiplexer #(.enable("false")) multiplexer_67 (
    .in0(comparator_17_eq), .in1(\高位等 ), .out(multiplexer_67_out), .sel(\高位 ));
  Multiplexer #(.select(4), .width(2), .disabled(0), .enable("false")) multiplexer_68 (
    .in0(2'b00), .in1(pred0), .in2(pred1), .in3(2'b00), .in4(pred2), .in5(2'b00), .in6(2'b00), .in7(2'b00),
    .in8(pred3), .in9(2'b00), .in10(2'b00), .in11(2'b00), .in12(2'b00), .in13(2'b00), .in14(2'b00),
    .in15(2'b00), .out(multiplexer_68_out), .sel(and_20_out));
  and and_38 (catch0, or_28_out, decoder_3_out1);
  and and_39 (catch1, decoder_3_out2, or_28_out);
  and and_40 (catch3, or_28_out, decoder_3_out8);
  and and_41 (eLRU2, decoder_3_out4, success);
  and and_42 (catch4, or_29_out, decoder_4_out1);
  and and_43 (catch5, decoder_4_out2, or_29_out);
  and and_44 (catch7, or_29_out, decoder_4_out8);
  and and_45 (eLRU4, success, decoder_4_out1);
  and and_46 (eLRU5, decoder_4_out2, success);
  and and_47 (eLRU6, decoder_4_out4, success);
  and and_48 (eLRU7, success, decoder_4_out8);
  Multiplexer #(.enable("false")) multiplexer_69 (
    .in0(multiplexer_68_out[1]), .in1(\高位预测 ), .out(pastpredict), .sel(\高位 ));
  not not_26 (not_26_out, multiplexer_67_out);
  and and_49 (eLRU0, success, decoder_3_out1);
  and and_50 (eLRU1, decoder_3_out2, success);
  and and_51 (eLRU3, success, decoder_3_out8);
  and and_52 (success, multiplexer_67_out, pastpredict);
  and and_53 (fail, or_27_out, not_26_out);
  or or_30 (or_30_out, eLRU0, eLRU1, eLRU2, eLRU3);
  or or_31 (or_31_out, or_30_out, or_32_out);
  or or_32 (or_32_out, eLRU4, eLRU5, eLRU6, eLRU7);
  not not_27 (not_27_out, eLRU4);
  not not_28 (not_28_out, eLRU6);
  not not_29 (not_29_out, eLRU7);
  or or_33 (or_33_out, replace4, replace5, replace6, replace7);
  not not_30 (not_30_out, eLRU0);
  and and_54 (and_54_out, not_30_out, or_31_out);
  not not_31 (not_31_out, eLRU1);
  and and_55 (and_55_out, not_31_out, or_31_out);
  not not_32 (not_32_out, eLRU2);
  and and_56 (and_56_out, not_32_out, or_31_out);
  not not_33 (not_33_out, eLRU3);
  and and_57 (and_57_out, not_33_out, or_31_out);
  or or_34 (or_34_out, replace0, replace1, replace2, replace3);
  or or_35 (or_35_out, or_34_out, or_33_out);
  and and_58 (and_58_out, not_27_out, or_31_out);
  not not_34 (not_34_out, eLRU5);
  and and_59 (and_59_out, not_34_out, or_31_out);
  and and_60 (and_60_out, not_28_out, or_31_out);
  and and_61 (and_61_out, not_29_out, or_31_out);
  not not_35 (not_35_out, replace4);
  not not_36 (not_36_out, replace5);
  not not_37 (not_37_out, replace6);
  not not_38 (not_38_out, replace7);
  not not_39 (not_39_out, replace0);
  and and_62 (and_62_out, not_39_out, or_35_out);
  not not_40 (not_40_out, replace1);
  and and_63 (and_63_out, not_40_out, or_35_out);
  not not_41 (not_41_out, replace2);
  and and_64 (and_64_out, not_41_out, or_35_out);
  not not_42 (not_42_out, replace3);
  and and_65 (and_65_out, not_42_out, or_35_out);
  and and_66 (and_66_out, not_35_out, or_35_out);
  and and_67 (and_67_out, not_36_out, or_35_out);
  and and_68 (and_68_out, not_37_out, or_35_out);
  and and_69 (and_69_out, not_38_out, or_35_out);
  or or_36 (addLRU4, and_58_out, and_66_out);
  or or_37 (addLRU5, and_59_out, and_67_out);
  or or_38 (addLRU6, and_60_out, and_68_out);
  or or_39 (addLRU7, and_61_out, and_69_out);
  or or_40 (addLRU0, and_54_out, and_62_out);
  or or_41 (addLRU1, and_55_out, and_63_out);
  or or_42 (addLRU2, and_56_out, and_64_out);
  or or_43 (addLRU3, and_57_out, and_65_out);
  Comparator #(.width(6)) comparator_18 (.a(IR[31:26]), .b({6{1'b0}}), .eq(comparator_18_eq));  // open: gt, lt
  Comparator #(.width(6)) comparator_19 (.a(IR[5:0]), .b(6'b001000), .eq(comparator_19_eq));  // open: gt, lt
  Comparator #(.width(6)) comparator_20 (.a(IR[31:26]), .b(6'b000001), .eq(bltz));  // open: gt, lt
  Comparator #(.width(6)) comparator_21 (.a(IR[31:26]), .b(6'b000100), .eq(beq));  // open: gt, lt
  Comparator #(.width(6)) comparator_22 (.a(IR[31:26]), .b(6'b000101), .eq(bne));  // open: gt, lt
  Comparator #(.width(6)) comparator_23 (.a(IR[31:26]), .b(6'b000010), .eq(j));  // open: gt, lt
  Comparator #(.width(6)) comparator_24 (.a(IR[31:26]), .b(6'b000011), .eq(jal));  // open: gt, lt
  and and_70 (jr, comparator_18_eq, comparator_19_eq);
  Comparator #(.width(16)) comparator_25 (.a(pcaddr), .b(pc0), .eq(comparator_25_eq));  // open: gt, lt
  Comparator #(.width(16)) comparator_26 (.a(pcaddr), .b(pc1), .eq(comparator_26_eq));  // open: gt, lt
  Comparator #(.width(16)) comparator_27 (.a(pcaddr), .b(pc2), .eq(comparator_27_eq));  // open: gt, lt
  Comparator #(.width(16)) comparator_28 (.a(pcaddr), .b(pc3), .eq(comparator_28_eq));  // open: gt, lt
  Comparator #(.width(16)) comparator_29 (.a(pcaddr), .b(pc4), .eq(comparator_29_eq));  // open: gt, lt
  Comparator #(.width(16)) comparator_30 (.a(pcaddr), .b(pc5), .eq(comparator_30_eq));  // open: gt, lt
  Comparator #(.width(16)) comparator_31 (.a(pcaddr), .b(pc6), .eq(comparator_31_eq));  // open: gt, lt
  Comparator #(.width(16)) comparator_32 (.a(pcaddr), .b(pc7), .eq(comparator_32_eq));  // open: gt, lt
  or or_44 (or_44_out, bltz, beq, bne, j, jal, jr);
  and and_71 (and_71_out[0], comparator_25_eq, vaild0, or_44_out);
  and and_72 (and_71_out[1], comparator_26_eq, vaild1, or_44_out);
  and and_73 (and_71_out[2], comparator_27_eq, vaild2, or_44_out);
  and and_74 (and_71_out[3], comparator_28_eq, vaild3, or_44_out);
  and and_75 (and_75_out[0], comparator_29_eq, vaild4, or_44_out);
  and and_76 (and_75_out[1], comparator_30_eq, vaild5, or_44_out);
  and and_77 (and_75_out[2], comparator_31_eq, vaild6, or_44_out);
  and and_78 (and_75_out[3], comparator_32_eq, vaild7, or_44_out);
  Multiplexer #(.select(4), .width(16), .disabled(0), .enable("false")) multiplexer_70 (
    .in0({16{1'b0}}), .in1(addr4), .in2(addr5), .in3({16{1'b0}}), .in4(addr6), .in5({16{1'b0}}),
    .in6({16{1'b0}}), .in7({16{1'b0}}), .in8(addr7), .in9({16{1'b0}}), .in10({16{1'b0}}), .in11({16{1'b0}}),
    .in12({16{1'b0}}), .in13({16{1'b0}}), .in14({16{1'b0}}), .in15({16{1'b0}}), .out(multiplexer_70_out),
    .sel(and_75_out));
  or or_45 (or_45_out, and_75_out[0], and_75_out[1], and_75_out[2], and_75_out[3]);
  Multiplexer #(.select(4), .width(16), .disabled(0)) multiplexer_71 (
    .in0({16{1'b0}}), .in1(addr0), .in2(addr1), .in3({16{1'b0}}), .in4(addr2), .in5({16{1'b0}}),
    .in6({16{1'b0}}), .in7({16{1'b0}}), .in8(addr3), .in9({16{1'b0}}), .in10({16{1'b0}}), .in11({16{1'b0}}),
    .in12({16{1'b0}}), .in13({16{1'b0}}), .in14({16{1'b0}}), .in15({16{1'b0}}), .out(multiplexer_71_out),
    .sel(and_71_out));  // open: en
  Multiplexer #(.select(4), .width(2), .disabled(0)) multiplexer_72 (
    .in0(2'b00), .in1(pred0), .in2(pred1), .in3(2'b00), .in4(pred2), .in5(2'b00), .in6(2'b00), .in7(2'b00),
    .in8(pred3), .in9(2'b00), .in10(2'b00), .in11(2'b00), .in12(2'b00), .in13(2'b00), .in14(2'b00),
    .in15(2'b00), .out(multiplexer_72_out), .sel(and_71_out));  // open: en
  Multiplexer #(.select(4), .width(2), .disabled(0), .enable("false")) multiplexer_73 (
    .in0(2'b00), .in1(pred4), .in2(pred5), .in3(2'b00), .in4(pred6), .in5(2'b00), .in6(2'b00), .in7(2'b00),
    .in8(pred3), .in9(2'b00), .in10(2'b00), .in11(2'b00), .in12(2'b00), .in13(2'b00), .in14(2'b00),
    .in15(2'b00), .out(multiplexer_73_out), .sel(and_75_out));
  Multiplexer #(.enable("false")) multiplexer_74 (
    .in0(multiplexer_72_out[1]), .in1(multiplexer_73_out[1]), .out(predict), .sel(or_45_out));
  Multiplexer #(.width(16), .enable("false")) multiplexer_75 (
    .in0(multiplexer_71_out), .in1(multiplexer_70_out), .out(pcout), .sel(or_45_out));

  // Other names for the same wires on the sheet: funct[5:0] = IR[5:0]; op[5:0] = IR[31:26];
  //   pastaddr[15:0] = pcaddrmux; replace = miss
endmodule

module Max3 (
  input  [15:0] Y,
  input  [15:0] X,
  input  [2:0] Y_num,
  input  [2:0] X_num,
  output [15:0] MAX,
  output [2:0] Max_num
);

  wire comparator_1_eq, comparator_1_gt, or_1_out;

  Multiplexer #(.width(16), .enable("false")) multiplexer_1 (.in0(Y), .in1(X), .out(MAX), .sel(or_1_out));
  Comparator #(.width(16), .mode("unsigned")) comparator_1 (
    .a(X), .b(Y), .gt(comparator_1_gt), .eq(comparator_1_eq));  // open: lt
  or or_1 (or_1_out, comparator_1_gt, comparator_1_eq);
  Multiplexer #(.width(3), .enable("false")) multiplexer_2 (.in0(Y_num), .in1(X_num), .out(Max_num), .sel(or_1_out));

  // Notes on the sheet:
  //   输出两个输入中的较大值，并输出较大值的3位编号
endmodule

module CP0 (
  input  \_1号中断 ,
  input  IE,
  input  [31:0] PCin,
  input  \_2号中断 ,
  input  ERET,
  input  \_3号中断 ,
  input  CLK,
  output W1,
  output [1:0] num,
  output W2,
  output IRstart,
  output W3,
  output [31:0] PCout
);

  wire and_1_out, and_2_out, and_3_out, and_4_out, and_5_out, and_6_out, and_7_out, and_8_out, and_9_out,
       and_10_out, comparator_1_gt, comparator_1_lt, d_ff_1_q, d_ff_2_q, d_ff_3_q, d_ff_4_q, d_ff_8_q,
       d_ff_9_q, demultiplexer_1_out1, demultiplexer_1_out2, demultiplexer_1_out3, IR1, IR2, IR3,
       multiplexer_2_out, or_2_out, or_3_out, or_4_out, or_5_out, or_7_out, or_10_out, R1exe, R2exe, R3exe,
       RST1, RST2, RST3;
  wire [1:0] counter_1_q, multiplexer_1_out, register_1_q;
  wire [31:0] ram_1_data;

  Demultiplexer #(.select(2), .enable("false")) demultiplexer_1 (
    .out1(demultiplexer_1_out1), .out2(demultiplexer_1_out2), .out3(demultiplexer_1_out3), .in(1'b1),
    .sel(num));  // open: out0
  or or_1 (W1, IR1, d_ff_1_q);
  Demultiplexer #(.select(2), .enable("false")) demultiplexer_2 (
    .out1(RST1), .out2(RST2), .out3(RST3), .in(ERET), .sel(num));  // open: out0
  D_Flip_Flop d_ff_1 (.clk(\_1号中断 ), .D(1'b1), .Q(d_ff_1_q), .reset(IR1));  // open: Qn, preset, en
  and and_1 (and_1_out, demultiplexer_1_out1, IRstart);
  and and_2 (and_2_out, demultiplexer_1_out2, IRstart);
  and and_3 (and_3_out, demultiplexer_1_out3, IRstart);
  or or_2 (or_2_out, d_ff_1_q, IR1);
  and and_4 (and_4_out, or_2_out, ~RST1);  // AND_Gate
  D_Flip_Flop u_IR1 (.clk(CLK), .D(and_4_out), .Q(IR1));  // open: Qn, preset, en, reset
  D_Flip_Flop d_ff_2 (.clk(and_1_out), .D(1'b1), .Q(d_ff_2_q), .reset(R1exe));  // open: Qn, preset, en
  D_Flip_Flop d_ff_3 (.clk(and_2_out), .D(1'b1), .Q(d_ff_3_q), .reset(R2exe));  // open: Qn, preset, en
  D_Flip_Flop d_ff_4 (.clk(and_3_out), .D(1'b1), .Q(d_ff_4_q), .reset(R3exe));  // open: Qn, preset, en
  // Probe on num
  Priority_Encoder #(.select(2)) priority_encoder_1 (
    .in0(1'b1), .in1(IR1), .in2(IR2), .in3(IR3), .out(num));  // open: gs, en_out, en_in
  or or_3 (or_3_out, d_ff_2_q, R1exe);
  or or_4 (or_4_out, d_ff_3_q, R2exe);
  or or_5 (or_5_out, d_ff_4_q, R3exe);
  D_Flip_Flop d_ff_5 (.clk(CLK), .D(and_5_out), .Q(R1exe));  // open: Qn, preset, en, reset
  and and_5 (and_5_out, or_3_out, ~RST1);  // AND_Gate
  D_Flip_Flop d_ff_6 (.clk(CLK), .D(and_6_out), .Q(R2exe));  // open: Qn, preset, en, reset
  and and_6 (and_6_out, or_4_out, ~RST2);  // AND_Gate
  D_Flip_Flop d_ff_7 (.clk(CLK), .D(and_7_out), .Q(R3exe));  // open: Qn, preset, en, reset
  and and_7 (and_7_out, or_5_out, ~RST3);  // AND_Gate
  or or_6 (W2, IR2, d_ff_8_q);
  D_Flip_Flop d_ff_8 (.clk(\_2号中断 ), .D(1'b1), .Q(d_ff_8_q), .reset(IR2));  // open: Qn, preset, en
  or or_7 (or_7_out, d_ff_8_q, IR2);
  and and_8 (and_8_out, or_7_out, ~RST2);  // AND_Gate
  Multiplexer #(.select(2), .width(2)) multiplexer_1 (
    .in0(2'b00), .in1(2'b11), .in2(2'b10), .in3(2'b00), .out(multiplexer_1_out), .sel({IRstart, ERET}));  // open: en
  D_Flip_Flop u_IR2 (.clk(CLK), .D(and_8_out), .Q(IR2));  // open: Qn, preset, en, reset
  Register #(.width(2)) register_1 (.D(num), .Q(register_1_q), .clk(CLK));  // open: en, clr
  Multiplexer #(.select(2), .enable("false")) multiplexer_2 (
    .in0(1'b1), .in1(R1exe), .in2(R2exe), .in3(R3exe), .out(multiplexer_2_out), .sel(num));
  Counter #(.width(2), .max('h3), .trigger("falling")) counter_1 (
    .load(multiplexer_1_out[0]), .count(multiplexer_1_out[1]), .Q(counter_1_q), .clk(CLK));  // open: D, carry, clr
  Comparator #(.width(2), .mode("unsigned")) comparator_1 (
    .a(num), .b(register_1_q), .gt(comparator_1_gt), .lt(comparator_1_lt));  // open: eq
  or or_8 (IRstart, comparator_1_gt, and_9_out);
  and and_9 (and_9_out, comparator_1_lt, ~multiplexer_2_out);  // AND_Gate
  or or_9 (W3, IR3, d_ff_9_q);
  RAM #(.addrWidth(2), .dataWidth(32), .bus("separate")) ram_1 (
    .addr(counter_1_q), .din(PCin), .data(ram_1_data), .str(IRstart), .clk(CLK), .ld(1'b1));  // open: sel, clr
  Register #(.width(32)) register_2 (.D(ram_1_data), .Q(PCout), .clk(CLK));  // open: en, clr
  D_Flip_Flop d_ff_9 (.clk(\_3号中断 ), .D(1'b1), .Q(d_ff_9_q), .reset(IR3));  // open: Qn, preset, en
  or or_10 (or_10_out, d_ff_9_q, IR3);
  and and_10 (and_10_out, or_10_out, ~RST3);  // AND_Gate
  D_Flip_Flop u_IR3 (.clk(CLK), .D(and_10_out), .Q(IR3));  // open: Qn, preset, en, reset

  // Notes on the sheet:
  //   Reset 
  //   Reset 
  //   PC stack
  //   Reset 
endmodule
